// Logisim project контроллер клавиатуры.circ as structural Verilog: 1 circuit, main circuit main
module main (
  input  in_1,
  input  in_2,
  input  in_3,
  input  _0,
  input  _1,
  input  _2,
  input  _3,
  input  _4,
  input  _5,
  input  _6,
  input  _7,
  input  _8,
  input  _9,
  output [7:0] out_14
);

  wire and_1_out, clock_1_out, or_4_out;
  wire [3:0] or_5_out;
  wire [7:0] multiplier_1_out, register_1_q, register_2_q;

  or or_1 (or_5_out[3], _9, _8);
  or or_2 (or_5_out[1], _7, _6, _3, _2);
  or or_3 (or_5_out[2], _7, _6, _5, _4);
  or or_4 (or_4_out, or_5_out[3], or_5_out[2], or_5_out[1], or_5_out[0], _0);
  or or_5 (or_5_out[0], _7, _9, _5, _3, _1);
  // Probe on {{4{in_2}}, or_5_out}
  Clock clock_1 (.out(clock_1_out));
  // Probe on {{4{in_2}}, in_1, in_2, in_1, in_2}
  Register register_1 (.D(out_14), .Q(register_1_q), .clk(and_1_out), .clr(in_3));  // open: en
  Register register_2 (.D({{4{in_2}}, or_5_out}), .Q(register_2_q), .clk(and_1_out), .clr(in_3));  // open: en
  and and_1 (and_1_out, or_4_out, clock_1_out);
  Multiplier multiplier_1 (
    .a({{4{in_2}}, in_1, in_2, in_1, in_2}), .b(register_1_q), .out(multiplier_1_out));  // open: cin, cout
  // Probe on register_2_q
  Adder adder_1 (.a(multiplier_1_out), .b(register_2_q), .out(out_14));  // open: cin, cout
  // Probe on out_14
endmodule
