// Logisim project контроллер портов ввода вывода.circ as structural Verilog: 1 circuit, main circuit main
module main (
  input  [7:0] in_1,
  input  [7:0] \порт_ввода_1 ,
  input  [7:0] \порт_ввода_2 ,
  input  [7:0] \порт_ввода_3 ,
  input  \такты ,
  input  [4:0] \адрес_управления ,
  output [7:0] \порт_1 ,
  output [7:0] \порт_1_2 ,
  output [7:0] \порт_2 ,
  output [7:0] \порт_2_2 ,
  output [7:0] \порт_3 ,
  output [7:0] \порт_3_2 ,
  output out_13,
  output [7:0] out_14,
  output out_15
);

  wire and_1_out, and_2_out, and_3_out, and_4_out, and_5_out, and_6_out, and_7_out, and_8_out, and_9_out,
       decoder_1_out1, decoder_1_out2, decoder_1_out3, decoder_1_out4, decoder_1_out5, decoder_1_out6,
       decoder_1_out7, decoder_1_out8, decoder_1_out9, decoder_1_out10, decoder_1_out11, s_r_ff_1_q,
       s_r_ff_2_q;
  wire [7:0] controlled_buffer_1_out, register_1_q, register_2_q, register_3_q;

  and and_1 (and_1_out, \такты , decoder_1_out8);
  Register register_1 (.D(\порт_ввода_1 ), .Q(register_1_q), .clk(and_2_out));  // open: en, clr
  and and_2 (and_2_out, s_r_ff_2_q, \такты );
  Register \u_управ_1  (.D(controlled_buffer_1_out), .Q(\порт_1 ), .clk(and_1_out));  // open: en, clr
  assign controlled_buffer_1_out = decoder_1_out11 ? register_1_q : 8'bz;  // Controlled_Buffer controlled_buffer_1
  S_R_Flip_Flop s_r_ff_1 (
    .S(decoder_1_out1), .clk(\такты ), .R(decoder_1_out2), .Q(s_r_ff_1_q));  // open: Qn, preset, reset, en
  Register \u_данные1  (.D(controlled_buffer_1_out), .Q(\порт_1_2 ), .clk(and_3_out));  // open: en, clr
  and and_3 (and_3_out, \такты , decoder_1_out7);
  assign controlled_buffer_1_out = decoder_1_out10 ? register_2_q : 8'bz;  // Controlled_Buffer controlled_buffer_2
  Register register_2 (.D(\порт_ввода_2 ), .Q(register_2_q), .clk(and_4_out));  // open: en, clr
  and and_4 (and_4_out, s_r_ff_2_q, \такты );
  Register \u_управ2  (.D(controlled_buffer_1_out), .Q(\порт_2 ), .clk(and_5_out));  // open: en, clr
  and and_5 (and_5_out, \такты , decoder_1_out6);
  Register register_3 (.D(\порт_ввода_3 ), .Q(register_3_q), .clk(and_6_out));  // open: en, clr
  and and_6 (and_6_out, s_r_ff_2_q, \такты );
  S_R_Flip_Flop s_r_ff_2 (
    .S(decoder_1_out2), .clk(\такты ), .R(decoder_1_out1), .Q(s_r_ff_2_q));  // open: Qn, preset, reset, en
  and and_7 (and_7_out, \такты , decoder_1_out5);
  assign controlled_buffer_1_out = decoder_1_out9 ? register_3_q : 8'bz;  // Controlled_Buffer controlled_buffer_3
  Register \u_данные2  (.D(controlled_buffer_1_out), .Q(\порт_2_2 ), .clk(and_7_out));  // open: en, clr
  Register \u_управ3  (.D(controlled_buffer_1_out), .Q(\порт_3 ), .clk(and_8_out));  // open: en, clr
  and and_8 (and_8_out, \такты , decoder_1_out4);
  or or_1 (out_15, decoder_1_out9, decoder_1_out10, decoder_1_out11);
  Register \u_данные3  (.D(controlled_buffer_1_out), .Q(\порт_3_2 ), .clk(and_9_out));  // open: en, clr
  and and_9 (and_9_out, \такты , decoder_1_out3);
  or or_2 (out_13, and_1_out, and_3_out, and_5_out, and_7_out, and_8_out, and_9_out);
  assign controlled_buffer_1_out = s_r_ff_1_q ? in_1 : 8'bz;  // Controlled_Buffer controlled_buffer_4
  assign out_14 = s_r_ff_2_q ? controlled_buffer_1_out : 8'bz;  // Controlled_Buffer controlled_buffer_5
  Decoder #(.select(5)) decoder_1 (
    .out1(decoder_1_out1), .out2(decoder_1_out2), .out3(decoder_1_out3), .out4(decoder_1_out4),
    .out5(decoder_1_out5), .out6(decoder_1_out6), .out7(decoder_1_out7), .out8(decoder_1_out8),
    .out9(decoder_1_out9), .out10(decoder_1_out10), .out11(decoder_1_out11), .sel(\адрес_управления ));  // open: out0, out12, out13, out14, out15, out16, out17, out18, out19, out20, out21, out22, out23, out24, out25, out26, out27, out28, out29, out30, out31, en
endmodule
