// Logisim project x y.circ as structural Verilog: 1 circuit, main circuit main
module main (
  input  [7:0] in_1,
  input  [7:0] in_2,
  output [31:0] out_3,
  output [31:0] out_4
);

  wire and_1_out, and_2_out, and_3_out, and_4_out, and_5_out, and_6_out, clock_1_out, comparator_1_eq,
       nor_1_out;
  wire [4:0] counter_1_q, ram_1_data, ram_2_data, register_1_q, register_2_q, x_q, y_2_q, y_q;

  nor nor_1 (nor_1_out, in_2[0], in_2[1], in_2[2], in_2[7]);
  and and_1 (and_1_out, in_2[5], clock_1_out, nor_1_out);
  and and_2 (and_2_out, in_2[4], clock_1_out, nor_1_out);
  and and_3 (and_3_out, in_2[6], clock_1_out, nor_1_out);
  and and_4 (and_4_out, in_2[3], clock_1_out, nor_1_out);
  Counter #(.width(5), .max('h1f)) counter_1 (.Q(counter_1_q), .clk(clock_1_out));  // open: load, D, count, carry, clr
  Register #(.width(5)) y (.D(in_1[4:0]), .Q(y_q), .clk(and_3_out));  // open: en, clr
  Register #(.width(5)) register_1 (.D(in_1[4:0]), .Q(register_1_q), .clk(and_1_out));  // open: en, clr
  Register #(.width(5)) register_2 (.D(in_1[4:0]), .Q(register_2_q), .clk(and_2_out));  // open: en, clr
  Comparator #(.width(5)) comparator_1 (.a(counter_1_q), .b(y_q), .eq(comparator_1_eq));  // open: gt, lt
  and and_5 (and_5_out, comparator_1_eq, clock_1_out);
  and and_6 (and_6_out, clock_1_out, and_4_out);
  RAM #(.addrWidth(5), .dataWidth(5), .bus("separate")) ram_1 (
    .addr(counter_1_q), .din(register_1_q), .data(ram_1_data), .clk(and_5_out), .clr(and_6_out));  // open: str, sel, ld
  RAM #(.addrWidth(5), .dataWidth(5), .bus("separate")) ram_2 (
    .addr(counter_1_q), .din(register_2_q), .data(ram_2_data), .clk(and_5_out), .clr(and_6_out));  // open: str, sel, ld
  Clock clock_1 (.out(clock_1_out));
  Register #(.width(5)) x (.D(ram_1_data), .Q(x_q), .clk(clock_1_out));  // open: en, clr
  Register #(.width(5)) y_2 (.D(ram_2_data), .Q(y_2_q), .clk(clock_1_out));  // open: en, clr
  Decoder #(.select(5)) decoder_1 (
    .out0(out_3[0]), .out1(out_3[1]), .out2(out_3[2]), .out3(out_3[3]), .out4(out_3[4]), .out5(out_3[5]),
    .out6(out_3[6]), .out7(out_3[7]), .out8(out_3[8]), .out9(out_3[9]), .out10(out_3[10]), .out11(out_3[11]),
    .out12(out_3[12]), .out13(out_3[13]), .out14(out_3[14]), .out15(out_3[15]), .out16(out_3[16]),
    .out17(out_3[17]), .out18(out_3[18]), .out19(out_3[19]), .out20(out_3[20]), .out21(out_3[21]),
    .out22(out_3[22]), .out23(out_3[23]), .out24(out_3[24]), .out25(out_3[25]), .out26(out_3[26]),
    .out27(out_3[27]), .out28(out_3[28]), .out29(out_3[29]), .out30(out_3[30]), .out31(out_3[31]), .sel(x_q));  // open: en
  Decoder #(.select(5)) decoder_2 (
    .out0(out_4[0]), .out1(out_4[1]), .out2(out_4[2]), .out3(out_4[3]), .out4(out_4[4]), .out5(out_4[5]),
    .out6(out_4[6]), .out7(out_4[7]), .out8(out_4[8]), .out9(out_4[9]), .out10(out_4[10]), .out11(out_4[11]),
    .out12(out_4[12]), .out13(out_4[13]), .out14(out_4[14]), .out15(out_4[15]), .out16(out_4[16]),
    .out17(out_4[17]), .out18(out_4[18]), .out19(out_4[19]), .out20(out_4[20]), .out21(out_4[21]),
    .out22(out_4[22]), .out23(out_4[23]), .out24(out_4[24]), .out25(out_4[25]), .out26(out_4[26]),
    .out27(out_4[27]), .out28(out_4[28]), .out29(out_4[29]), .out30(out_4[30]), .out31(out_4[31]), .sel(y_2_q));  // open: en

  assign in_1[6:5] = {2{in_1[7]}};
  // also tied to GND on the sheet: in_1[7]
endmodule
