// Logisim project банковая память 8 на 8.circ as structural Verilog: 2 circuits, main circuit main
module main (
  input  [5:0] \кординаты_банка ,
  input  \записать_координаты_банка ,
  input  [7:0] \данные_банков ,
  input  [7:0] \адресация ,
  input  [7:0] \данные_jamp ,
  input  \запись_в_память ,
  input  \сбросить_сщётчик ,
  input  jamp,
  input  \такт ,
  input  in_10,
  input  [7:0] \адресация_записи ,
  input  \очистить_все_банки ,
  input  \запись_регистр_адреса ,
  output [7:0] \выход_данных 
);

  wire and_1_out, and_2_out, and_3_out, and_4_out, and_5_out, and_6_out, and_7_out, and_8_out, and_9_out,
       and_10_out, and_11_out, and_12_out, and_13_out, and_14_out, and_15_out, and_16_out, and_18_out,
       and_19_out, and_20_out, and_21_out, and_22_out, and_23_out, and_24_out, and_25_out, and_26_out,
       and_27_out, and_28_out, and_29_out, and_30_out, and_31_out, and_32_out, and_33_out, and_34_out,
       and_35_out, and_36_out, and_37_out, and_38_out, and_39_out, and_40_out, and_41_out, and_42_out,
       and_43_out, and_44_out, and_45_out, and_46_out, and_47_out, and_48_out, and_49_out, and_50_out,
       and_51_out, and_52_out, and_53_out, and_54_out, and_55_out, and_56_out, and_57_out, and_58_out,
       and_59_out, and_60_out, and_61_out, and_62_out, and_63_out, and_64_out, and_65_out, and_66_out,
       and_67_out, and_68_out, and_69_out, and_70_out, and_71_out, and_72_out, and_73_out, and_74_out,
       and_75_out, and_76_out, and_77_out, and_78_out, and_79_out, and_80_out, and_81_out, and_82_out,
       and_83_out, and_84_out, and_85_out, and_86_out, and_87_out, and_88_out, and_89_out, and_90_out,
       and_91_out, and_92_out, and_93_out, and_94_out, and_95_out, and_96_out, and_97_out, and_98_out,
       and_99_out, and_100_out, and_101_out, and_102_out, and_103_out, and_104_out, and_105_out, and_106_out,
       and_107_out, and_108_out, and_109_out, and_110_out, and_111_out, and_112_out, and_113_out,
       and_114_out, and_115_out, and_116_out, and_117_out, and_118_out, and_119_out, and_120_out,
       and_121_out, and_122_out, and_123_out, and_124_out, and_125_out, and_126_out, and_127_out,
       and_128_out, and_129_out, and_130_out, and_131_out, comparator_1_eq, decoder_1_out0, decoder_1_out1,
       decoder_1_out2, decoder_1_out3, decoder_1_out4, decoder_1_out5, decoder_1_out6, decoder_1_out7,
       decoder_2_out0, decoder_2_out1, decoder_2_out2, decoder_2_out3, decoder_2_out4, decoder_2_out5,
       decoder_2_out6, decoder_2_out7, not_1_out, not_2_out, or_1_out, or_2_out, or_3_out;
  wire [2:0] register_1_q, register_1_q_2;
  wire [7:0] counter_1_q, multiplexer_1_out, register_2_q;

  and and_1 (and_1_out, \записать_координаты_банка , \такт );
  Decoder #(.select(3)) decoder_1 (
    .out0(decoder_1_out0), .out1(decoder_1_out1), .out2(decoder_1_out2), .out3(decoder_1_out3),
    .out4(decoder_1_out4), .out5(decoder_1_out5), .out6(decoder_1_out6), .out7(decoder_1_out7),
    .sel(register_1_q));  // open: en
  Register #(.width(6)) register_1 (
    .D(\кординаты_банка ), .Q({register_1_q_2, register_1_q}), .clk(and_1_out));  // open: en, clr
  or or_1 (or_1_out, and_1_out, \сбросить_сщётчик );
  not not_1 (not_1_out, jamp);
  Register register_2 (.D(\адресация_записи ), .Q(register_2_q), .clk(and_2_out));  // open: en, clr
  and and_2 (and_2_out, \такт , \запись_регистр_адреса );
  Multiplexer #(.width(8)) multiplexer_1 (
    .in0(\адресация ), .in1(counter_1_q), .out(multiplexer_1_out), .sel(not_2_out));  // open: en
  Counter counter_1 (
    .load(jamp), .D(\данные_jamp ), .count(not_1_out), .Q(counter_1_q), .clk(\такт ), .clr(or_1_out));  // open: carry
  not not_2 (not_2_out, in_10);
  Comparator comparator_1 (.a(multiplexer_1_out), .b(register_2_q), .eq(comparator_1_eq));  // open: gt, lt
  or or_2 (or_2_out, register_2_q[0], register_2_q[1], register_2_q[2], register_2_q[3], register_2_q[5], register_2_q[6], register_2_q[7], register_2_q[4]);
  and and_3 (and_3_out, decoder_2_out0, decoder_1_out0);
  and and_4 (and_4_out, decoder_2_out0, decoder_1_out1);
  and and_5 (and_5_out, decoder_2_out0, decoder_1_out2);
  and and_6 (and_6_out, decoder_2_out0, decoder_1_out3);
  and and_7 (and_7_out, decoder_2_out0, decoder_1_out4);
  and and_8 (and_8_out, decoder_2_out0, decoder_1_out5);
  and and_9 (and_9_out, decoder_2_out0, decoder_1_out6);
  and and_10 (and_10_out, decoder_2_out0, decoder_1_out7);
  and and_11 (and_11_out, or_2_out, \такт , comparator_1_eq);
  and and_12 (and_12_out, decoder_2_out0, decoder_1_out0, \очистить_все_банки );
  and and_13 (and_13_out, decoder_2_out0, decoder_1_out1, \очистить_все_банки );
  and and_14 (and_14_out, decoder_2_out0, decoder_1_out2, \очистить_все_банки );
  and and_15 (and_15_out, decoder_2_out0, decoder_1_out3, \очистить_все_банки );
  and and_16 (and_16_out, decoder_2_out0, decoder_1_out4, \очистить_все_банки );
  // AND_Gate and_17 has open pins: in0=decoder_2_out0, in1=decoder_1_out5, in2=\очистить_все_банки , out=open
  and and_18 (and_18_out, decoder_2_out0, decoder_1_out6, \очистить_все_банки );
  and and_19 (and_19_out, decoder_2_out0, decoder_1_out7, \очистить_все_банки );
  or or_3 (or_3_out, \запись_в_память , and_11_out);
  RAM #(.bus("separate")) ram_1 (
    .addr(multiplexer_1_out), .din(\данные_банков ), .data(\выход_данных ), .sel(and_3_out), .clk(or_3_out),
    .clr(and_12_out));  // open: str, ld
  RAM #(.bus("separate")) ram_2 (
    .addr(multiplexer_1_out), .din(\данные_банков ), .data(\выход_данных ), .sel(and_4_out), .clk(or_3_out),
    .clr(and_13_out));  // open: str, ld
  RAM #(.bus("separate")) ram_3 (
    .addr(multiplexer_1_out), .din(\данные_банков ), .data(\выход_данных ), .sel(and_5_out), .clk(or_3_out),
    .clr(and_14_out));  // open: str, ld
  RAM #(.bus("separate")) ram_4 (
    .addr(multiplexer_1_out), .din(\данные_банков ), .data(\выход_данных ), .sel(and_6_out), .clk(or_3_out),
    .clr(and_15_out));  // open: str, ld
  RAM #(.bus("separate")) ram_5 (
    .addr(multiplexer_1_out), .din(\данные_банков ), .data(\выход_данных ), .sel(and_7_out), .clk(or_3_out),
    .clr(and_16_out));  // open: str, ld
  RAM #(.bus("separate")) ram_6 (
    .addr(multiplexer_1_out), .din(\данные_банков ), .data(\выход_данных ), .sel(and_8_out), .clk(or_3_out));  // open: str, ld, clr
  RAM #(.bus("separate")) ram_7 (
    .addr(multiplexer_1_out), .din(\данные_банков ), .data(\выход_данных ), .sel(and_9_out), .clk(or_3_out),
    .clr(and_18_out));  // open: str, ld
  RAM #(.bus("separate")) ram_8 (
    .addr(multiplexer_1_out), .din(\данные_банков ), .data(\выход_данных ), .sel(and_10_out), .clk(or_3_out),
    .clr(and_19_out));  // open: str, ld
  and and_20 (and_20_out, decoder_2_out1, decoder_1_out0);
  and and_21 (and_21_out, decoder_2_out1, decoder_1_out1);
  and and_22 (and_22_out, decoder_2_out1, decoder_1_out2);
  and and_23 (and_23_out, decoder_2_out1, decoder_1_out3);
  and and_24 (and_24_out, decoder_2_out1, decoder_1_out4);
  and and_25 (and_25_out, decoder_2_out1, decoder_1_out5);
  and and_26 (and_26_out, decoder_2_out1, decoder_1_out6);
  and and_27 (and_27_out, decoder_2_out1, decoder_1_out7);
  RAM #(.bus("separate")) ram_9 (
    .addr(multiplexer_1_out), .din(\данные_банков ), .data(\выход_данных ), .sel(and_20_out), .clk(or_3_out),
    .clr(and_28_out));  // open: str, ld
  and and_28 (and_28_out, decoder_2_out1, decoder_1_out0, \очистить_все_банки );
  RAM #(.bus("separate")) ram_10 (
    .addr(multiplexer_1_out), .din(\данные_банков ), .data(\выход_данных ), .sel(and_21_out), .clk(or_3_out),
    .clr(and_29_out));  // open: str, ld
  and and_29 (and_29_out, decoder_2_out1, decoder_1_out1, \очистить_все_банки );
  RAM #(.bus("separate")) ram_11 (
    .addr(multiplexer_1_out), .din(\данные_банков ), .data(\выход_данных ), .sel(and_22_out), .clk(or_3_out),
    .clr(and_30_out));  // open: str, ld
  and and_30 (and_30_out, decoder_2_out1, decoder_1_out2, \очистить_все_банки );
  RAM #(.bus("separate")) ram_12 (
    .addr(multiplexer_1_out), .din(\данные_банков ), .data(\выход_данных ), .sel(and_23_out), .clk(or_3_out),
    .clr(and_31_out));  // open: str, ld
  and and_31 (and_31_out, decoder_2_out1, decoder_1_out3, \очистить_все_банки );
  RAM #(.bus("separate")) ram_13 (
    .addr(multiplexer_1_out), .din(\данные_банков ), .data(\выход_данных ), .sel(and_24_out), .clk(or_3_out),
    .clr(and_32_out));  // open: str, ld
  and and_32 (and_32_out, decoder_2_out1, decoder_1_out4, \очистить_все_банки );
  RAM #(.bus("separate")) ram_14 (
    .addr(multiplexer_1_out), .din(\данные_банков ), .data(\выход_данных ), .sel(and_25_out), .clk(or_3_out),
    .clr(and_33_out));  // open: str, ld
  and and_33 (and_33_out, decoder_2_out1, decoder_1_out5, \очистить_все_банки );
  RAM #(.bus("separate")) ram_15 (
    .addr(multiplexer_1_out), .din(\данные_банков ), .data(\выход_данных ), .sel(and_26_out), .clk(or_3_out),
    .clr(and_34_out));  // open: str, ld
  and and_34 (and_34_out, decoder_2_out1, decoder_1_out6, \очистить_все_банки );
  RAM #(.bus("separate")) ram_16 (
    .addr(multiplexer_1_out), .din(\данные_банков ), .data(\выход_данных ), .sel(and_27_out), .clk(or_3_out),
    .clr(and_35_out));  // open: str, ld
  and and_35 (and_35_out, decoder_2_out1, decoder_1_out7, \очистить_все_банки );
  and and_36 (and_36_out, decoder_2_out2, decoder_1_out0, \очистить_все_банки );
  and and_37 (and_37_out, decoder_2_out2, decoder_1_out0);
  and and_38 (and_38_out, decoder_2_out2, decoder_1_out1, \очистить_все_банки );
  and and_39 (and_39_out, decoder_2_out2, decoder_1_out1);
  and and_40 (and_40_out, decoder_2_out2, decoder_1_out2, \очистить_все_банки );
  and and_41 (and_41_out, decoder_2_out2, decoder_1_out2);
  and and_42 (and_42_out, decoder_2_out2, decoder_1_out3, \очистить_все_банки );
  and and_43 (and_43_out, decoder_2_out2, decoder_1_out3);
  and and_44 (and_44_out, decoder_2_out2, decoder_1_out4, \очистить_все_банки );
  and and_45 (and_45_out, decoder_2_out2, decoder_1_out4);
  and and_46 (and_46_out, decoder_2_out2, decoder_1_out5, \очистить_все_банки );
  and and_47 (and_47_out, decoder_2_out2, decoder_1_out5);
  and and_48 (and_48_out, decoder_2_out2, decoder_1_out6, \очистить_все_банки );
  and and_49 (and_49_out, decoder_2_out2, decoder_1_out6);
  and and_50 (and_50_out, decoder_2_out2, decoder_1_out7, \очистить_все_банки );
  and and_51 (and_51_out, decoder_2_out2, decoder_1_out7);
  RAM #(.bus("separate")) ram_17 (
    .addr(multiplexer_1_out), .din(\данные_банков ), .data(\выход_данных ), .sel(and_37_out), .clk(or_3_out),
    .clr(and_36_out));  // open: str, ld
  RAM #(.bus("separate")) ram_18 (
    .addr(multiplexer_1_out), .din(\данные_банков ), .data(\выход_данных ), .sel(and_39_out), .clk(or_3_out),
    .clr(and_38_out));  // open: str, ld
  RAM #(.bus("separate")) ram_19 (
    .addr(multiplexer_1_out), .din(\данные_банков ), .data(\выход_данных ), .sel(and_41_out), .clk(or_3_out),
    .clr(and_40_out));  // open: str, ld
  RAM #(.bus("separate")) ram_20 (
    .addr(multiplexer_1_out), .din(\данные_банков ), .data(\выход_данных ), .sel(and_43_out), .clk(or_3_out),
    .clr(and_42_out));  // open: str, ld
  RAM #(.bus("separate")) ram_21 (
    .addr(multiplexer_1_out), .din(\данные_банков ), .data(\выход_данных ), .sel(and_45_out), .clk(or_3_out),
    .clr(and_44_out));  // open: str, ld
  RAM #(.bus("separate")) ram_22 (
    .addr(multiplexer_1_out), .din(\данные_банков ), .data(\выход_данных ), .sel(and_47_out), .clk(or_3_out),
    .clr(and_46_out));  // open: str, ld
  RAM #(.bus("separate")) ram_23 (
    .addr(multiplexer_1_out), .din(\данные_банков ), .data(\выход_данных ), .sel(and_49_out), .clk(or_3_out),
    .clr(and_48_out));  // open: str, ld
  RAM #(.bus("separate")) ram_24 (
    .addr(multiplexer_1_out), .din(\данные_банков ), .data(\выход_данных ), .sel(and_51_out), .clk(or_3_out),
    .clr(and_50_out));  // open: str, ld
  and and_52 (and_52_out, decoder_2_out3, decoder_1_out0);
  and and_53 (and_53_out, decoder_2_out3, decoder_1_out1);
  and and_54 (and_54_out, decoder_2_out3, decoder_1_out2);
  and and_55 (and_55_out, decoder_2_out3, decoder_1_out3);
  and and_56 (and_56_out, decoder_2_out3, decoder_1_out4);
  and and_57 (and_57_out, decoder_2_out3, decoder_1_out5);
  and and_58 (and_58_out, decoder_2_out3, decoder_1_out6);
  and and_59 (and_59_out, decoder_2_out3, decoder_1_out7);
  RAM #(.bus("separate")) ram_25 (
    .addr(multiplexer_1_out), .din(\данные_банков ), .data(\выход_данных ), .sel(and_52_out), .clk(or_3_out),
    .clr(and_60_out));  // open: str, ld
  and and_60 (and_60_out, decoder_2_out3, decoder_1_out0, \очистить_все_банки );
  RAM #(.bus("separate")) ram_26 (
    .addr(multiplexer_1_out), .din(\данные_банков ), .data(\выход_данных ), .sel(and_53_out), .clk(or_3_out),
    .clr(and_61_out));  // open: str, ld
  and and_61 (and_61_out, decoder_2_out3, decoder_1_out1, \очистить_все_банки );
  RAM #(.bus("separate")) ram_27 (
    .addr(multiplexer_1_out), .din(\данные_банков ), .data(\выход_данных ), .sel(and_54_out), .clk(or_3_out),
    .clr(and_62_out));  // open: str, ld
  and and_62 (and_62_out, decoder_2_out3, decoder_1_out2, \очистить_все_банки );
  RAM #(.bus("separate")) ram_28 (
    .addr(multiplexer_1_out), .din(\данные_банков ), .data(\выход_данных ), .sel(and_55_out), .clk(or_3_out),
    .clr(and_63_out));  // open: str, ld
  and and_63 (and_63_out, decoder_2_out3, decoder_1_out3, \очистить_все_банки );
  RAM #(.bus("separate")) ram_29 (
    .addr(multiplexer_1_out), .din(\данные_банков ), .data(\выход_данных ), .sel(and_56_out), .clk(or_3_out),
    .clr(and_64_out));  // open: str, ld
  and and_64 (and_64_out, decoder_2_out3, decoder_1_out4, \очистить_все_банки );
  RAM #(.bus("separate")) ram_30 (
    .addr(multiplexer_1_out), .din(\данные_банков ), .data(\выход_данных ), .sel(and_57_out), .clk(or_3_out),
    .clr(and_65_out));  // open: str, ld
  and and_65 (and_65_out, decoder_2_out3, decoder_1_out5, \очистить_все_банки );
  RAM #(.bus("separate")) ram_31 (
    .addr(multiplexer_1_out), .din(\данные_банков ), .data(\выход_данных ), .sel(and_58_out), .clk(or_3_out),
    .clr(and_66_out));  // open: str, ld
  and and_66 (and_66_out, decoder_2_out3, decoder_1_out6, \очистить_все_банки );
  RAM #(.bus("separate")) ram_32 (
    .addr(multiplexer_1_out), .din(\данные_банков ), .data(\выход_данных ), .sel(and_59_out), .clk(or_3_out),
    .clr(and_67_out));  // open: str, ld
  and and_67 (and_67_out, decoder_2_out3, decoder_1_out7, \очистить_все_банки );
  Decoder #(.select(3)) decoder_2 (
    .out0(decoder_2_out0), .out1(decoder_2_out1), .out2(decoder_2_out2), .out3(decoder_2_out3),
    .out4(decoder_2_out4), .out5(decoder_2_out5), .out6(decoder_2_out6), .out7(decoder_2_out7),
    .sel(register_1_q_2));  // open: en
  and and_68 (and_68_out, decoder_2_out4, decoder_1_out0);
  and and_69 (and_69_out, decoder_2_out4, decoder_1_out1);
  and and_70 (and_70_out, decoder_2_out4, decoder_1_out2);
  and and_71 (and_71_out, decoder_2_out4, decoder_1_out3);
  and and_72 (and_72_out, decoder_2_out4, decoder_1_out4);
  and and_73 (and_73_out, decoder_2_out4, decoder_1_out5);
  and and_74 (and_74_out, decoder_2_out4, decoder_1_out6);
  and and_75 (and_75_out, decoder_2_out4, decoder_1_out7);
  RAM #(.bus("separate")) ram_33 (
    .addr(multiplexer_1_out), .din(\данные_банков ), .data(\выход_данных ), .sel(and_68_out), .clk(or_3_out),
    .clr(and_76_out));  // open: str, ld
  and and_76 (and_76_out, decoder_2_out4, decoder_1_out0, \очистить_все_банки );
  RAM #(.bus("separate")) ram_34 (
    .addr(multiplexer_1_out), .din(\данные_банков ), .data(\выход_данных ), .sel(and_69_out), .clk(or_3_out),
    .clr(and_77_out));  // open: str, ld
  and and_77 (and_77_out, decoder_2_out4, decoder_1_out1, \очистить_все_банки );
  RAM #(.bus("separate")) ram_35 (
    .addr(multiplexer_1_out), .din(\данные_банков ), .data(\выход_данных ), .sel(and_70_out), .clk(or_3_out),
    .clr(and_78_out));  // open: str, ld
  and and_78 (and_78_out, decoder_2_out4, decoder_1_out2, \очистить_все_банки );
  RAM #(.bus("separate")) ram_36 (
    .addr(multiplexer_1_out), .din(\данные_банков ), .data(\выход_данных ), .sel(and_71_out), .clk(or_3_out),
    .clr(and_79_out));  // open: str, ld
  and and_79 (and_79_out, decoder_2_out4, decoder_1_out3, \очистить_все_банки );
  RAM #(.bus("separate")) ram_37 (
    .addr(multiplexer_1_out), .din(\данные_банков ), .data(\выход_данных ), .sel(and_72_out), .clk(or_3_out),
    .clr(and_80_out));  // open: str, ld
  and and_80 (and_80_out, decoder_2_out4, decoder_1_out4, \очистить_все_банки );
  RAM #(.bus("separate")) ram_38 (
    .addr(multiplexer_1_out), .din(\данные_банков ), .data(\выход_данных ), .sel(and_73_out), .clk(or_3_out),
    .clr(and_81_out));  // open: str, ld
  and and_81 (and_81_out, decoder_2_out4, decoder_1_out5, \очистить_все_банки );
  RAM #(.bus("separate")) ram_39 (
    .addr(multiplexer_1_out), .din(\данные_банков ), .data(\выход_данных ), .sel(and_74_out), .clk(or_3_out),
    .clr(and_82_out));  // open: str, ld
  and and_82 (and_82_out, decoder_2_out4, decoder_1_out6, \очистить_все_банки );
  RAM #(.bus("separate")) ram_40 (
    .addr(multiplexer_1_out), .din(\данные_банков ), .data(\выход_данных ), .sel(and_75_out), .clk(or_3_out),
    .clr(and_83_out));  // open: str, ld
  and and_83 (and_83_out, decoder_2_out4, decoder_1_out7, \очистить_все_банки );
  and and_84 (and_84_out, decoder_2_out5, decoder_1_out0, \очистить_все_банки );
  and and_85 (and_85_out, decoder_2_out5, decoder_1_out0);
  and and_86 (and_86_out, decoder_2_out5, decoder_1_out1, \очистить_все_банки );
  and and_87 (and_87_out, decoder_2_out5, decoder_1_out1);
  and and_88 (and_88_out, decoder_2_out5, decoder_1_out2, \очистить_все_банки );
  and and_89 (and_89_out, decoder_2_out5, decoder_1_out2);
  and and_90 (and_90_out, decoder_2_out5, decoder_1_out3, \очистить_все_банки );
  and and_91 (and_91_out, decoder_2_out5, decoder_1_out3);
  and and_92 (and_92_out, decoder_2_out5, decoder_1_out4, \очистить_все_банки );
  and and_93 (and_93_out, decoder_2_out5, decoder_1_out4);
  and and_94 (and_94_out, decoder_2_out5, decoder_1_out5, \очистить_все_банки );
  and and_95 (and_95_out, decoder_2_out5, decoder_1_out5);
  and and_96 (and_96_out, decoder_2_out5, decoder_1_out6, \очистить_все_банки );
  and and_97 (and_97_out, decoder_2_out5, decoder_1_out6);
  and and_98 (and_98_out, decoder_2_out5, decoder_1_out7, \очистить_все_банки );
  and and_99 (and_99_out, decoder_2_out5, decoder_1_out7);
  RAM #(.bus("separate")) ram_41 (
    .addr(multiplexer_1_out), .din(\данные_банков ), .data(\выход_данных ), .sel(and_85_out), .clk(or_3_out),
    .clr(and_84_out));  // open: str, ld
  RAM #(.bus("separate")) ram_42 (
    .addr(multiplexer_1_out), .din(\данные_банков ), .data(\выход_данных ), .sel(and_87_out), .clk(or_3_out),
    .clr(and_86_out));  // open: str, ld
  RAM #(.bus("separate")) ram_43 (
    .addr(multiplexer_1_out), .din(\данные_банков ), .data(\выход_данных ), .sel(and_89_out), .clk(or_3_out),
    .clr(and_88_out));  // open: str, ld
  RAM #(.bus("separate")) ram_44 (
    .addr(multiplexer_1_out), .din(\данные_банков ), .data(\выход_данных ), .sel(and_91_out), .clk(or_3_out),
    .clr(and_90_out));  // open: str, ld
  RAM #(.bus("separate")) ram_45 (
    .addr(multiplexer_1_out), .din(\данные_банков ), .data(\выход_данных ), .sel(and_93_out), .clk(or_3_out),
    .clr(and_92_out));  // open: str, ld
  RAM #(.bus("separate")) ram_46 (
    .addr(multiplexer_1_out), .din(\данные_банков ), .data(\выход_данных ), .sel(and_95_out), .clk(or_3_out),
    .clr(and_94_out));  // open: str, ld
  RAM #(.bus("separate")) ram_47 (
    .addr(multiplexer_1_out), .din(\данные_банков ), .data(\выход_данных ), .sel(and_97_out), .clk(or_3_out),
    .clr(and_96_out));  // open: str, ld
  RAM #(.bus("separate")) ram_48 (
    .addr(multiplexer_1_out), .din(\данные_банков ), .data(\выход_данных ), .sel(and_99_out), .clk(or_3_out),
    .clr(and_98_out));  // open: str, ld
  and and_100 (and_100_out, decoder_2_out6, decoder_1_out0);
  and and_101 (and_101_out, decoder_2_out6, decoder_1_out1);
  and and_102 (and_102_out, decoder_2_out6, decoder_1_out2);
  and and_103 (and_103_out, decoder_2_out6, decoder_1_out3);
  and and_104 (and_104_out, decoder_2_out6, decoder_1_out4);
  and and_105 (and_105_out, decoder_2_out6, decoder_1_out5);
  and and_106 (and_106_out, decoder_2_out6, decoder_1_out6);
  and and_107 (and_107_out, decoder_2_out6, decoder_1_out7);
  RAM #(.bus("separate")) ram_49 (
    .addr(multiplexer_1_out), .din(\данные_банков ), .data(\выход_данных ), .sel(and_100_out),
    .clk(or_3_out), .clr(and_108_out));  // open: str, ld
  and and_108 (and_108_out, decoder_2_out6, decoder_1_out0, \очистить_все_банки );
  RAM #(.bus("separate")) ram_50 (
    .addr(multiplexer_1_out), .din(\данные_банков ), .data(\выход_данных ), .sel(and_101_out),
    .clk(or_3_out), .clr(and_109_out));  // open: str, ld
  and and_109 (and_109_out, decoder_2_out6, decoder_1_out1, \очистить_все_банки );
  RAM #(.bus("separate")) ram_51 (
    .addr(multiplexer_1_out), .din(\данные_банков ), .data(\выход_данных ), .sel(and_102_out),
    .clk(or_3_out), .clr(and_110_out));  // open: str, ld
  and and_110 (and_110_out, decoder_2_out6, decoder_1_out2, \очистить_все_банки );
  RAM #(.bus("separate")) ram_52 (
    .addr(multiplexer_1_out), .din(\данные_банков ), .data(\выход_данных ), .sel(and_103_out),
    .clk(or_3_out), .clr(and_111_out));  // open: str, ld
  and and_111 (and_111_out, decoder_2_out6, decoder_1_out3, \очистить_все_банки );
  RAM #(.bus("separate")) ram_53 (
    .addr(multiplexer_1_out), .din(\данные_банков ), .data(\выход_данных ), .sel(and_104_out),
    .clk(or_3_out), .clr(and_112_out));  // open: str, ld
  and and_112 (and_112_out, decoder_2_out6, decoder_1_out4, \очистить_все_банки );
  RAM #(.bus("separate")) ram_54 (
    .addr(multiplexer_1_out), .din(\данные_банков ), .data(\выход_данных ), .sel(and_105_out),
    .clk(or_3_out), .clr(and_113_out));  // open: str, ld
  and and_113 (and_113_out, decoder_2_out6, decoder_1_out5, \очистить_все_банки );
  RAM #(.bus("separate")) ram_55 (
    .addr(multiplexer_1_out), .din(\данные_банков ), .data(\выход_данных ), .sel(and_106_out),
    .clk(or_3_out), .clr(and_114_out));  // open: str, ld
  and and_114 (and_114_out, decoder_2_out6, decoder_1_out6, \очистить_все_банки );
  RAM #(.bus("separate")) ram_56 (
    .addr(multiplexer_1_out), .din(\данные_банков ), .data(\выход_данных ), .sel(and_107_out),
    .clk(or_3_out), .clr(and_115_out));  // open: str, ld
  and and_115 (and_115_out, decoder_2_out6, decoder_1_out7, \очистить_все_банки );
  and and_116 (and_116_out, decoder_2_out7, decoder_1_out0, \очистить_все_банки );
  and and_117 (and_117_out, decoder_2_out7, decoder_1_out0);
  and and_118 (and_118_out, decoder_2_out7, decoder_1_out1, \очистить_все_банки );
  and and_119 (and_119_out, decoder_2_out7, decoder_1_out1);
  and and_120 (and_120_out, decoder_2_out7, decoder_1_out2, \очистить_все_банки );
  and and_121 (and_121_out, decoder_2_out7, decoder_1_out2);
  and and_122 (and_122_out, decoder_2_out7, decoder_1_out3, \очистить_все_банки );
  and and_123 (and_123_out, decoder_2_out7, decoder_1_out3);
  and and_124 (and_124_out, decoder_2_out7, decoder_1_out4, \очистить_все_банки );
  and and_125 (and_125_out, decoder_2_out7, decoder_1_out4);
  and and_126 (and_126_out, decoder_2_out7, decoder_1_out5, \очистить_все_банки );
  and and_127 (and_127_out, decoder_2_out7, decoder_1_out5);
  and and_128 (and_128_out, decoder_2_out7, decoder_1_out6, \очистить_все_банки );
  and and_129 (and_129_out, decoder_2_out7, decoder_1_out6);
  and and_130 (and_130_out, decoder_2_out7, decoder_1_out7, \очистить_все_банки );
  and and_131 (and_131_out, decoder_2_out7, decoder_1_out7);
  RAM #(.bus("separate")) ram_57 (
    .addr(multiplexer_1_out), .din(\данные_банков ), .data(\выход_данных ), .sel(and_117_out),
    .clk(or_3_out), .clr(and_116_out));  // open: str, ld
  RAM #(.bus("separate")) ram_58 (
    .addr(multiplexer_1_out), .din(\данные_банков ), .data(\выход_данных ), .sel(and_119_out),
    .clk(or_3_out), .clr(and_118_out));  // open: str, ld
  RAM #(.bus("separate")) ram_59 (
    .addr(multiplexer_1_out), .din(\данные_банков ), .data(\выход_данных ), .sel(and_121_out),
    .clk(or_3_out), .clr(and_120_out));  // open: str, ld
  RAM #(.bus("separate")) ram_60 (
    .addr(multiplexer_1_out), .din(\данные_банков ), .data(\выход_данных ), .sel(and_123_out),
    .clk(or_3_out), .clr(and_122_out));  // open: str, ld
  RAM #(.bus("separate")) ram_61 (
    .addr(multiplexer_1_out), .din(\данные_банков ), .data(\выход_данных ), .sel(and_125_out),
    .clk(or_3_out), .clr(and_124_out));  // open: str, ld
  RAM #(.bus("separate")) ram_62 (
    .addr(multiplexer_1_out), .din(\данные_банков ), .data(\выход_данных ), .sel(and_127_out),
    .clk(or_3_out), .clr(and_126_out));  // open: str, ld
  RAM #(.bus("separate")) ram_63 (
    .addr(multiplexer_1_out), .din(\данные_банков ), .data(\выход_данных ), .sel(and_129_out),
    .clk(or_3_out), .clr(and_128_out));  // open: str, ld
  RAM #(.bus("separate")) ram_64 (
    .addr(multiplexer_1_out), .din(\данные_банков ), .data(\выход_данных ), .sel(and_131_out),
    .clk(or_3_out), .clr(and_130_out));  // open: str, ld
endmodule

// озу
module _1 (
);

  main main_1 ();  // open: кординаты_банка, записать_координаты_банка, данные_банков, данные_jamp, запись_в_память, сбросить_сщётчик, jamp, такт, адресация_записи, очистить_все_банки, запись_регистр_адреса, выход_данных, адресация, in_10
endmodule
