// Logisim project джостик.circ as structural Verilog: 1 circuit, main circuit main
module main (
  input  w,
  input  s,
  input  a,
  input  d,
  input  in_5,
  input  run,
  output [7:0] out_7
);


  assign out_7 = {w, s, a, d, in_5, run, 2'b00};
endmodule
