// Logisim project полная сборка.circ as structural Verilog: 1 circuit, main circuit main
module main (
  input  in_1,
  input  in_2,
  input  in_3,
  input  in_4,
  output out_5,
  output out_6
);

  wire button_1_out, button_2_out, button_3_out, button_4_out, button_5_out, button_6_out, button_7_out,
       button_8_out, button_9_out, button_10_out, main_2_clock, x_minus_out, x_plus_out, y_minus_out,
       y_plus_out;
  wire [7:0] main_1_out_7, main_2_data, main_2_output_address, main_3_out_14, \main_3_порт_1 ,
       \main_3_порт_1_2 ;
  wire [31:0] main_4_out_3, main_4_out_4;

  Button x_plus (.out(x_plus_out));
  Button y_minus (.out(y_minus_out));
  Button x_minus (.out(x_minus_out));
  Button button_1 (.out(button_1_out));
  Button button_2 (.out(button_2_out));
  Button button_3 (.out(button_3_out));
  Button button_4 (.out(button_4_out));
  Button button_5 (.out(button_5_out));
  Button button_6 (.out(button_6_out));
  Button button_7 (.out(button_7_out));
  Button button_8 (.out(button_8_out));
  Button y_plus (.out(y_plus_out));
  Button button_9 (.out(button_9_out));
  Button button_10 (.out(button_10_out));
  \джостик_main  main_1 (
    .w(x_plus_out), .s(x_minus_out), .a(y_plus_out), .d(y_minus_out), .in_5(button_9_out),
    .run(button_10_out), .out_7(main_1_out_7));
  \процессор_номер_4_main  main_2 (
    .\адресс (button_1_out), .\ввод (main_3_out_14), .\данные (button_2_out), .\команды (button_3_out),
    .entering_an_address(button_4_out), .\данные_2 (in_1), .\команды_2 (in_2), .reset(button_5_out),
    .\сохранить (button_6_out), .\прервать (in_3), .\возобновить (in_4), .run(button_7_out),
    .stop(button_8_out), .data(main_2_data), .clock(main_2_clock), .output_address(main_2_output_address));  // open: out_15, out_16, out_17, out_18, out_19, conclusion
  \контроллер_портов_ввода_вывода_main  main_3 (
    .out_14(main_3_out_14), .\порт_ввода_1 (main_1_out_7), .\такты (main_2_clock),
    .\адрес_управления (main_2_output_address[4:0]), .\порт_1 (\main_3_порт_1 ),
    .\порт_1_2 (\main_3_порт_1_2 ), .out_13(out_5), .in_1(main_2_data), .out_15(out_6));  // open: порт_ввода_2, порт_ввода_3, порт_2, порт_2_2, порт_3, порт_3_2
  x_y_main main_4 (.in_1(\main_3_порт_1_2 ), .in_2(\main_3_порт_1 ), .out_3(main_4_out_3), .out_4(main_4_out_4));
  // DotMatrix #(.inputtype("select"), .matrixcols(32), .matrixrows(32), .persist(60)) dotmatrix_1: pin names not known; wires that end beside it: main_4_out_3, main_4_out_4
endmodule
