// Logisim project процессор номер 4.circ as structural Verilog: 8 circuits, main circuit main
module main (
  input  \адресс ,
  input  [7:0] \ввод ,
  input  \данные ,
  input  \команды ,
  input  entering_an_address,
  input  \данные_2 ,
  input  \команды_2 ,
  input  reset,
  input  \сохранить ,
  input  \прервать ,
  input  \возобновить ,
  input  run,
  input  stop,
  output [7:0] data,
  output out_15,
  output out_16,
  output out_17,
  output out_18,
  output out_19,
  output clock,
  output [7:0] output_address,
  output conclusion
);

  wire _1, _2, _3, _4, _5, _6, _7, _9, _11, _12, _13, _14, _15, _16, and_1_out, and_4_out, and_5_out,
       and_6_out, and_7_out, and_9_out, and_10_out, clock_out, d_ff_1_q, demultiplexer_2_out0,
       demultiplexer_2_out1, main_1_out_4, \n2_дешифратор_1_out_2 , \n2_дешифратор_1_out_3 ,
       \n2_дешифратор_1_out_4 , \n2_дешифратор_1_out_9 , \n2_дешифратор_1_out_11 , or_1_out, or_2_out,
       or_3_out, or_4_out, or_5_out, or_6_out, or_7_out, or_8_out, s_r_ff_1_q, s_r_ff_2_q, s_r_ff_3_q,
       s_r_ff_3_qn, \выбор_команды_данные_1_а1 , \выбор_команды_данные_1_б1 , \дешифратор_команд_1_j ,
       \дешифратор_команд_1_o , \дешифратор_команд_1_r , \дешифратор_команд_1_u , \дешифратор_команд_1_y ,
       \дешифратр_для_остатка_1_c ;
  wire [1:0] \данные_выход_данных ;
  wire [5:0] _10;
  wire [7:0] a, demultiplexer_1_out0, demultiplexer_1_out1, multiplexer_1_out, multiplexer_3_out,
       multiplexer_4_out, multiplexer_5_out, register_2_q, register_3_q, \адр , \дан ,
       \команды_выход_данных , \модернизация_для_эвм_1_out_6 , \модернизация_для_эвм_1_out_7 ;

  Clock u_clock (.out(clock_out));
  S_R_Flip_Flop s_r_ff_1 (
    .S(or_1_out), .clk(main_1_out_4), .R(\возобновить ), .Q(s_r_ff_1_q));  // open: Qn, preset, reset, en
  or or_1 (or_1_out, or_3_out, entering_an_address);
  \частотный_делитель_тактов_main  main_1 (
    .in_1(clock_out), .in_2(multiplexer_4_out), .in_3(and_1_out), .out_4(main_1_out_4));
  and and_1 (and_1_out, main_1_out_4, \n2_дешифратор_1_out_11 );
  \выбор_команды_данные  \u_выбор_команды_данные_1  (
    .\фж (\данные_2 ), .\а (\команды_2 ), .\а1 (\выбор_команды_данные_1_а1 ),
    .\б1 (\выбор_команды_данные_1_б1 ));
  Register register_1 (.D(\ввод ), .Q(\адр ), .clk(\адресс ));  // open: en, clr
  Register register_2 (.D(\ввод ), .Q(register_2_q), .clk(or_4_out));  // open: en, clr
  Register register_3 (.D(\ввод ), .Q(register_3_q), .clk(\команды ));  // open: en, clr
  Demultiplexer #(.width(8)) demultiplexer_1 (
    .out0(demultiplexer_1_out0), .out1(demultiplexer_1_out1), .in(register_2_q),
    .sel(\выбор_команды_данные_1_а1 ));  // open: en
  Demultiplexer demultiplexer_2 (
    .out0(demultiplexer_2_out0), .out1(demultiplexer_2_out1), .in(\сохранить ),
    .sel(\выбор_команды_данные_1_а1 ));  // open: en
  or or_2 (or_2_out, stop, _16);
  Multiplexer #(.width(8)) multiplexer_1 (
    .in0(\дан ), .in1(demultiplexer_1_out0), .out(multiplexer_1_out), .sel(\выбор_команды_данные_1_б1 ));  // open: en
  and and_2 (_7, clock, s_r_ff_3_qn);
  or or_3 (or_3_out, \прервать , _15);
  and and_3 (clock, main_1_out_4, s_r_ff_2_q);
  S_R_Flip_Flop s_r_ff_2 (.S(run), .clk(main_1_out_4), .R(or_2_out), .Q(s_r_ff_2_q));  // open: Qn, preset, reset, en
  or or_4 (or_4_out, \данные , d_ff_1_q);
  D_Flip_Flop d_ff_1 (.clk(clock), .D(or_6_out), .Q(d_ff_1_q));  // open: Qn, preset, en, reset
  \банковая_память_8_на_8_main  \u_команды  (
    .\кординаты_банка (_10), .\записать_координаты_банка (_11), .\данные_банков (multiplexer_1_out),
    .\данные_jamp ({\данные_выход_данных , _10}), .\запись_в_память (demultiplexer_2_out0),
    .\сбросить_сщётчик (reset), .jamp(_9), .\такт (_7), .\адресация_записи ({\данные_выход_данных , _10}),
    .\очистить_все_банки (_13), .\запись_регистр_адреса (_14), .\выход_данных (\команды_выход_данных ),
    .\адресация (\адр ), .in_10(s_r_ff_1_q));
  S_R_Flip_Flop s_r_ff_3 (
    .S(or_3_out), .clk(clock), .R(\возобновить ), .Q(s_r_ff_3_q), .Qn(s_r_ff_3_qn));  // open: preset, reset, en
  \дешифратр_для_остатка  \u_дешифратр_для_остатка_1  (
    .a(a[7]), .b(a[6]), .a_2(_16), .b_2(_15), .c(\дешифратр_для_остатка_1_c ));
  \дешифратор_команд  \u_дешифратор_команд_1  (
    .a(a[5]), .b(a[4]), .c(a[3]), .d(a[2]), .e(a[1]), .f(a[0]), .in_7(a[6]), .in_8(a[7]), .a_2(_1), .b_2(_2),
    .c_2(_3), .d_2(_4), .e_2(_5), .f_2(_6), .j(\дешифратор_команд_1_j ), .r(\дешифратор_команд_1_r ),
    .u(\дешифратор_команд_1_u ), .o(\дешифратор_команд_1_o ), .y(\дешифратор_команд_1_y ));
  \_2_дешифратор  \u_2_дешифратор_1  (
    .in_1(a), .out_2(\n2_дешифратор_1_out_2 ), .out_3(\n2_дешифратор_1_out_3 ),
    .out_4(\n2_дешифратор_1_out_4 ), .out_5(_11), .out_6(_12), .out_7(_13), .out_8(_14),
    .out_9(\n2_дешифратор_1_out_9 ), .out_11(\n2_дешифратор_1_out_11 ));  // open: out_10
  Multiplexer #(.width(8)) multiplexer_2 (
    .in0(\команды_выход_данных ), .in1(register_3_q), .out(a), .sel(s_r_ff_3_q));  // open: en
  Multiplexer #(.width(8)) multiplexer_3 (
    .in0(\дан ), .in1(demultiplexer_1_out1), .out(multiplexer_3_out), .sel(\выбор_команды_данные_1_а1 ));  // open: en
  or or_5 (or_5_out, a[0], a[1], a[2], a[3], \дешифратр_для_остатка_1_c );
  \банковая_память_8_на_8_main  \u_данные  (
    .\кординаты_банка (_10), .\записать_координаты_банка (_11), .\данные_банков (multiplexer_3_out),
    .\данные_jamp ({\данные_выход_данных , _10}), .\запись_в_память (demultiplexer_2_out1),
    .\сбросить_сщётчик (reset), .jamp(_9), .\такт (_7), .\адресация_записи ({\данные_выход_данных , _10}),
    .\очистить_все_банки (_13), .\запись_регистр_адреса (_12), .\выход_данных ({\данные_выход_данных , _10}),
    .\адресация (\адр ), .in_10(s_r_ff_1_q));
  or or_6 (or_6_out, s_r_ff_3_q, \n2_дешифратор_1_out_9 );
  Multiplexer #(.width(8)) multiplexer_4 (
    .in0({\данные_выход_данных , _10}), .in1(register_2_q), .out(multiplexer_4_out), .sel(or_6_out));  // open: en
  Multiplexer #(.width(8)) multiplexer_5 (
    .in0(multiplexer_4_out), .in1(\дан ), .out(multiplexer_5_out), .sel(\дешифратор_команд_1_y ));  // open: en
  or or_7 (or_7_out, \дешифратор_команд_1_y , \n2_дешифратор_1_out_9 , \дешифратор_команд_1_u );
  and and_4 (and_4_out, or_7_out, clock);
  and and_5 (and_5_out, clock, \дешифратор_команд_1_o );
  and and_6 (and_6_out, clock, \n2_дешифратор_1_out_2 );
  \модернизация_для_эвм  \u_модернизация_для_эвм_1  (
    .in_1(multiplexer_5_out), .in_2(and_6_out), .in_3(and_4_out), .in_4(and_5_out), .in_5(s_r_ff_2_q),
    .out_6(\модернизация_для_эвм_1_out_6 ), .out_7(\модернизация_для_эвм_1_out_7 ));
  or or_8 (or_8_out, \n2_дешифратор_1_out_4 , or_5_out);
  alu alu_1 (
    .in_2(\модернизация_для_эвм_1_out_6 ), .in_3(\модернизация_для_эвм_1_out_7 ), .out_7(\дан ),
    .out_8(out_15), .out_9(out_16), .out_10(out_17), .out_11(out_18), .out_12(out_19), .in_1(a),
    .in_5(\дешифратр_для_остатка_1_c ), .in_4(and_7_out), .in_6(\n2_дешифратор_1_out_4 ));
  and and_7 (and_7_out, or_8_out, clock);
  \джамп_в_случае  \u_джамп_в_случае_1  (
    .in_1(_1), .in_2(_2), .in_3(_3), .in_4(_4), .in_5(_5), .in_6(_6), .in_7(out_19), .in_8(out_18),
    .in_9(out_17), .in_10(out_16), .in_11(out_15), .out_12(_9));
  and and_8 (conclusion, \дешифратор_команд_1_r , clock);
  and and_9 (and_9_out, \дешифратор_команд_1_j , clock);
  Register register_4 (.D(multiplexer_4_out), .Q(output_address), .clk(and_10_out));  // open: en, clr
  and and_10 (and_10_out, clock, \n2_дешифратор_1_out_3 );
  // Probe on data
  Register register_5 (.D(\дан ), .Q(data), .clk(and_9_out));  // open: en, clr

  // Other names for the same wires on the sheet: _8 = reset; b = clock
endmodule

// ALU
module alu (
  input  [7:0] in_1,
  input  [7:0] in_2,
  input  [7:0] in_3,
  input  in_4,
  input  in_5,
  input  in_6,
  output [7:0] out_7,
  output out_8,
  output out_9,
  output out_10,
  output out_11,
  output out_12
);

  wire controlled_buffer_1_out, controlled_buffer_2_out, controlled_buffer_3_out, controlled_buffer_4_out,
       controlled_buffer_5_out, controlled_buffer_6_out, not_1_out, or_1_out, \дешифратор_для_алу_1_a_2 ,
       \дешифратор_для_алу_1_b_2 , \дешифратор_для_алу_1_c_2 , \дешифратор_для_алу_1_d_2 ,
       \дешифратор_для_алу_1_e_2 , \дешифратор_для_алу_1_f_2 , \дешифратор_для_алу_1_j ,
       \дешифратор_для_алу_1_r , \дешифратор_для_алу_1_t , \дешифратор_для_алу_1_w ;
  wire [7:0] adder_1_out, and_1_out, controlled_buffer_7_out, divider_1_out, divider_1_rem, multiplier_1_out,
       nand_1_out, nor_1_out, not_2_out, or_2_out, subtractor_1_out, xor_1_out;

  // Probe on in_1
  not not_1 (not_1_out, or_1_out);
  or or_1 (or_1_out, in_1[7], in_1[6]);
  assign controlled_buffer_1_out = not_1_out ? in_1[5] : 1'bz;  // Controlled_Buffer controlled_buffer_1
  assign controlled_buffer_2_out = not_1_out ? in_1[4] : 1'bz;  // Controlled_Buffer controlled_buffer_2
  assign controlled_buffer_3_out = not_1_out ? in_1[3] : 1'bz;  // Controlled_Buffer controlled_buffer_3
  assign controlled_buffer_4_out = not_1_out ? in_1[2] : 1'bz;  // Controlled_Buffer controlled_buffer_4
  assign controlled_buffer_5_out = not_1_out ? in_1[1] : 1'bz;  // Controlled_Buffer controlled_buffer_5
  assign controlled_buffer_6_out = not_1_out ? in_1[0] : 1'bz;  // Controlled_Buffer controlled_buffer_6
  Adder adder_1 (.a(in_2), .b(in_3), .out(adder_1_out));  // open: cin, cout
  Subtractor subtractor_1 (.a(in_2), .b(in_3), .out(subtractor_1_out));  // open: bin, bout
  Multiplier multiplier_1 (.a(in_2), .b(in_3), .out(multiplier_1_out));  // open: cin, cout
  Divider divider_1 (.a(in_2), .b(in_3), .out(divider_1_out), .rem(divider_1_rem));  // open: upper
  assign not_2_out = ~in_2;  // NOT_Gate not_2, 8 bits wide
  assign and_1_out = in_2 & in_3;  // AND_Gate and_1, 8 bits wide
  assign or_2_out = in_2 | in_3;  // OR_Gate or_2, 8 bits wide
  assign xor_1_out = in_2 ^ in_3;  // XOR_Gate xor_1, 8 bits wide
  assign nand_1_out = ~(in_2 & in_3);  // NAND_Gate nand_1, 8 bits wide
  assign nor_1_out = ~(in_2 | in_3);  // NOR_Gate nor_1, 8 bits wide
  Comparator comparator_1 (.a(in_2), .b(in_3), .gt(out_10), .eq(out_11), .lt(out_12));
  \дешифратор_для_алу  \u_дешифратор_для_алу_1  (
    .a(controlled_buffer_1_out), .b(controlled_buffer_2_out), .c(controlled_buffer_3_out),
    .d(controlled_buffer_4_out), .e(controlled_buffer_5_out), .f(controlled_buffer_6_out),
    .a_2(\дешифратор_для_алу_1_a_2 ), .b_2(\дешифратор_для_алу_1_b_2 ), .c_2(\дешифратор_для_алу_1_c_2 ),
    .d_2(\дешифратор_для_алу_1_d_2 ), .f_2(\дешифратор_для_алу_1_f_2 ), .e_2(\дешифратор_для_алу_1_e_2 ),
    .j(\дешифратор_для_алу_1_j ), .t(\дешифратор_для_алу_1_t ), .w(\дешифратор_для_алу_1_w ),
    .r(\дешифратор_для_алу_1_r ));
  assign controlled_buffer_7_out = in_5 ? divider_1_rem : 8'bz;  // Controlled_Buffer controlled_buffer_7
  assign controlled_buffer_7_out = in_6 ? in_2 : 8'bz;  // Controlled_Buffer controlled_buffer_8
  assign controlled_buffer_7_out = \дешифратор_для_алу_1_a_2  ? adder_1_out : 8'bz;  // Controlled_Buffer controlled_buffer_9
  assign controlled_buffer_7_out = \дешифратор_для_алу_1_b_2  ? subtractor_1_out : 8'bz;  // Controlled_Buffer controlled_buffer_10
  assign controlled_buffer_7_out = \дешифратор_для_алу_1_c_2  ? multiplier_1_out : 8'bz;  // Controlled_Buffer controlled_buffer_11
  assign controlled_buffer_7_out = \дешифратор_для_алу_1_d_2  ? divider_1_out : 8'bz;  // Controlled_Buffer controlled_buffer_12
  assign controlled_buffer_7_out = \дешифратор_для_алу_1_f_2  ? not_2_out : 8'bz;  // Controlled_Buffer controlled_buffer_13
  assign controlled_buffer_7_out = \дешифратор_для_алу_1_e_2  ? and_1_out : 8'bz;  // Controlled_Buffer controlled_buffer_14
  assign controlled_buffer_7_out = \дешифратор_для_алу_1_j  ? or_2_out : 8'bz;  // Controlled_Buffer controlled_buffer_15
  assign controlled_buffer_7_out = \дешифратор_для_алу_1_t  ? xor_1_out : 8'bz;  // Controlled_Buffer controlled_buffer_16
  assign controlled_buffer_7_out = \дешифратор_для_алу_1_w  ? nand_1_out : 8'bz;  // Controlled_Buffer controlled_buffer_17
  assign controlled_buffer_7_out = \дешифратор_для_алу_1_r  ? nor_1_out : 8'bz;  // Controlled_Buffer controlled_buffer_18
  Register register_1 (.D(controlled_buffer_7_out), .Q(out_7), .clk(in_4));  // open: en, clr
  or or_3 (out_8, out_7[0], out_7[1], out_7[2], out_7[3], out_7[4], out_7[5], out_7[6], out_7[7]);
  not not_3 (out_9, out_8);
endmodule

module \дешифратор_для_алу  (
  input  a,
  input  b,
  input  c,
  input  d,
  input  e,
  input  f,
  output a_2,
  output b_2,
  output c_2,
  output d_2,
  output f_2,
  output e_2,
  output j,
  output t,
  output w,
  output r
);

  wire not_1_out, not_2_out, not_3_out, not_4_out, not_5_out, not_6_out, not_7_out, not_8_out, not_9_out,
       not_10_out, not_11_out, not_12_out, not_13_out, not_14_out, not_15_out, not_16_out, not_17_out,
       not_18_out, not_19_out, not_20_out, not_21_out, not_22_out, not_23_out, not_24_out, not_25_out,
       not_26_out, not_27_out, not_28_out, not_29_out, not_30_out, not_31_out, not_32_out, not_33_out,
       not_34_out, not_35_out, not_36_out, not_37_out, not_38_out, not_39_out, not_40_out, not_41_out,
       not_42_out, not_43_out;

  not not_1 (not_1_out, a);
  not not_2 (not_2_out, b);
  not not_3 (not_3_out, c);
  not not_4 (not_4_out, d);
  not not_5 (not_5_out, e);
  not not_6 (not_6_out, a);
  not not_7 (not_7_out, b);
  not not_8 (not_8_out, c);
  not not_9 (not_9_out, d);
  not not_10 (not_10_out, f);
  not not_11 (not_11_out, a);
  not not_12 (not_12_out, b);
  not not_13 (not_13_out, c);
  not not_14 (not_14_out, d);
  not not_15 (not_15_out, a);
  not not_16 (not_16_out, b);
  not not_17 (not_17_out, c);
  not not_18 (not_18_out, e);
  not not_19 (not_19_out, f);
  not not_20 (not_20_out, a);
  not not_21 (not_21_out, b);
  not not_22 (not_22_out, c);
  not not_23 (not_23_out, e);
  not not_24 (not_24_out, a);
  not not_25 (not_25_out, b);
  not not_26 (not_26_out, c);
  not not_27 (not_27_out, f);
  not not_28 (not_28_out, a);
  not not_29 (not_29_out, b);
  not not_30 (not_30_out, c);
  not not_31 (not_31_out, a);
  not not_32 (not_32_out, b);
  not not_33 (not_33_out, d);
  not not_34 (not_34_out, e);
  not not_35 (not_35_out, f);
  not not_36 (not_36_out, a);
  not not_37 (not_37_out, b);
  not not_38 (not_38_out, d);
  not not_39 (not_39_out, e);
  not not_40 (not_40_out, a);
  not not_41 (not_41_out, b);
  not not_42 (not_42_out, d);
  not not_43 (not_43_out, f);
  and and_1 (a_2, not_1_out, not_2_out, not_3_out, not_4_out, not_5_out, f);
  and and_2 (b_2, not_6_out, not_7_out, not_8_out, not_9_out, e, not_10_out);
  and and_3 (c_2, not_11_out, not_12_out, not_13_out, not_14_out, e, f);
  and and_4 (d_2, not_15_out, not_16_out, not_17_out, d, not_18_out, not_19_out);
  and and_5 (f_2, not_20_out, not_21_out, not_22_out, d, not_23_out, f);
  and and_6 (e_2, not_24_out, not_25_out, not_26_out, d, e, not_27_out);
  and and_7 (j, not_28_out, not_29_out, not_30_out, d, e, f);
  and and_8 (t, not_31_out, not_32_out, c, not_33_out, not_34_out, not_35_out);
  and and_9 (w, not_36_out, not_37_out, c, not_38_out, not_39_out, f);
  and and_10 (r, not_40_out, not_41_out, c, not_42_out, e, not_43_out);
endmodule

// дешифратор
module \дешифратор_команд  (
  input  a,
  input  b,
  input  c,
  input  d,
  input  e,
  input  f,
  input  in_7,
  input  in_8,
  output a_2,
  output b_2,
  output c_2,
  output d_2,
  output e_2,
  output f_2,
  output j,
  output r,
  output u,
  output o,
  output y
);

  wire controlled_buffer_1_out, controlled_buffer_2_out, controlled_buffer_3_out, controlled_buffer_4_out,
       controlled_buffer_5_out, controlled_buffer_6_out, not_1_out, not_2_out, not_3_out, not_4_out,
       not_5_out, not_6_out, not_7_out, not_8_out, not_9_out, not_10_out, not_11_out, not_12_out, not_13_out,
       not_14_out, not_15_out, not_16_out, not_17_out, not_18_out, not_19_out, not_20_out, not_21_out,
       not_22_out, not_23_out, not_24_out, not_25_out, not_26_out, not_27_out, not_28_out, not_29_out,
       not_30_out, not_31_out, not_32_out, not_33_out, not_34_out, not_35_out, not_36_out, not_37_out,
       not_38_out, not_39_out, or_1_out;

  assign controlled_buffer_1_out = not_1_out ? a : 1'bz;  // Controlled_Buffer controlled_buffer_1
  assign controlled_buffer_2_out = not_1_out ? b : 1'bz;  // Controlled_Buffer controlled_buffer_2
  assign controlled_buffer_3_out = not_1_out ? c : 1'bz;  // Controlled_Buffer controlled_buffer_3
  assign controlled_buffer_4_out = not_1_out ? d : 1'bz;  // Controlled_Buffer controlled_buffer_4
  assign controlled_buffer_5_out = not_1_out ? e : 1'bz;  // Controlled_Buffer controlled_buffer_5
  assign controlled_buffer_6_out = not_1_out ? f : 1'bz;  // Controlled_Buffer controlled_buffer_6
  not not_1 (not_1_out, or_1_out);
  or or_1 (or_1_out, in_7, in_8);
  not not_2 (not_2_out, controlled_buffer_1_out);
  not not_3 (not_3_out, controlled_buffer_2_out);
  not not_4 (not_4_out, controlled_buffer_4_out);
  not not_5 (not_5_out, controlled_buffer_1_out);
  not not_6 (not_6_out, controlled_buffer_2_out);
  not not_7 (not_7_out, controlled_buffer_5_out);
  not not_8 (not_8_out, controlled_buffer_6_out);
  not not_9 (not_9_out, controlled_buffer_1_out);
  not not_10 (not_10_out, controlled_buffer_2_out);
  not not_11 (not_11_out, controlled_buffer_5_out);
  not not_12 (not_12_out, controlled_buffer_1_out);
  not not_13 (not_13_out, controlled_buffer_2_out);
  not not_14 (not_14_out, controlled_buffer_6_out);
  not not_15 (not_15_out, controlled_buffer_1_out);
  not not_16 (not_16_out, controlled_buffer_2_out);
  not not_17 (not_17_out, controlled_buffer_1_out);
  not not_18 (not_18_out, controlled_buffer_3_out);
  not not_19 (not_19_out, controlled_buffer_4_out);
  not not_20 (not_20_out, controlled_buffer_5_out);
  not not_21 (not_21_out, controlled_buffer_6_out);
  not not_22 (not_22_out, controlled_buffer_1_out);
  not not_23 (not_23_out, controlled_buffer_3_out);
  not not_24 (not_24_out, controlled_buffer_4_out);
  not not_25 (not_25_out, controlled_buffer_5_out);
  not not_26 (not_26_out, controlled_buffer_1_out);
  not not_27 (not_27_out, controlled_buffer_3_out);
  not not_28 (not_28_out, controlled_buffer_4_out);
  not not_29 (not_29_out, controlled_buffer_6_out);
  not not_30 (not_30_out, controlled_buffer_1_out);
  not not_31 (not_31_out, controlled_buffer_3_out);
  not not_32 (not_32_out, controlled_buffer_4_out);
  not not_33 (not_33_out, controlled_buffer_1_out);
  not not_34 (not_34_out, controlled_buffer_3_out);
  not not_35 (not_35_out, controlled_buffer_5_out);
  not not_36 (not_36_out, controlled_buffer_6_out);
  not not_37 (not_37_out, controlled_buffer_1_out);
  not not_38 (not_38_out, controlled_buffer_3_out);
  not not_39 (not_39_out, controlled_buffer_5_out);
  and and_1 (a_2, not_2_out, not_3_out, controlled_buffer_3_out, not_4_out, controlled_buffer_5_out, controlled_buffer_6_out);
  and and_2 (b_2, not_5_out, not_6_out, controlled_buffer_3_out, controlled_buffer_4_out, not_7_out, not_8_out);
  and and_3 (c_2, not_9_out, not_10_out, controlled_buffer_3_out, controlled_buffer_4_out, not_11_out, controlled_buffer_6_out);
  and and_4 (d_2, not_12_out, not_13_out, controlled_buffer_3_out, controlled_buffer_4_out, controlled_buffer_5_out, not_14_out);
  and and_5 (e_2, not_15_out, not_16_out, controlled_buffer_3_out, controlled_buffer_4_out, controlled_buffer_5_out, controlled_buffer_6_out);
  and and_6 (f_2, not_17_out, controlled_buffer_2_out, not_18_out, not_19_out, not_20_out, not_21_out);
  and and_7 (j, not_22_out, controlled_buffer_2_out, not_23_out, not_24_out, not_25_out, controlled_buffer_6_out);
  and and_8 (r, not_26_out, controlled_buffer_2_out, not_27_out, not_28_out, controlled_buffer_5_out, not_29_out);
  and and_9 (u, not_30_out, controlled_buffer_2_out, not_31_out, not_32_out, controlled_buffer_5_out, controlled_buffer_6_out);
  and and_10 (o, not_33_out, controlled_buffer_2_out, not_34_out, controlled_buffer_4_out, not_35_out, not_36_out);
  and and_11 (y, not_37_out, controlled_buffer_2_out, not_38_out, controlled_buffer_4_out, not_39_out, controlled_buffer_6_out);
endmodule

// jump
module \джамп_в_случае  (
  input  in_1,
  input  in_2,
  input  in_3,
  input  in_4,
  input  in_5,
  input  in_6,
  input  in_7,
  input  in_8,
  input  in_9,
  input  in_10,
  input  in_11,
  output out_12
);

  wire and_1_out, and_2_out, and_3_out, and_4_out, and_5_out;

  and and_1 (and_1_out, in_6, in_7);
  and and_2 (and_2_out, in_5, in_8);
  and and_3 (and_3_out, in_4, in_9);
  and and_4 (and_4_out, in_3, in_10);
  and and_5 (and_5_out, in_2, in_11);
  or or_1 (out_12, in_1, and_1_out, and_2_out, and_3_out, and_4_out, and_5_out);
endmodule

module \дешифратр_для_остатка  (
  input  a,
  input  b,
  output a_2,
  output b_2,
  output c
);

  wire not_1_out, not_2_out;

  not not_1 (not_1_out, a);
  not not_2 (not_2_out, b);
  and and_1 (c, a, b);
  and and_2 (a_2, not_1_out, b);
  and and_3 (b_2, a, not_2_out);
endmodule

// дешифратор
module \_2_дешифратор  (
  input  [7:0] in_1,
  output out_2,
  output out_3,
  output out_4,
  output out_5,
  output out_6,
  output out_7,
  output out_8,
  output out_9,
  output out_10,
  output out_11
);

  wire not_1_out, not_2_out, not_3_out, not_4_out, not_5_out, not_6_out, not_7_out, not_8_out, not_9_out,
       not_10_out, not_11_out, not_12_out, not_13_out, not_14_out, not_15_out, not_16_out, not_17_out,
       not_18_out, not_19_out, not_20_out, not_21_out, not_22_out, not_23_out, not_24_out, not_25_out,
       not_26_out, not_27_out, not_28_out, not_29_out, not_30_out, not_31_out, not_32_out, not_33_out,
       not_34_out, not_35_out, not_36_out, not_37_out, not_38_out, not_39_out, not_40_out, not_41_out,
       not_42_out, not_43_out, not_44_out, not_45_out, not_46_out, not_47_out, not_48_out, not_49_out,
       not_50_out, not_51_out, not_52_out, not_53_out, not_54_out, not_55_out;

  not not_1 (not_1_out, in_1[0]);
  not not_2 (not_2_out, in_1[3]);
  not not_3 (not_3_out, in_1[5]);
  not not_4 (not_4_out, in_1[6]);
  not not_5 (not_5_out, in_1[7]);
  not not_6 (not_6_out, in_1[3]);
  not not_7 (not_7_out, in_1[5]);
  not not_8 (not_8_out, in_1[6]);
  not not_9 (not_9_out, in_1[7]);
  not not_10 (not_10_out, in_1[0]);
  not not_11 (not_11_out, in_1[1]);
  not not_12 (not_12_out, in_1[2]);
  not not_13 (not_13_out, in_1[5]);
  not not_14 (not_14_out, in_1[6]);
  not not_15 (not_15_out, in_1[7]);
  not not_16 (not_16_out, in_1[1]);
  not not_17 (not_17_out, in_1[2]);
  not not_18 (not_18_out, in_1[5]);
  not not_19 (not_19_out, in_1[6]);
  not not_20 (not_20_out, in_1[7]);
  not not_21 (not_21_out, in_1[0]);
  not not_22 (not_22_out, in_1[1]);
  not not_23 (not_23_out, in_1[2]);
  not not_24 (not_24_out, in_1[3]);
  not not_25 (not_25_out, in_1[4]);
  not not_26 (not_26_out, in_1[6]);
  not not_27 (not_27_out, in_1[7]);
  not not_28 (not_28_out, in_1[1]);
  not not_29 (not_29_out, in_1[2]);
  not not_30 (not_30_out, in_1[3]);
  not not_31 (not_31_out, in_1[4]);
  not not_32 (not_32_out, in_1[6]);
  not not_33 (not_33_out, in_1[7]);
  not not_34 (not_34_out, in_1[0]);
  not not_35 (not_35_out, in_1[2]);
  not not_36 (not_36_out, in_1[3]);
  not not_37 (not_37_out, in_1[4]);
  not not_38 (not_38_out, in_1[6]);
  not not_39 (not_39_out, in_1[7]);
  not not_40 (not_40_out, in_1[2]);
  not not_41 (not_41_out, in_1[3]);
  not not_42 (not_42_out, in_1[4]);
  not not_43 (not_43_out, in_1[6]);
  not not_44 (not_44_out, in_1[7]);
  not not_45 (not_45_out, in_1[0]);
  not not_46 (not_46_out, in_1[1]);
  not not_47 (not_47_out, in_1[3]);
  not not_48 (not_48_out, in_1[4]);
  not not_49 (not_49_out, in_1[6]);
  not not_50 (not_50_out, in_1[7]);
  not not_51 (not_51_out, in_1[1]);
  not not_52 (not_52_out, in_1[3]);
  not not_53 (not_53_out, in_1[4]);
  not not_54 (not_54_out, in_1[6]);
  not not_55 (not_55_out, in_1[7]);
  and and_1 (out_2, not_1_out, in_1[1], in_1[2], not_2_out, in_1[4], not_3_out, not_4_out, not_5_out);
  and and_2 (out_3, in_1[0], in_1[1], in_1[2], not_6_out, in_1[4], not_7_out, not_8_out, not_9_out);
  and and_3 (out_4, not_10_out, not_11_out, not_12_out, in_1[3], in_1[4], not_13_out, not_14_out, not_15_out);
  and and_4 (out_5, in_1[0], not_16_out, not_17_out, in_1[3], in_1[4], not_18_out, not_19_out, not_20_out);
  and and_5 (out_6, not_21_out, not_22_out, not_23_out, not_24_out, not_25_out, in_1[5], not_26_out, not_27_out);
  and and_6 (out_7, in_1[0], not_28_out, not_29_out, not_30_out, not_31_out, in_1[5], not_32_out, not_33_out);
  and and_7 (out_8, not_34_out, in_1[1], not_35_out, not_36_out, not_37_out, in_1[5], not_38_out, not_39_out);
  and and_8 (out_9, in_1[0], in_1[1], not_40_out, not_41_out, not_42_out, in_1[5], not_43_out, not_44_out);
  and and_9 (out_10, not_45_out, not_46_out, in_1[2], not_47_out, not_48_out, in_1[5], not_49_out, not_50_out);
  and and_10 (out_11, in_1[0], not_51_out, in_1[2], not_52_out, not_53_out, in_1[5], not_54_out, not_55_out);
endmodule

module \выбор_команды_данные  (
  input  \фж ,
  input  \а ,
  output \а1 ,
  output \б1 
);

  wire not_1_out, not_2_out;

  not not_1 (not_1_out, \а );
  not not_2 (not_2_out, \фж );
  and and_1 (\а1 , \фж , not_1_out);
  and and_2 (\б1 , not_2_out, \а );
endmodule
