// Logisim project регистер с эмитацией двойного чтения.circ as structural Verilog: 4 circuits, main circuit регистр
module \регистр  (
  input  [3:0] in_1,
  input  [7:0] in_2,
  input  in_3,
  input  in_4,
  input  [3:0] in_5,
  output [7:0] out_6
);

  wire and_1_out, and_2_out, and_3_out, and_4_out, and_5_out, and_6_out, and_7_out, and_8_out, and_9_out,
       and_10_out, and_11_out, and_12_out, and_13_out, and_14_out, and_15_out, and_16_out, \декодер_1_out_2 ,
       \декодер_1_out_3 , \декодер_1_out_4 , \декодер_1_out_5 , \декодер_1_out_6 , \декодер_1_out_7 ,
       \декодер_1_out_8 , \декодер_1_out_9 , \декодер_1_out_10 , \декодер_1_out_11 , \декодер_1_out_12 ,
       \декодер_1_out_13 , \декодер_1_out_14 , \декодер_1_out_15 , \декодер_1_out_16 , \декодер_2_out_2 ,
       \декодер_2_out_3 , \декодер_2_out_4 , \декодер_2_out_5 , \декодер_2_out_6 , \декодер_2_out_7 ,
       \декодер_2_out_8 , \декодер_2_out_9 , \декодер_2_out_10 , \декодер_2_out_11 , \декодер_2_out_12 ,
       \декодер_2_out_13 , \декодер_2_out_14 , \декодер_2_out_15 , \декодер_2_out_16 ;
  wire [7:0] controlled_buffer_1_out, register_1_q, register_2_q, register_3_q, register_4_q, register_5_q,
       register_6_q, register_7_q, register_8_q, register_9_q, register_10_q, register_11_q, register_12_q,
       register_13_q, register_14_q, register_15_q;

  \декодер  \u_декодер_1  (
    .in_1(in_1), .out_2(\декодер_1_out_2 ), .out_3(\декодер_1_out_3 ), .out_4(\декодер_1_out_4 ),
    .out_5(\декодер_1_out_5 ), .out_6(\декодер_1_out_6 ), .out_7(\декодер_1_out_7 ),
    .out_8(\декодер_1_out_8 ), .out_9(\декодер_1_out_9 ), .out_10(\декодер_1_out_10 ),
    .out_11(\декодер_1_out_11 ), .out_12(\декодер_1_out_12 ), .out_13(\декодер_1_out_13 ),
    .out_14(\декодер_1_out_14 ), .out_15(\декодер_1_out_15 ), .out_16(\декодер_1_out_16 ));
  \декодер  \u_декодер_2  (
    .in_1(in_5), .out_2(\декодер_2_out_2 ), .out_3(\декодер_2_out_3 ), .out_4(\декодер_2_out_4 ),
    .out_5(\декодер_2_out_5 ), .out_6(\декодер_2_out_6 ), .out_7(\декодер_2_out_7 ),
    .out_8(\декодер_2_out_8 ), .out_9(\декодер_2_out_9 ), .out_10(\декодер_2_out_10 ),
    .out_11(\декодер_2_out_11 ), .out_12(\декодер_2_out_12 ), .out_13(\декодер_2_out_13 ),
    .out_14(\декодер_2_out_14 ), .out_15(\декодер_2_out_15 ), .out_16(\декодер_2_out_16 ));
  and and_1 (and_1_out, in_3, in_4);
  assign controlled_buffer_1_out = \декодер_1_out_2  ? register_1_q : 8'bz;  // Controlled_Buffer controlled_buffer_1
  Register register_1 (.D(in_2), .Q(register_1_q), .clk(and_3_out));  // open: en, clr
  and and_2 (and_2_out, and_1_out, \декодер_2_out_3 );
  and and_3 (and_3_out, and_1_out, \декодер_2_out_2 );
  assign controlled_buffer_1_out = \декодер_1_out_4  ? register_2_q : 8'bz;  // Controlled_Buffer controlled_buffer_2
  assign controlled_buffer_1_out = \декодер_1_out_3  ? register_3_q : 8'bz;  // Controlled_Buffer controlled_buffer_3
  Register register_2 (.D(in_2), .Q(register_2_q), .clk(and_4_out));  // open: en, clr
  Register register_3 (.D(in_2), .Q(register_3_q), .clk(and_2_out));  // open: en, clr
  and and_4 (and_4_out, and_1_out, \декодер_2_out_4 );
  assign controlled_buffer_1_out = \декодер_1_out_5  ? register_4_q : 8'bz;  // Controlled_Buffer controlled_buffer_4
  Register register_4 (.D(in_2), .Q(register_4_q), .clk(and_5_out));  // open: en, clr
  and and_5 (and_5_out, and_1_out, \декодер_2_out_5 );
  assign controlled_buffer_1_out = \декодер_1_out_6  ? register_5_q : 8'bz;  // Controlled_Buffer controlled_buffer_5
  Register register_5 (.D(in_2), .Q(register_5_q), .clk(and_7_out));  // open: en, clr
  and and_6 (and_6_out, and_1_out, \декодер_2_out_7 );
  and and_7 (and_7_out, and_1_out, \декодер_2_out_6 );
  assign controlled_buffer_1_out = \декодер_1_out_8  ? register_6_q : 8'bz;  // Controlled_Buffer controlled_buffer_6
  assign controlled_buffer_1_out = \декодер_1_out_7  ? register_7_q : 8'bz;  // Controlled_Buffer controlled_buffer_7
  Register register_6 (.D(in_2), .Q(register_6_q), .clk(and_8_out));  // open: en, clr
  Register register_7 (.D(in_2), .Q(register_7_q), .clk(and_6_out));  // open: en, clr
  and and_8 (and_8_out, and_1_out, \декодер_2_out_8 );
  assign controlled_buffer_1_out = \декодер_1_out_9  ? register_8_q : 8'bz;  // Controlled_Buffer controlled_buffer_8
  Register register_8 (.D(in_2), .Q(register_8_q), .clk(and_9_out));  // open: en, clr
  and and_9 (and_9_out, and_1_out, \декодер_2_out_9 );
  assign controlled_buffer_1_out = \декодер_1_out_10  ? register_9_q : 8'bz;  // Controlled_Buffer controlled_buffer_9
  Register register_9 (.D(in_2), .Q(register_9_q), .clk(and_11_out));  // open: en, clr
  and and_10 (and_10_out, and_1_out, \декодер_2_out_11 );
  and and_11 (and_11_out, and_1_out, \декодер_2_out_10 );
  assign controlled_buffer_1_out = \декодер_1_out_12  ? register_11_q : 8'bz;  // Controlled_Buffer controlled_buffer_10
  assign controlled_buffer_1_out = \декодер_1_out_11  ? register_10_q : 8'bz;  // Controlled_Buffer controlled_buffer_11
  Register register_10 (.D(in_2), .Q(register_10_q), .clk(and_10_out));  // open: en, clr
  Register register_11 (.D(in_2), .Q(register_11_q), .clk(and_12_out));  // open: en, clr
  and and_12 (and_12_out, and_1_out, \декодер_2_out_12 );
  assign controlled_buffer_1_out = \декодер_1_out_13  ? register_12_q : 8'bz;  // Controlled_Buffer controlled_buffer_12
  Register register_12 (.D(in_2), .Q(register_12_q), .clk(and_13_out));  // open: en, clr
  and and_13 (and_13_out, and_1_out, \декодер_2_out_13 );
  assign controlled_buffer_1_out = \декодер_1_out_14  ? register_13_q : 8'bz;  // Controlled_Buffer controlled_buffer_13
  Register register_13 (.D(in_2), .Q(register_13_q), .clk(and_14_out));  // open: en, clr
  and and_14 (and_14_out, and_1_out, \декодер_2_out_14 );
  and and_15 (and_15_out, and_1_out, \декодер_2_out_15 );
  assign controlled_buffer_1_out = \декодер_1_out_16  ? register_15_q : 8'bz;  // Controlled_Buffer controlled_buffer_14
  assign controlled_buffer_1_out = \декодер_1_out_15  ? register_14_q : 8'bz;  // Controlled_Buffer controlled_buffer_15
  Register register_14 (.D(in_2), .Q(register_14_q), .clk(and_15_out));  // open: en, clr
  Register register_15 (.D(in_2), .Q(register_15_q), .clk(and_16_out));  // open: en, clr
  and and_16 (and_16_out, and_1_out, \декодер_2_out_16 );
  assign out_6 = controlled_buffer_1_out & {8{in_4}};  // AND_Gate and_17, 8 bits wide
endmodule

module \декодер  (
  input  [3:0] in_1,
  output out_2,
  output out_3,
  output out_4,
  output out_5,
  output out_6,
  output out_7,
  output out_8,
  output out_9,
  output out_10,
  output out_11,
  output out_12,
  output out_13,
  output out_14,
  output out_15,
  output out_16
);

  wire not_1_out, not_2_out, not_3_out, not_4_out, not_5_out, not_6_out, not_7_out, not_8_out, not_9_out,
       not_10_out, not_11_out, not_12_out, not_13_out, not_14_out, not_15_out, not_16_out, not_17_out,
       not_18_out, not_19_out, not_20_out, not_21_out, not_22_out, not_23_out, not_24_out, not_25_out,
       not_26_out, not_27_out, not_28_out, not_29_out, not_30_out, not_31_out, not_32_out;

  not not_1 (not_1_out, in_1[0]);
  not not_2 (not_2_out, in_1[1]);
  not not_3 (not_3_out, in_1[2]);
  not not_4 (not_4_out, in_1[3]);
  not not_5 (not_5_out, in_1[1]);
  not not_6 (not_6_out, in_1[2]);
  not not_7 (not_7_out, in_1[3]);
  not not_8 (not_8_out, in_1[0]);
  not not_9 (not_9_out, in_1[2]);
  not not_10 (not_10_out, in_1[3]);
  not not_11 (not_11_out, in_1[2]);
  not not_12 (not_12_out, in_1[3]);
  not not_13 (not_13_out, in_1[0]);
  not not_14 (not_14_out, in_1[1]);
  not not_15 (not_15_out, in_1[3]);
  not not_16 (not_16_out, in_1[1]);
  not not_17 (not_17_out, in_1[3]);
  not not_18 (not_18_out, in_1[0]);
  not not_19 (not_19_out, in_1[3]);
  not not_20 (not_20_out, in_1[3]);
  not not_21 (not_21_out, in_1[0]);
  not not_22 (not_22_out, in_1[1]);
  not not_23 (not_23_out, in_1[2]);
  not not_24 (not_24_out, in_1[1]);
  not not_25 (not_25_out, in_1[2]);
  not not_26 (not_26_out, in_1[0]);
  not not_27 (not_27_out, in_1[2]);
  not not_28 (not_28_out, in_1[2]);
  not not_29 (not_29_out, in_1[0]);
  not not_30 (not_30_out, in_1[1]);
  not not_31 (not_31_out, in_1[1]);
  not not_32 (not_32_out, in_1[0]);
  // AND_Gate and_1 has open pins: in0=not_1_out, in1=not_2_out, in2=not_3_out, in3=not_4_out, out=open
  and and_2 (out_2, in_1[0], not_5_out, not_6_out, not_7_out);
  and and_3 (out_3, not_8_out, in_1[1], not_9_out, not_10_out);
  and and_4 (out_4, in_1[0], in_1[1], not_11_out, not_12_out);
  and and_5 (out_5, not_13_out, not_14_out, in_1[2], not_15_out);
  and and_6 (out_6, in_1[0], not_16_out, in_1[2], not_17_out);
  and and_7 (out_7, not_18_out, in_1[1], in_1[2], not_19_out);
  and and_8 (out_8, in_1[0], in_1[1], in_1[2], not_20_out);
  and and_9 (out_9, not_21_out, not_22_out, not_23_out, in_1[3]);
  and and_10 (out_10, in_1[0], not_24_out, not_25_out, in_1[3]);
  and and_11 (out_11, not_26_out, in_1[1], not_27_out, in_1[3]);
  and and_12 (out_12, in_1[0], in_1[1], not_28_out, in_1[3]);
  and and_13 (out_13, not_29_out, not_30_out, in_1[2], in_1[3]);
  and and_14 (out_14, in_1[0], not_31_out, in_1[2], in_1[3]);
  and and_15 (out_15, not_32_out, in_1[1], in_1[2], in_1[3]);
  and and_16 (out_16, in_1[0], in_1[1], in_1[2], in_1[3]);
endmodule

module \эмитация_двойного_чтения  (
  input  [3:0] in_1,
  input  [3:0] in_2,
  input  [7:0] in_3,
  input  in_4,
  input  in_5,
  input  [3:0] in_6,
  output [7:0] out_7,
  output [7:0] out_8
);

  \регистр  \u_регистр_1  (.in_1(in_1), .in_2(in_3), .in_3(in_4), .in_4(in_5), .in_5(in_6), .out_6(out_7));
  \регистр  \u_регистр_2  (.in_1(in_2), .in_2(in_3), .in_3(in_4), .in_4(in_5), .in_5(in_6), .out_6(out_8));
endmodule

module \модернизация_для_эвм  (
  input  [7:0] in_1,
  input  in_2,
  input  in_3,
  input  in_4,
  input  in_5,
  output [7:0] out_6,
  output [7:0] out_7
);

  wire [3:0] register_1_q, register_2_q, register_3_q;

  Register #(.width(4)) register_1 (.D(in_1[3:0]), .Q(register_1_q), .clk(in_2));  // open: en, clr
  Register #(.width(4)) register_2 (.D(in_1[7:4]), .Q(register_2_q), .clk(in_2));  // open: en, clr
  Register #(.width(4)) register_3 (.D(in_1[3:0]), .Q(register_3_q), .clk(in_4));  // open: en, clr
  \эмитация_двойного_чтения  \u_эмитация_двойного_чтения_1  (
    .in_1(register_1_q), .in_2(register_2_q), .in_3(in_1), .in_4(in_3), .in_5(in_5), .in_6(register_3_q),
    .out_7(out_6), .out_8(out_7));
endmodule
