// Logisim project частотный делитель тактов.circ as structural Verilog: 1 circuit, main circuit main
module main (
  input  in_1,
  input  [7:0] in_2,
  input  in_3,
  output out_4
);

  wire and_1_out, and_2_out, comparator_1_eq, comparator_2_eq, d_ff_1_q, not_1_out;
  wire [7:0] counter_1_q, register_1_q;

  Counter counter_1 (.Q(counter_1_q), .clk(in_1), .clr(d_ff_1_q));  // open: load, D, count, carry
  Register register_1 (.D(in_2), .Q(register_1_q), .clk(in_3));  // open: en, clr
  Comparator comparator_1 (.a(counter_1_q), .b(register_1_q), .eq(comparator_1_eq));  // open: gt, lt
  Comparator comparator_2 (.a(register_1_q), .b({8{1'b0}}), .eq(comparator_2_eq));  // open: gt, lt
  and and_1 (and_1_out, comparator_2_eq, in_1);
  D_Flip_Flop d_ff_1 (.clk(in_1), .D(comparator_1_eq), .Q(d_ff_1_q));  // open: Qn, preset, en, reset
  and and_2 (and_2_out, d_ff_1_q, not_1_out);
  not not_1 (not_1_out, comparator_2_eq);
  or or_1 (out_4, and_2_out, and_1_out);
endmodule
