// Logisim project полная реализация эвм.circ as structural Verilog: 3 circuits, main circuit main
module main (
  input  \не_используется ,
  input  manual_execution_of_operations,
  input  entering_data_into_the_register,
  input  address,
  input  remember_the_address,
  input  manual_address_management,
  input  commands_data,
  input  in_8,
  output out_9,
  output out_10,
  output out_11,
  output out_12,
  output out_13,
  output clock
);

  wire _0_out, _1_out, _2_out, _3_out, _4_out, _5_out, _6_out, _7_out, _8_out, _9_out,
       continue_execution_out, delete_out, input_commands_data_out, main_2_conclusion, main_3_out_4,
       main_3_out_5, main_3_out_6, main_3_out_7, main_3_out_8, main_3_out_9, main_3_out_10, main_3_out_11,
       main_3_out_12, main_3_out_13, main_3_out_14, main_3_out_15, main_3_out_16, main_3_out_17,
       main_3_out_18, main_3_out_19, main_3_out_20, main_3_out_21, main_3_out_22, main_3_out_23,
       main_3_out_24, reset_pc_out, run_out, stop_out;
  wire [7:0] main_1_out_14, main_2_data, main_2_output_address, \схема_выбора_шин_1_out_6 ,
       \схема_выбора_шин_1_out_7 , \схема_выбора_шин_1_out_8 ;

  Button _9 (.out(_9_out));
  Button _8 (.out(_8_out));
  Button _6 (.out(_6_out));
  Button _5 (.out(_5_out));
  Button _2 (.out(_2_out));
  Button _3 (.out(_3_out));
  Button _0 (.out(_0_out));
  \контроллер_клавиатуры_main  main_1 (
    .in_1(in_8), .in_2(\не_используется ), .in_3(delete_out), .out_14(main_1_out_14), ._0(_0_out),
    ._1(_1_out), ._2(_2_out), ._3(_3_out), ._4(_4_out), ._5(_5_out), ._6(_6_out), ._7(_7_out), ._8(_8_out),
    ._9(_9_out));
  Button _7 (.out(_7_out));
  Button _4 (.out(_4_out));
  Button _1 (.out(_1_out));
  Button delete (.out(delete_out));
  // Probe on main_1_out_14
  Button reset_pc (.out(reset_pc_out));
  Button input_commands_data (.out(input_commands_data_out));
  Button continue_execution (.out(continue_execution_out));
  Button run (.out(run_out));
  Button stop (.out(stop_out));
  \схема_выбора_шин  \u_схема_выбора_шин_1  (
    .in_1(main_1_out_14), .in_2(manual_execution_of_operations), .in_3(entering_data_into_the_register),
    .in_4(address), .in_5(remember_the_address), .out_6(\схема_выбора_шин_1_out_6 ),
    .out_7(\схема_выбора_шин_1_out_7 ), .out_8(\схема_выбора_шин_1_out_8 ));
  \процессор_номер_3_main  main_2 (
    .address(\схема_выбора_шин_1_out_6 ), .entering_data_into_the_register(\схема_выбора_шин_1_out_7 ),
    .manual_operation(\схема_выбора_шин_1_out_8 ), .entering_an_address(manual_address_management),
    .manual_input(commands_data), .reset(reset_pc_out), .in_7(input_commands_data_out),
    .\input (continue_execution_out), .run(run_out), .stop(stop_out), .data(main_2_data), .out_12(out_9),
    .out_13(out_10), .out_14(out_11), .out_15(out_12), .out_16(out_13), .clock(clock),
    .output_address(main_2_output_address), .conclusion(main_2_conclusion));
  \программная_реализация_устройства_вывода_на_3_7_сегментных_индикаторах_с_портом_main  main_3 (
    .in_1(main_2_data), .in_2(main_2_conclusion), .in_3(main_2_output_address), .out_16(main_3_out_16),
    .out_17(main_3_out_17), .out_18(main_3_out_18), .out_19(main_3_out_19), .out_20(main_3_out_20),
    .out_21(main_3_out_21), .out_22(main_3_out_22), .out_23(main_3_out_23), .out_24(main_3_out_24),
    .out_4(main_3_out_4), .out_5(main_3_out_5), .out_6(main_3_out_6), .out_7(main_3_out_7),
    .out_8(main_3_out_8), .out_9(main_3_out_9), .out_10(main_3_out_10), .out_11(main_3_out_11),
    .out_12(main_3_out_12), .out_13(main_3_out_13), .out_14(main_3_out_14), .out_15(main_3_out_15));
  _7_Segment_Display u_7_segment_display_1 (
    .g(main_3_out_4), .f(main_3_out_5), .a(main_3_out_6), .b(main_3_out_7), .e(main_3_out_16),
    .d(main_3_out_17), .c(main_3_out_18));  // open: dp
  _7_Segment_Display u_7_segment_display_2 (
    .g(main_3_out_8), .f(main_3_out_9), .a(main_3_out_10), .b(main_3_out_11), .e(main_3_out_19),
    .d(main_3_out_20), .c(main_3_out_21));  // open: dp
  _7_Segment_Display u_7_segment_display_3 (
    .g(main_3_out_12), .f(main_3_out_13), .a(main_3_out_14), .b(main_3_out_15), .e(main_3_out_22),
    .d(main_3_out_23), .c(main_3_out_24));  // open: dp
endmodule

module \шифратор  (
  input  a1,
  input  a2,
  input  a3,
  output b1,
  output b2
);

  wire and_1_out, and_2_out, and_3_out, and_4_out, not_1_out, not_2_out, not_3_out, not_4_out, not_5_out,
       not_6_out, not_7_out, not_8_out;

  not not_1 (not_1_out, a1);
  not not_2 (not_2_out, a3);
  not not_3 (not_3_out, a2);
  not not_4 (not_4_out, a3);
  not not_5 (not_5_out, a1);
  not not_6 (not_6_out, a2);
  not not_7 (not_7_out, a2);
  not not_8 (not_8_out, a3);
  and and_1 (and_1_out, not_1_out, a2, not_2_out);
  and and_2 (and_2_out, a1, not_3_out, not_4_out);
  and and_3 (and_3_out, not_5_out, not_6_out, a3);
  and and_4 (and_4_out, a1, not_7_out, not_8_out);
  or or_1 (b1, and_1_out, and_2_out);
  or or_2 (b2, and_3_out, and_4_out);
endmodule

module \схема_выбора_шин  (
  input  [7:0] in_1,
  input  in_2,
  input  in_3,
  input  in_4,
  input  in_5,
  output [7:0] out_6,
  output [7:0] out_7,
  output [7:0] out_8
);

  wire [1:0] \шифратор_1_b2 ;
  wire [7:0] demultiplexer_1_out1;

  Demultiplexer #(.select(2), .width(8)) demultiplexer_1 (
    .out1(demultiplexer_1_out1), .out2(out_7), .out3(out_8), .in(in_1), .sel(\шифратор_1_b2 ));  // open: out0, en
  \шифратор  \u_шифратор_1  (.a1(in_2), .a2(in_3), .a3(in_4), .b1(\шифратор_1_b2 [1]), .b2(\шифратор_1_b2 [0]));
  Register register_1 (.D(demultiplexer_1_out1), .Q(out_6), .clk(in_5));  // open: en, clr
endmodule
