// Logisim project программная реализация устройства вывода на 3 7 сегментных индикаторах с портом.circ as structural Verilog: 4 circuits, main circuit main
module main (
  input  [7:0] in_1,
  input  in_2,
  input  [7:0] in_3,
  output out_4,
  output out_5,
  output out_6,
  output out_7,
  output out_8,
  output out_9,
  output out_10,
  output out_11,
  output out_12,
  output out_13,
  output out_14,
  output out_15,
  output out_16,
  output out_17,
  output out_18,
  output out_19,
  output out_20,
  output out_21,
  output out_22,
  output out_23,
  output out_24
);

  wire and_1_out, and_2_out, and_3_out, and_4_out, and_5_out, and_6_out, clock_1_out, not_1_out, or_1_out;
  wire [3:0] register_1_q, register_2_q, register_3_q;

  Clock clock_1 (.out(clock_1_out));
  or or_1 (or_1_out, in_3[3], in_3[4], in_3[5], in_3[6], in_3[7]);
  Register #(.width(4)) register_1 (.D(in_1[3:0]), .Q(register_1_q), .clk(and_1_out));  // open: en, clr
  and and_1 (and_1_out, and_2_out, in_2, clock_1_out);
  and and_2 (and_2_out, in_3[2], not_1_out);
  not not_1 (not_1_out, or_1_out);
  Register #(.width(4)) register_2 (.D(in_1[3:0]), .Q(register_2_q), .clk(and_3_out));  // open: en, clr
  and and_3 (and_3_out, and_4_out, in_2, clock_1_out);
  and and_4 (and_4_out, in_3[1], not_1_out);
  Register #(.width(4)) register_3 (.D(in_1[3:0]), .Q(register_3_q), .clk(and_5_out));  // open: en, clr
  and and_5 (and_5_out, and_6_out, in_2, clock_1_out);
  and and_6 (and_6_out, in_3[0], not_1_out);
  dc_7_segment dc_7_segment_1 (
    .in_1(register_1_q), .b(out_7), .a(out_6), .f(out_5), .g(out_4), .e(out_16), .d(out_17), .c(out_18));
  dc_7_segment dc_7_segment_2 (
    .in_1(register_2_q), .b(out_11), .a(out_10), .f(out_9), .g(out_8), .e(out_19), .d(out_20), .c(out_21));
  dc_7_segment dc_7_segment_3 (
    .in_1(register_3_q), .b(out_15), .a(out_14), .f(out_13), .g(out_12), .e(out_22), .d(out_23), .c(out_24));
endmodule

module dc (
  input  [3:0] in_1,
  output _0,
  output _1,
  output _2,
  output _3,
  output _4,
  output _5,
  output _6,
  output _7,
  output _8,
  output _9
);

  wire not_1_out, not_2_out, not_3_out, not_4_out;

  not not_1 (not_1_out, in_1[3]);
  not not_2 (not_2_out, in_1[2]);
  not not_3 (not_3_out, in_1[1]);
  not not_4 (not_4_out, in_1[0]);
  and and_1 (_0, not_4_out, not_3_out, not_2_out, not_1_out);
  and and_2 (_1, in_1[0], not_3_out, not_2_out, not_1_out);
  and and_3 (_2, not_4_out, in_1[1], not_2_out, not_1_out);
  and and_4 (_3, in_1[0], in_1[1], not_2_out, not_1_out);
  and and_5 (_4, not_3_out, not_4_out, in_1[2], not_1_out);
  and and_6 (_5, in_1[0], not_3_out, in_1[2], not_1_out);
  and and_7 (_6, not_4_out, in_1[1], in_1[2], not_1_out);
  and and_8 (_7, in_1[0], in_1[1], in_1[2], not_1_out);
  and and_9 (_8, not_2_out, not_3_out, not_4_out, in_1[3]);
  and and_10 (_9, in_1[0], not_3_out, not_2_out, in_1[3]);
endmodule

module dc_7_segment (
  input  [3:0] in_1,
  output b,
  output a,
  output f,
  output g,
  output e,
  output d,
  output c
);

  wire dc_1__0, dc_1__1, dc_1__2, dc_1__3, dc_1__4, dc_1__5, dc_1__6, dc_1__7, dc_1__8, dc_1__9;

  dc dc_1 (
    .in_1(in_1), ._0(dc_1__0), ._1(dc_1__1), ._2(dc_1__2), ._3(dc_1__3), ._4(dc_1__4), ._5(dc_1__5),
    ._6(dc_1__6), ._7(dc_1__7), ._8(dc_1__8), ._9(dc_1__9));
  _7_segment u_7_segment_1 (
    ._9(dc_1__9), ._8(dc_1__8), ._7(dc_1__7), ._6(dc_1__6), ._5(dc_1__5), ._4(dc_1__4), ._3(dc_1__3),
    ._2(dc_1__2), ._1(dc_1__1), ._0(dc_1__0), .b(b), .a(a), .f(f), .g(g), .e(e), .d(d), .c(c));
endmodule

module _7_segment (
  input  _9,
  input  _8,
  input  _7,
  input  _6,
  input  _5,
  input  _4,
  input  _3,
  input  _2,
  input  _1,
  input  _0,
  output b,
  output a,
  output f,
  output g,
  output e,
  output d,
  output c
);

  or or_1 (b, _9, _8, _7, _4, _3, _2, _1, _0);
  or or_2 (a, _9, _8, _7, _6, _5, _3, _2, _0);
  or or_3 (f, _9, _8, _6, _5, _4, _0);
  or or_4 (g, _8, _6, _5, _9, _4, _3, _2);
  or or_5 (e, _8, _6, _2, _0);
  or or_6 (d, _9, _8, _6, _5, _3, _2, _0);
  or or_7 (c, _0, _1, _3, _4, _5, _6, _7, _8, _9);
endmodule
