// Logisim project процессор номер 3.circ as structural Verilog: 6 circuits, main circuit main
module main (
  input  [7:0] address,
  input  [7:0] entering_data_into_the_register,
  input  [7:0] manual_operation,
  input  entering_an_address,
  input  manual_input,
  input  reset,
  input  in_7,
  input  \input ,
  input  run,
  input  stop,
  output [7:0] data,
  output out_12,
  output out_13,
  output out_14,
  output out_15,
  output out_16,
  output clock,
  output [7:0] output_address,
  output conclusion
);

  wire and_1_out, and_3_out, and_4_out, and_5_out, and_6_out, clock_out, demultiplexer_2_out0,
       demultiplexer_2_out1, not_1_out, or_1_out, or_2_out, or_3_out, s_r_ff_1_q, s_r_ff_2_q, s_r_ff_2_qn,
       \дешифратор_команд_1_a_2 , \дешифратор_команд_1_b_2 , \дешифратор_команд_1_c_2 ,
       \дешифратор_команд_1_d_2 , \дешифратор_команд_1_e_2 , \дешифратор_команд_1_f_2 ,
       \дешифратор_команд_1_j , \дешифратор_команд_1_o , \дешифратор_команд_1_r , \дешифратор_команд_1_u ,
       \дешифратор_команд_1_y , \дешифратр_для_остатка_1_a_2 , \дешифратр_для_остатка_1_b_2 ,
       \дешифратр_для_остатка_1_c , \джамп_в_случае_1_out_12 ;
  wire [7:0] alu_1_out_5, counter_1_q, demultiplexer_1_out0, demultiplexer_1_out1, demultiplexer_3_out0,
       demultiplexer_3_out1, multiplexer_1_out, multiplexer_2_out, multiplexer_3_out, multiplexer_5_out,
       ram_1_data, ram_2_data, register_1_q, register_2_q, register_3_q;

  Clock u_clock (.out(clock_out));
  Demultiplexer #(.width(8)) demultiplexer_1 (
    .out0(demultiplexer_1_out0), .out1(demultiplexer_1_out1), .in(entering_data_into_the_register),
    .sel(manual_input));  // open: en
  Demultiplexer demultiplexer_2 (
    .out0(demultiplexer_2_out0), .out1(demultiplexer_2_out1), .in(in_7), .sel(manual_input));  // open: en
  or or_1 (or_1_out, stop, \дешифратр_для_остатка_1_a_2 );
  not not_1 (not_1_out, \джамп_в_случае_1_out_12 );
  Counter counter_1 (
    .load(\джамп_в_случае_1_out_12 ), .D(output_address), .count(not_1_out), .Q(counter_1_q),
    .clk(and_1_out), .clr(reset));  // open: carry
  and and_1 (and_1_out, clock, s_r_ff_2_qn);
  and and_2 (clock, clock_out, s_r_ff_1_q);
  S_R_Flip_Flop s_r_ff_1 (.S(run), .clk(clock_out), .R(or_1_out), .Q(s_r_ff_1_q));  // open: Qn, preset, reset, en
  Multiplexer #(.width(8)) multiplexer_1 (
    .in0(counter_1_q), .in1(address), .out(multiplexer_1_out), .sel(entering_an_address));  // open: en
  S_R_Flip_Flop s_r_ff_2 (
    .S(\дешифратр_для_остатка_1_b_2 ), .clk(clock), .R(\input ), .Q(s_r_ff_2_q), .Qn(s_r_ff_2_qn));  // open: preset, reset, en
  RAM #(.bus("separate")) ram_1 (
    .addr(multiplexer_1_out), .din(demultiplexer_1_out0), .data(ram_1_data), .clk(demultiplexer_2_out0));  // open: str, sel, ld, clr
  \дешифратр_для_остатка  \u_дешифратр_для_остатка_1  (
    .a(multiplexer_2_out[7]), .b(multiplexer_2_out[6]), .a_2(\дешифратр_для_остатка_1_a_2 ),
    .b_2(\дешифратр_для_остатка_1_b_2 ), .c(\дешифратр_для_остатка_1_c ));
  \дешифратор_команд  \u_дешифратор_команд_1  (
    .a(multiplexer_2_out[5]), .b(multiplexer_2_out[4]), .c(multiplexer_2_out[3]), .d(multiplexer_2_out[2]),
    .e(multiplexer_2_out[1]), .f(multiplexer_2_out[0]), .a_2(\дешифратор_команд_1_a_2 ),
    .b_2(\дешифратор_команд_1_b_2 ), .c_2(\дешифратор_команд_1_c_2 ), .d_2(\дешифратор_команд_1_d_2 ),
    .e_2(\дешифратор_команд_1_e_2 ), .f_2(\дешифратор_команд_1_f_2 ), .j(\дешифратор_команд_1_j ),
    .r(\дешифратор_команд_1_r ), .u(\дешифратор_команд_1_u ), .o(\дешифратор_команд_1_o ),
    .y(\дешифратор_команд_1_y ));
  Multiplexer #(.width(8)) multiplexer_2 (
    .in0(ram_1_data), .in1(manual_operation), .out(multiplexer_2_out), .sel(s_r_ff_2_q));  // open: en
  Multiplexer #(.width(8)) multiplexer_3 (
    .in0(register_3_q), .in1(demultiplexer_1_out1), .out(multiplexer_3_out), .sel(manual_input));  // open: en
  or or_2 (or_2_out, multiplexer_2_out[0], multiplexer_2_out[1], multiplexer_2_out[2], multiplexer_2_out[3], \дешифратр_для_остатка_1_c );
  RAM #(.bus("separate")) ram_2 (
    .addr(multiplexer_1_out), .din(multiplexer_3_out), .data(ram_2_data), .clk(demultiplexer_2_out1));  // open: str, sel, ld, clr
  Multiplexer #(.width(8)) multiplexer_4 (
    .in0(ram_2_data), .in1(entering_data_into_the_register), .out(output_address), .sel(s_r_ff_2_q));  // open: en
  Multiplexer #(.width(8)) multiplexer_5 (
    .in0(output_address), .in1(register_3_q), .out(multiplexer_5_out), .sel(\дешифратор_команд_1_y ));  // open: en
  or or_3 (or_3_out, \дешифратор_команд_1_y , \дешифратор_команд_1_u );
  Demultiplexer #(.width(8)) demultiplexer_3 (
    .out0(demultiplexer_3_out0), .out1(demultiplexer_3_out1), .in(multiplexer_5_out),
    .sel(\дешифратор_команд_1_o ));  // open: en
  and and_3 (and_3_out, or_3_out, clock);
  and and_4 (and_4_out, clock, \дешифратор_команд_1_o );
  Register register_1 (.D(demultiplexer_3_out0), .Q(register_1_q), .clk(and_3_out));  // open: en, clr
  Register register_2 (.D(demultiplexer_3_out1), .Q(register_2_q), .clk(and_4_out));  // open: en, clr
  alu alu_1 (
    .in_2(register_1_q), .in_3(register_2_q), .out_5(alu_1_out_5), .out_6(out_12), .out_7(out_13),
    .out_8(out_14), .out_9(out_15), .out_10(out_16), .in_1(multiplexer_2_out),
    .in_4(\дешифратр_для_остатка_1_c ));
  \джамп_в_случае  \u_джамп_в_случае_1  (
    .in_1(\дешифратор_команд_1_a_2 ), .in_2(\дешифратор_команд_1_b_2 ), .in_3(\дешифратор_команд_1_c_2 ),
    .in_4(\дешифратор_команд_1_d_2 ), .in_5(\дешифратор_команд_1_e_2 ), .in_6(\дешифратор_команд_1_f_2 ),
    .in_7(out_16), .in_8(out_15), .in_9(out_14), .in_10(out_13), .in_11(out_12),
    .out_12(\джамп_в_случае_1_out_12 ));
  and and_5 (and_5_out, or_2_out, clock);
  Register register_3 (.D(alu_1_out_5), .Q(register_3_q), .clk(and_5_out));  // open: en, clr
  and and_6 (and_6_out, \дешифратор_команд_1_j , clock);
  and and_7 (conclusion, \дешифратор_команд_1_r , clock);
  Register register_4 (.D(register_3_q), .Q(data), .clk(and_6_out));  // open: en, clr
endmodule

module alu (
  input  [7:0] in_1,
  input  [7:0] in_2,
  input  [7:0] in_3,
  input  in_4,
  output [7:0] out_5,
  output out_6,
  output out_7,
  output out_8,
  output out_9,
  output out_10
);

  wire \дешифратор_для_алу_1_a_2 , \дешифратор_для_алу_1_b_2 , \дешифратор_для_алу_1_c_2 ,
       \дешифратор_для_алу_1_d_2 , \дешифратор_для_алу_1_e_2 , \дешифратор_для_алу_1_f_2 ,
       \дешифратор_для_алу_1_j , \дешифратор_для_алу_1_r , \дешифратор_для_алу_1_t , \дешифратор_для_алу_1_w ;
  wire [7:0] adder_1_out, and_1_out, divider_1_out, divider_1_rem, multiplier_1_out, nand_1_out, nor_1_out,
       not_1_out, or_1_out, subtractor_1_out, xor_1_out;

  // Probe on in_1
  Adder adder_1 (.a(in_2), .b(in_3), .out(adder_1_out));  // open: cin, cout
  Subtractor subtractor_1 (.a(in_2), .b(in_3), .out(subtractor_1_out));  // open: bin, bout
  Multiplier multiplier_1 (.a(in_2), .b(in_3), .out(multiplier_1_out));  // open: cin, cout
  Divider divider_1 (.a(in_2), .b(in_3), .out(divider_1_out), .rem(divider_1_rem));  // open: upper
  assign not_1_out = ~in_2;  // NOT_Gate not_1, 8 bits wide
  assign and_1_out = in_2 & in_3;  // AND_Gate and_1, 8 bits wide
  assign or_1_out = in_2 | in_3;  // OR_Gate or_1, 8 bits wide
  assign xor_1_out = in_2 ^ in_3;  // XOR_Gate xor_1, 8 bits wide
  assign nand_1_out = ~(in_2 & in_3);  // NAND_Gate nand_1, 8 bits wide
  assign nor_1_out = ~(in_2 | in_3);  // NOR_Gate nor_1, 8 bits wide
  Comparator comparator_1 (.a(in_2), .b(in_3), .gt(out_8), .eq(out_9), .lt(out_10));
  \дешифратор_для_алу  \u_дешифратор_для_алу_1  (
    .a(in_1[5]), .b(in_1[4]), .c(in_1[3]), .d(in_1[2]), .e(in_1[1]), .f(in_1[0]),
    .a_2(\дешифратор_для_алу_1_a_2 ), .b_2(\дешифратор_для_алу_1_b_2 ), .c_2(\дешифратор_для_алу_1_c_2 ),
    .d_2(\дешифратор_для_алу_1_d_2 ), .f_2(\дешифратор_для_алу_1_f_2 ), .e_2(\дешифратор_для_алу_1_e_2 ),
    .j(\дешифратор_для_алу_1_j ), .t(\дешифратор_для_алу_1_t ), .w(\дешифратор_для_алу_1_w ),
    .r(\дешифратор_для_алу_1_r ));
  assign out_5 = in_4 ? divider_1_rem : 8'bz;  // Controlled_Buffer controlled_buffer_1
  assign out_5 = \дешифратор_для_алу_1_a_2  ? adder_1_out : 8'bz;  // Controlled_Buffer controlled_buffer_2
  assign out_5 = \дешифратор_для_алу_1_b_2  ? subtractor_1_out : 8'bz;  // Controlled_Buffer controlled_buffer_3
  assign out_5 = \дешифратор_для_алу_1_c_2  ? multiplier_1_out : 8'bz;  // Controlled_Buffer controlled_buffer_4
  assign out_5 = \дешифратор_для_алу_1_d_2  ? divider_1_out : 8'bz;  // Controlled_Buffer controlled_buffer_5
  assign out_5 = \дешифратор_для_алу_1_f_2  ? not_1_out : 8'bz;  // Controlled_Buffer controlled_buffer_6
  assign out_5 = \дешифратор_для_алу_1_e_2  ? and_1_out : 8'bz;  // Controlled_Buffer controlled_buffer_7
  assign out_5 = \дешифратор_для_алу_1_j  ? or_1_out : 8'bz;  // Controlled_Buffer controlled_buffer_8
  assign out_5 = \дешифратор_для_алу_1_t  ? xor_1_out : 8'bz;  // Controlled_Buffer controlled_buffer_9
  assign out_5 = \дешифратор_для_алу_1_w  ? nand_1_out : 8'bz;  // Controlled_Buffer controlled_buffer_10
  assign out_5 = \дешифратор_для_алу_1_r  ? nor_1_out : 8'bz;  // Controlled_Buffer controlled_buffer_11
  or or_2 (out_6, out_5[0], out_5[1], out_5[2], out_5[3], out_5[4], out_5[5], out_5[6], out_5[7]);
  not not_2 (out_7, out_6);
endmodule

module \дешифратор_для_алу  (
  input  a,
  input  b,
  input  c,
  input  d,
  input  e,
  input  f,
  output a_2,
  output b_2,
  output c_2,
  output d_2,
  output f_2,
  output e_2,
  output j,
  output t,
  output w,
  output r
);

  wire not_1_out, not_2_out, not_3_out, not_4_out, not_5_out, not_6_out, not_7_out, not_8_out, not_9_out,
       not_10_out, not_11_out, not_12_out, not_13_out, not_14_out, not_15_out, not_16_out, not_17_out,
       not_18_out, not_19_out, not_20_out, not_21_out, not_22_out, not_23_out, not_24_out, not_25_out,
       not_26_out, not_27_out, not_28_out, not_29_out, not_30_out, not_31_out, not_32_out, not_33_out,
       not_34_out, not_35_out, not_36_out, not_37_out, not_38_out, not_39_out, not_40_out, not_41_out,
       not_42_out, not_43_out;

  not not_1 (not_1_out, a);
  not not_2 (not_2_out, b);
  not not_3 (not_3_out, c);
  not not_4 (not_4_out, d);
  not not_5 (not_5_out, e);
  not not_6 (not_6_out, a);
  not not_7 (not_7_out, b);
  not not_8 (not_8_out, c);
  not not_9 (not_9_out, d);
  not not_10 (not_10_out, f);
  not not_11 (not_11_out, a);
  not not_12 (not_12_out, b);
  not not_13 (not_13_out, c);
  not not_14 (not_14_out, d);
  not not_15 (not_15_out, a);
  not not_16 (not_16_out, b);
  not not_17 (not_17_out, c);
  not not_18 (not_18_out, e);
  not not_19 (not_19_out, f);
  not not_20 (not_20_out, a);
  not not_21 (not_21_out, b);
  not not_22 (not_22_out, c);
  not not_23 (not_23_out, e);
  not not_24 (not_24_out, a);
  not not_25 (not_25_out, b);
  not not_26 (not_26_out, c);
  not not_27 (not_27_out, f);
  not not_28 (not_28_out, a);
  not not_29 (not_29_out, b);
  not not_30 (not_30_out, c);
  not not_31 (not_31_out, a);
  not not_32 (not_32_out, b);
  not not_33 (not_33_out, d);
  not not_34 (not_34_out, e);
  not not_35 (not_35_out, f);
  not not_36 (not_36_out, a);
  not not_37 (not_37_out, b);
  not not_38 (not_38_out, d);
  not not_39 (not_39_out, e);
  not not_40 (not_40_out, a);
  not not_41 (not_41_out, b);
  not not_42 (not_42_out, d);
  not not_43 (not_43_out, f);
  and and_1 (a_2, not_1_out, not_2_out, not_3_out, not_4_out, not_5_out, f);
  and and_2 (b_2, not_6_out, not_7_out, not_8_out, not_9_out, e, not_10_out);
  and and_3 (c_2, not_11_out, not_12_out, not_13_out, not_14_out, e, f);
  and and_4 (d_2, not_15_out, not_16_out, not_17_out, d, not_18_out, not_19_out);
  and and_5 (f_2, not_20_out, not_21_out, not_22_out, d, not_23_out, f);
  and and_6 (e_2, not_24_out, not_25_out, not_26_out, d, e, not_27_out);
  and and_7 (j, not_28_out, not_29_out, not_30_out, d, e, f);
  and and_8 (t, not_31_out, not_32_out, c, not_33_out, not_34_out, not_35_out);
  and and_9 (w, not_36_out, not_37_out, c, not_38_out, not_39_out, f);
  and and_10 (r, not_40_out, not_41_out, c, not_42_out, e, not_43_out);
endmodule

module \дешифратор_команд  (
  input  a,
  input  b,
  input  c,
  input  d,
  input  e,
  input  f,
  output a_2,
  output b_2,
  output c_2,
  output d_2,
  output e_2,
  output f_2,
  output j,
  output r,
  output u,
  output o,
  output y
);

  wire not_1_out, not_2_out, not_3_out, not_4_out, not_5_out, not_6_out, not_7_out, not_8_out, not_9_out,
       not_10_out, not_11_out, not_12_out, not_13_out, not_14_out, not_15_out, not_16_out, not_17_out,
       not_18_out, not_19_out, not_20_out, not_21_out, not_22_out, not_23_out, not_24_out, not_25_out,
       not_26_out, not_27_out, not_28_out, not_29_out, not_30_out, not_31_out, not_32_out, not_33_out,
       not_34_out, not_35_out, not_36_out, not_37_out, not_38_out;

  not not_1 (not_1_out, a);
  not not_2 (not_2_out, b);
  not not_3 (not_3_out, d);
  not not_4 (not_4_out, a);
  not not_5 (not_5_out, b);
  not not_6 (not_6_out, e);
  not not_7 (not_7_out, f);
  not not_8 (not_8_out, a);
  not not_9 (not_9_out, b);
  not not_10 (not_10_out, e);
  not not_11 (not_11_out, a);
  not not_12 (not_12_out, b);
  not not_13 (not_13_out, f);
  not not_14 (not_14_out, a);
  not not_15 (not_15_out, b);
  not not_16 (not_16_out, a);
  not not_17 (not_17_out, c);
  not not_18 (not_18_out, d);
  not not_19 (not_19_out, e);
  not not_20 (not_20_out, f);
  not not_21 (not_21_out, a);
  not not_22 (not_22_out, c);
  not not_23 (not_23_out, d);
  not not_24 (not_24_out, e);
  not not_25 (not_25_out, a);
  not not_26 (not_26_out, c);
  not not_27 (not_27_out, d);
  not not_28 (not_28_out, f);
  not not_29 (not_29_out, a);
  not not_30 (not_30_out, c);
  not not_31 (not_31_out, d);
  not not_32 (not_32_out, a);
  not not_33 (not_33_out, c);
  not not_34 (not_34_out, e);
  not not_35 (not_35_out, f);
  not not_36 (not_36_out, a);
  not not_37 (not_37_out, c);
  not not_38 (not_38_out, e);
  and and_1 (a_2, not_1_out, not_2_out, c, not_3_out, e, f);
  and and_2 (b_2, not_4_out, not_5_out, c, d, not_6_out, not_7_out);
  and and_3 (c_2, not_8_out, not_9_out, c, d, not_10_out, f);
  and and_4 (d_2, not_11_out, not_12_out, c, d, e, not_13_out);
  and and_5 (e_2, not_14_out, not_15_out, c, d, e, f);
  and and_6 (f_2, not_16_out, b, not_17_out, not_18_out, not_19_out, not_20_out);
  and and_7 (j, not_21_out, b, not_22_out, not_23_out, not_24_out, f);
  and and_8 (r, not_25_out, b, not_26_out, not_27_out, e, not_28_out);
  and and_9 (u, not_29_out, b, not_30_out, not_31_out, e, f);
  and and_10 (o, not_32_out, b, not_33_out, d, not_34_out, not_35_out);
  and and_11 (y, not_36_out, b, not_37_out, d, not_38_out, f);
endmodule

module \джамп_в_случае  (
  input  in_1,
  input  in_2,
  input  in_3,
  input  in_4,
  input  in_5,
  input  in_6,
  input  in_7,
  input  in_8,
  input  in_9,
  input  in_10,
  input  in_11,
  output out_12
);

  wire and_1_out, and_2_out, and_3_out, and_4_out, and_5_out;

  and and_1 (and_1_out, in_5, in_8);
  and and_2 (and_2_out, in_6, in_7);
  and and_3 (and_3_out, in_4, in_9);
  and and_4 (and_4_out, in_3, in_10);
  and and_5 (and_5_out, in_2, in_11);
  or or_1 (out_12, in_1, and_2_out, and_1_out, and_3_out, and_4_out, and_5_out);
endmodule

module \дешифратр_для_остатка  (
  input  a,
  input  b,
  output a_2,
  output b_2,
  output c
);

  wire not_1_out, not_2_out;

  not not_1 (not_1_out, a);
  not not_2 (not_2_out, b);
  and and_1 (c, a, b);
  and and_2 (a_2, not_1_out, b);
  and and_3 (b_2, a, not_2_out);
endmodule
