// Logisim project процессор гарвардской архитектуры.circ as structural Verilog: 7 circuits, main circuit main
module main (
  input  [7:0] in_1,
  input  [7:0] in_2,
  input  in_3,
  input  in_4,
  input  in_5
);

  wire and_1_out, and_2_out, clock_1_out, demultiplexer_2_out0, demultiplexer_2_out1, not_1_out, or_1_out,
       or_2_out;
  wire [7:0] adder_1_out, counter_1_q, demultiplexer_1_out0, demultiplexer_1_out1, multiplexer_1_out,
       multiplexer_2_out, multiplexer_3_out, multiplexer_4_out, ram_1_data, ram_2_data, register_1_q,
       subtractor_1_out;

  Clock clock_1 (.out(clock_1_out));
  Demultiplexer #(.width(8)) demultiplexer_1 (
    .out0(demultiplexer_1_out0), .out1(demultiplexer_1_out1), .in(in_2), .sel(in_3));  // open: en
  Demultiplexer demultiplexer_2 (
    .out0(demultiplexer_2_out0), .out1(demultiplexer_2_out1), .in(in_4), .sel(in_3));  // open: en
  not not_1 (not_1_out, ram_1_data[3]);
  Multiplexer #(.width(8)) multiplexer_1 (
    .in0(counter_1_q), .in1(in_1), .out(multiplexer_1_out), .sel(in_3));  // open: en
  Counter counter_1 (
    .load(ram_1_data[3]), .D(ram_2_data), .count(not_1_out), .Q(counter_1_q), .clk(clock_1_out), .clr(in_5));  // open: carry
  RAM #(.bus("separate")) ram_1 (
    .addr(multiplexer_1_out), .din(demultiplexer_1_out0), .data(ram_1_data), .clk(demultiplexer_2_out0));  // open: str, sel, ld, clr
  Multiplexer #(.width(8)) multiplexer_2 (
    .in0(register_1_q), .in1(demultiplexer_1_out1), .out(multiplexer_2_out), .sel(in_3));  // open: en
  or or_1 (or_1_out, demultiplexer_2_out1, and_1_out);
  and and_1 (and_1_out, clock_1_out, ram_1_data[4]);
  RAM #(.bus("separate")) ram_2 (
    .addr(multiplexer_1_out), .din(multiplexer_2_out), .data(ram_2_data), .clk(or_1_out));  // open: str, sel, ld, clr
  Adder adder_1 (.a(register_1_q), .b(ram_2_data), .out(adder_1_out));  // open: cin, cout
  Subtractor subtractor_1 (.a(register_1_q), .b(ram_2_data), .out(subtractor_1_out));  // open: bin, bout
  Multiplexer #(.width(8)) multiplexer_3 (
    .in0(adder_1_out), .in1(subtractor_1_out), .out(multiplexer_3_out), .sel(ram_1_data[2]));  // open: en
  Multiplexer #(.width(8)) multiplexer_4 (
    .in0(multiplexer_3_out), .in1(ram_2_data), .out(multiplexer_4_out), .sel(ram_1_data[0]));  // open: en
  or or_2 (or_2_out, ram_1_data[2], ram_1_data[1], ram_1_data[0]);
  and and_2 (and_2_out, or_2_out, clock_1_out);
  Register register_1 (.D(multiplexer_4_out), .Q(register_1_q), .clk(and_2_out));  // open: en, clr
endmodule

module \алу  (
  input  [7:0] in_1,
  input  [7:0] in_2,
  input  [7:0] in_3,
  output [7:0] out_4
);

  wire [2:0] \чтоб_небыло_ошибок_1_v_2 ;
  wire [7:0] adder_1_out, and_1_out, divider_1_out, multiplier_1_out, or_1_out, subtractor_1_out, xor_1_out;

  // Probe on in_1
  // Probe on in_2
  Adder adder_1 (.a(in_1), .b(in_2), .out(adder_1_out));  // open: cin, cout
  Subtractor subtractor_1 (.a(in_1), .b(in_2), .out(subtractor_1_out));  // open: bin, bout
  Multiplier multiplier_1 (.a(in_1), .b(in_2), .out(multiplier_1_out));  // open: cin, cout
  Divider divider_1 (.a(in_1), .b(in_2), .out(divider_1_out));  // open: upper, rem
  assign and_1_out = in_1 & in_2;  // AND_Gate and_1, 8 bits wide
  assign or_1_out = in_1 | in_2;  // OR_Gate or_1, 8 bits wide
  assign xor_1_out = in_1 ^ in_2;  // XOR_Gate xor_1, 8 bits wide
  // Probe on \чтоб_небыло_ошибок_1_v_2 
  Multiplexer #(.select(3), .width(8)) multiplexer_1 (
    .in0(adder_1_out), .in1(subtractor_1_out), .in2(multiplier_1_out), .in3(divider_1_out), .in4(and_1_out),
    .in5(or_1_out), .in6(xor_1_out), .in7(in_2), .out(out_4), .sel(\чтоб_небыло_ошибок_1_v_2 ));  // open: en
  \чтоб_небыло_ошибок  \u_чтоб_небыло_ошибок_1  (
    .a(in_3[7]), .b(in_3[6]), .v(in_3[5]), .g(in_3[4]), .d(in_3[3]), .w(in_3[2]), .e(in_3[1]), .z(in_3[0]),
    .a_2(\чтоб_небыло_ошибок_1_v_2 [2]), .d_2(\чтоб_небыло_ошибок_1_v_2 [1]),
    .v_2(\чтоб_небыло_ошибок_1_v_2 [0]));
  // Probe on out_4
endmodule

module \дешифратор_команд  (
  input  \а ,
  input  \б ,
  input  \в ,
  input  \г ,
  output \б_2 ,
  output \в_2 ,
  output \г_2 ,
  output \д ,
  output \е ,
  output \ё ,
  output \ж ,
  output \з 
);

  wire not_1_out, not_2_out, not_3_out, not_4_out, not_5_out, not_6_out, not_7_out, not_8_out, not_9_out,
       not_10_out, not_11_out, not_12_out;

  and and_1 (\б_2 , \а , \б , \в , \г );
  not not_1 (not_1_out, \г );
  not not_2 (not_2_out, \в );
  not not_3 (not_3_out, \в );
  not not_4 (not_4_out, \г );
  not not_5 (not_5_out, \б );
  not not_6 (not_6_out, \б );
  not not_7 (not_7_out, \г );
  not not_8 (not_8_out, \б );
  not not_9 (not_9_out, \в );
  not not_10 (not_10_out, \б );
  not not_11 (not_11_out, \в );
  not not_12 (not_12_out, \г );
  and and_2 (\в_2 , \а , \б , \в , not_1_out);
  and and_3 (\г_2 , \а , \б , not_2_out, \г );
  and and_4 (\д , \а , \б , not_3_out, not_4_out);
  and and_5 (\е , \а , not_5_out, \в , \г );
  and and_6 (\ё , \а , not_6_out, \в , not_7_out);
  and and_7 (\ж , \а , not_8_out, not_9_out, \г );
  and and_8 (\з , \а , not_10_out, not_11_out, not_12_out);
endmodule

module \моя_реализация_на_дешифраторе_с_алу  (
  input  [7:0] in_1,
  input  in_2,
  input  in_3,
  input  in_4,
  input  in_5,
  input  in_6,
  input  in_7,
  input  in_8,
  output [7:0] out_9,
  output [7:0] out_10
);

  wire and_1_out, and_2_out, and_3_out, and_4_out, clock_1_out, demultiplexer_2_out0, demultiplexer_2_out1,
       not_1_out, or_1_out, or_2_out, or_3_out, or_4_out, or_5_out, s_r_ff_1_q, \дешифратор_команд_1_в_2 ,
       \дешифратор_команд_1_г_2 , \дешифратор_команд_1_д , \дешифратор_команд_1_е , \дешифратор_команд_1_ж ,
       \дешифратор_команд_1_з , \дешифратор_команд_1_ё ;
  wire [7:0] counter_1_q, demultiplexer_1_out0, demultiplexer_1_out1, multiplexer_1_out, ram_1_data,
       ram_2_data, register_1_q, \алу_1_out_4 , \регистер_а_1_out_6 ;

  Demultiplexer #(.width(8)) demultiplexer_1 (
    .out0(demultiplexer_1_out0), .out1(demultiplexer_1_out1), .in(in_1), .sel(in_2));  // open: en
  Demultiplexer demultiplexer_2 (
    .out0(demultiplexer_2_out0), .out1(demultiplexer_2_out1), .in(in_4), .sel(in_2));  // open: en
  Clock clock_1 (.out(clock_1_out));
  or or_1 (or_1_out, \дешифратор_команд_1_з , in_7);
  not not_1 (not_1_out, \дешифратор_команд_1_ж );
  S_R_Flip_Flop s_r_ff_1 (.Q(s_r_ff_1_q), .preset(in_8), .reset(or_1_out));  // open: S, clk, R, Qn, en
  Counter counter_1 (
    .load(\дешифратор_команд_1_ж ), .D(ram_2_data), .count(not_1_out), .Q(counter_1_q), .clk(or_2_out),
    .clr(in_5));  // open: carry
  or or_2 (or_2_out, in_6, and_1_out);
  and and_1 (and_1_out, clock_1_out, s_r_ff_1_q);
  \дешифратор_команд  \u_дешифратор_команд_1  (
    .\а (ram_1_data[3]), .\б (ram_1_data[2]), .\в (ram_1_data[1]), .\г (ram_1_data[0]),
    .\в_2 (\дешифратор_команд_1_в_2 ), .\г_2 (\дешифратор_команд_1_г_2 ), .\д (\дешифратор_команд_1_д ),
    .\е (\дешифратор_команд_1_е ), .\ё (\дешифратор_команд_1_ё ), .\ж (\дешифратор_команд_1_ж ),
    .\з (\дешифратор_команд_1_з ));  // open: б_2
  RAM #(.bus("separate")) ram_1 (
    .addr(counter_1_q), .din(demultiplexer_1_out0), .data(ram_1_data), .clk(demultiplexer_2_out0));  // open: str, sel, ld, clr
  Multiplexer #(.width(8)) multiplexer_1 (
    .in0(register_1_q), .in1(demultiplexer_1_out1), .out(multiplexer_1_out), .sel(in_2));  // open: en
  or or_3 (or_3_out, demultiplexer_2_out1, and_2_out);
  and and_2 (and_2_out, and_1_out, \дешифратор_команд_1_ё );
  RAM #(.bus("separate")) ram_2 (
    .addr(counter_1_q), .din(multiplexer_1_out), .data(ram_2_data), .clk(or_3_out));  // open: str, sel, ld, clr
  \регистер_а  \u_регистер_а_1  (
    .in_1(ram_2_data), .in_2(register_1_q), .in_3(\дешифратор_команд_1_г_2 ), .in_4(\дешифратор_команд_1_д ),
    .out_6(\регистер_а_1_out_6 ), .in_5(and_1_out));
  \алу  \u_алу_1  (.in_1(register_1_q), .in_2(\регистер_а_1_out_6 ), .out_4(\алу_1_out_4 ), .in_3(ram_1_data));
  or or_4 (or_4_out, \дешифратор_команд_1_е , ram_1_data[2]);
  or or_5 (or_5_out, or_4_out, ram_1_data[1], ram_1_data[0]);
  // Probe on \алу_1_out_4 
  // Probe on register_1_q
  and and_3 (and_3_out, or_5_out, and_1_out);
  Register register_1 (.D(\алу_1_out_4 ), .Q(register_1_q), .clk(and_3_out), .clr(in_3));  // open: en
  Register register_2 (.D(register_1_q), .Q(out_9), .clk(\дешифратор_команд_1_в_2 ));  // open: en, clr
  Register register_3 (.D(ram_2_data), .Q(out_10), .clk(and_4_out), .clr(and_4_out));  // open: en
  and and_4 (and_4_out, ram_1_data[4], \дешифратор_команд_1_з );
  // Probe on out_9
endmodule

module \дешифратор_для_алу  (
  input  \а ,
  input  \б ,
  input  \в ,
  output \а_2 ,
  output \б_2 ,
  output \в_2 
);

  wire not_1_out, not_2_out, not_3_out, not_4_out;

  not not_1 (not_1_out, \в );
  not not_2 (not_2_out, \в );
  not not_3 (not_3_out, \а );
  not not_4 (not_4_out, \б );
  and and_1 (\а_2 , \а , not_1_out);
  and and_2 (\б_2 , \б , not_2_out);
  and and_3 (\в_2 , not_3_out, not_4_out, \в );
endmodule

module \чтоб_небыло_ошибок  (
  input  a,
  input  b,
  input  v,
  input  g,
  input  d,
  input  w,
  input  e,
  input  z,
  output a_2,
  output d_2,
  output v_2
);

  wire not_1_out, not_2_out, not_3_out, not_4_out, not_5_out, not_6_out, not_7_out, not_8_out, not_9_out,
       not_10_out, not_11_out, not_12_out, not_13_out, not_14_out, not_15_out;

  not not_1 (not_1_out, a);
  not not_2 (not_2_out, b);
  not not_3 (not_3_out, v);
  not not_4 (not_4_out, g);
  not not_5 (not_5_out, d);
  not not_6 (not_6_out, a);
  not not_7 (not_7_out, b);
  not not_8 (not_8_out, v);
  not not_9 (not_9_out, g);
  not not_10 (not_10_out, d);
  not not_11 (not_11_out, a);
  not not_12 (not_12_out, b);
  not not_13 (not_13_out, v);
  not not_14 (not_14_out, g);
  not not_15 (not_15_out, d);
  and and_1 (a_2, not_1_out, not_2_out, not_3_out, not_4_out, not_5_out, w);
  and and_2 (d_2, not_6_out, not_7_out, not_8_out, not_9_out, not_10_out, e);
  and and_3 (v_2, not_11_out, not_12_out, not_13_out, not_14_out, not_15_out, z);
endmodule

module \регистер_а  (
  input  [7:0] in_1,
  input  [7:0] in_2,
  input  in_3,
  input  in_4,
  input  in_5,
  output [7:0] out_6
);

  wire and_1_out, or_1_out;
  wire [7:0] multiplexer_1_out;

  Multiplexer #(.width(8)) multiplexer_1 (.in0(in_1), .in1(in_2), .out(multiplexer_1_out), .sel(in_3));  // open: en
  or or_1 (or_1_out, in_3, in_4);
  and and_1 (and_1_out, or_1_out, in_5);
  Register register_1 (.D(multiplexer_1_out), .Q(out_6), .clk(and_1_out));  // open: en, clr
endmodule
