// Logisim project реализация процессора 2.circ as structural Verilog: 1 circuit, main circuit main
module main (
  input  in_1
);

  wire and_1_out, and_2_out, and_3_out, clock_1_out, not_1_out, or_1_out, or_2_out;
  wire [7:0] adder_1_out, counter_1_q, multiplexer_1_out, multiplexer_2_out, multiplexer_3_out, ram_1_data,
       ram_2_data, register_1_q, register_2_q, subtractor_1_out;

  not not_1 (not_1_out, ram_1_data[5]);
  Clock clock_1 (.out(clock_1_out));
  Counter counter_1 (
    .load(ram_1_data[5]), .D(ram_2_data), .count(not_1_out), .Q(counter_1_q), .clk(clock_1_out), .clr(in_1));  // open: carry
  RAM ram_1 (.addr(counter_1_q), .data(ram_1_data));  // open: sel, clk, ld, clr
  and and_1 (and_1_out, ram_1_data[2], clock_1_out);
  RAM #(.bus("separate")) ram_2 (
    .addr(counter_1_q), .din(register_2_q), .data(ram_2_data), .clk(and_1_out));  // open: str, sel, ld, clr
  // Probe on ram_2_data
  Multiplexer #(.width(8)) multiplexer_1 (
    .in0(ram_2_data), .in1(register_2_q), .out(multiplexer_1_out), .sel(ram_1_data[3]));  // open: en
  or or_1 (or_1_out, ram_1_data[3], ram_1_data[4]);
  and and_2 (and_2_out, or_1_out, clock_1_out);
  // Probe on register_1_q
  Register register_1 (.D(multiplexer_1_out), .Q(register_1_q), .clk(and_2_out));  // open: en, clr
  Adder adder_1 (.a(ram_2_data), .b(register_1_q), .out(adder_1_out));  // open: cin, cout
  Subtractor subtractor_1 (.a(ram_2_data), .b(register_1_q), .out(subtractor_1_out));  // open: bin, bout
  Multiplexer #(.width(8)) multiplexer_2 (
    .in0(adder_1_out), .in1(subtractor_1_out), .out(multiplexer_2_out), .sel(ram_1_data[1]));  // open: en
  // Probe on register_2_q
  Register register_2 (.D(multiplexer_3_out), .Q(register_2_q), .clk(and_3_out));  // open: en, clr
  Multiplexer #(.width(8)) multiplexer_3 (
    .in0(multiplexer_2_out), .in1(ram_2_data), .out(multiplexer_3_out), .sel(ram_1_data[6]));  // open: en
  or or_2 (or_2_out, ram_1_data[1], ram_1_data[6], ram_1_data[0]);
  and and_3 (and_3_out, or_2_out, clock_1_out);

  // Notes on the sheet:
  //   озу команд
  //   озу данных
endmodule
