// Logisim project текстовый дисплей — копия.circ as structural Verilog: 1 circuit, main circuit main
module main (
);

  wire _1, _1a, _1b, _1c, _2, _2a, _2b, _2c, _3, _3a, _3b, _3c, _4, _4a, _4b, _4c, _5, _5a, _5b, _5c, _6,
       _6a, _6b, _6c, _7, _7a, _7b, _7c, _8, _8a, _8b, _8c, a, clock_1_out, controlled_buffer_3_out,
       controlled_buffer_6_out, controlled_buffer_9_out, controlled_buffer_12_out, controlled_buffer_15_out,
       controlled_buffer_18_out, controlled_buffer_21_out, controlled_buffer_24_out,
       controlled_buffer_27_out, controlled_buffer_30_out, controlled_buffer_33_out,
       controlled_buffer_36_out, controlled_buffer_39_out, controlled_buffer_42_out,
       controlled_buffer_45_out, controlled_buffer_48_out, controlled_buffer_51_out,
       controlled_buffer_54_out, controlled_buffer_57_out, controlled_buffer_60_out,
       controlled_buffer_63_out, controlled_buffer_66_out, controlled_buffer_69_out,
       controlled_buffer_72_out, controlled_buffer_75_out, controlled_buffer_78_out,
       controlled_buffer_81_out, controlled_buffer_84_out, controlled_buffer_87_out,
       controlled_buffer_90_out, controlled_buffer_93_out, controlled_buffer_96_out,
       controlled_buffer_99_out, controlled_buffer_102_out, controlled_buffer_105_out,
       controlled_buffer_108_out, controlled_buffer_111_out, controlled_buffer_114_out,
       controlled_buffer_117_out, controlled_buffer_120_out, controlled_buffer_123_out,
       controlled_buffer_126_out, controlled_buffer_129_out, controlled_buffer_132_out,
       controlled_buffer_135_out, controlled_buffer_138_out, controlled_buffer_141_out,
       controlled_buffer_144_out, controlled_buffer_147_out, controlled_buffer_150_out,
       controlled_buffer_153_out, controlled_buffer_156_out, controlled_buffer_159_out,
       controlled_buffer_162_out, controlled_buffer_165_out, controlled_buffer_168_out,
       controlled_buffer_171_out, controlled_buffer_174_out, controlled_buffer_177_out,
       controlled_buffer_180_out, controlled_buffer_183_out, controlled_buffer_186_out,
       controlled_buffer_189_out, controlled_buffer_192_out, controlled_buffer_194_out,
       controlled_buffer_196_out, controlled_buffer_198_out, controlled_buffer_200_out,
       controlled_buffer_202_out, controlled_buffer_204_out, controlled_buffer_206_out,
       controlled_buffer_208_out, controlled_buffer_210_out, controlled_buffer_212_out,
       controlled_buffer_214_out, controlled_buffer_216_out, controlled_buffer_218_out,
       controlled_buffer_220_out, controlled_buffer_222_out, controlled_buffer_224_out,
       controlled_buffer_226_out, controlled_buffer_228_out, controlled_buffer_230_out,
       controlled_buffer_232_out, controlled_buffer_234_out, controlled_buffer_236_out,
       controlled_buffer_238_out, controlled_buffer_240_out, controlled_buffer_242_out,
       controlled_buffer_244_out, controlled_buffer_246_out, controlled_buffer_248_out,
       controlled_buffer_250_out, controlled_buffer_252_out, controlled_buffer_254_out,
       controlled_buffer_256_out, controlled_buffer_259_out, controlled_buffer_262_out,
       controlled_buffer_265_out, controlled_buffer_268_out, controlled_buffer_271_out,
       controlled_buffer_274_out, controlled_buffer_277_out, controlled_buffer_280_out,
       controlled_buffer_283_out, controlled_buffer_286_out, controlled_buffer_289_out,
       controlled_buffer_292_out, controlled_buffer_295_out, controlled_buffer_298_out,
       controlled_buffer_301_out, controlled_buffer_304_out, controlled_buffer_307_out,
       controlled_buffer_310_out, controlled_buffer_313_out, controlled_buffer_316_out,
       controlled_buffer_319_out, controlled_buffer_322_out, controlled_buffer_325_out,
       controlled_buffer_328_out, controlled_buffer_331_out, controlled_buffer_334_out,
       controlled_buffer_337_out, controlled_buffer_340_out, controlled_buffer_343_out,
       controlled_buffer_346_out, controlled_buffer_349_out, controlled_buffer_352_out, d_ff_4_q,
       decoder_2_out0, decoder_2_out1, decoder_2_out2, decoder_2_out3, decoder_2_out4, decoder_2_out5,
       decoder_2_out6, decoder_2_out7, decoder_2_out8, decoder_2_out9, decoder_2_out10, decoder_2_out11,
       decoder_2_out12, decoder_2_out13, decoder_2_out14, decoder_2_out15, decoder_2_out16, decoder_2_out17,
       decoder_2_out18, decoder_2_out19, decoder_2_out20, decoder_2_out21, decoder_2_out22, decoder_2_out23,
       decoder_2_out24, decoder_2_out25, decoder_2_out26, decoder_2_out27, decoder_2_out28, decoder_2_out29,
       decoder_2_out30, decoder_2_out31, not_1_out, not_3_out, or_1_out, or_2_out, or_3_out;
  wire [2:0] counter_1_q;
  wire [4:0] counter_2_q;
  wire [7:0] controlled_buffer_1_out, controlled_buffer_2_out, controlled_buffer_5_out,
       controlled_buffer_7_out, controlled_buffer_10_out, controlled_buffer_13_out, controlled_buffer_16_out,
       controlled_buffer_20_out, controlled_buffer_22_out, controlled_buffer_25_out,
       controlled_buffer_29_out, controlled_buffer_32_out, controlled_buffer_34_out,
       controlled_buffer_38_out, controlled_buffer_40_out, controlled_buffer_43_out,
       controlled_buffer_46_out, controlled_buffer_49_out, controlled_buffer_53_out,
       controlled_buffer_55_out, controlled_buffer_59_out, controlled_buffer_62_out,
       controlled_buffer_64_out, controlled_buffer_68_out, controlled_buffer_70_out,
       controlled_buffer_74_out, controlled_buffer_76_out, controlled_buffer_79_out,
       controlled_buffer_82_out, controlled_buffer_85_out, controlled_buffer_88_out,
       controlled_buffer_92_out, controlled_buffer_94_out, controlled_buffer_97_out,
       controlled_buffer_98_out, controlled_buffer_100_out, controlled_buffer_104_out,
       controlled_buffer_107_out, controlled_buffer_109_out, controlled_buffer_112_out,
       controlled_buffer_115_out, controlled_buffer_118_out, controlled_buffer_121_out,
       controlled_buffer_125_out, controlled_buffer_127_out, controlled_buffer_131_out,
       controlled_buffer_133_out, controlled_buffer_136_out, controlled_buffer_139_out,
       controlled_buffer_143_out, controlled_buffer_145_out, controlled_buffer_148_out,
       controlled_buffer_151_out, controlled_buffer_154_out, controlled_buffer_157_out,
       controlled_buffer_161_out, controlled_buffer_164_out, controlled_buffer_167_out,
       controlled_buffer_170_out, controlled_buffer_173_out, controlled_buffer_175_out,
       controlled_buffer_179_out, controlled_buffer_181_out, controlled_buffer_185_out,
       controlled_buffer_187_out, controlled_buffer_190_out, controlled_buffer_193_out,
       controlled_buffer_195_out, controlled_buffer_197_out, controlled_buffer_199_out,
       controlled_buffer_201_out, controlled_buffer_203_out, controlled_buffer_205_out,
       controlled_buffer_207_out, controlled_buffer_209_out, controlled_buffer_211_out,
       controlled_buffer_213_out, controlled_buffer_215_out, controlled_buffer_217_out,
       controlled_buffer_219_out, controlled_buffer_221_out, controlled_buffer_223_out,
       controlled_buffer_225_out, controlled_buffer_227_out, controlled_buffer_229_out,
       controlled_buffer_231_out, controlled_buffer_233_out, controlled_buffer_235_out,
       controlled_buffer_237_out, controlled_buffer_239_out, controlled_buffer_241_out,
       controlled_buffer_243_out, controlled_buffer_245_out, controlled_buffer_247_out,
       controlled_buffer_249_out, controlled_buffer_251_out, controlled_buffer_253_out,
       controlled_buffer_255_out, controlled_buffer_257_out, controlled_buffer_258_out,
       controlled_buffer_260_out, controlled_buffer_264_out, controlled_buffer_267_out,
       controlled_buffer_269_out, controlled_buffer_272_out, controlled_buffer_275_out,
       controlled_buffer_278_out, controlled_buffer_281_out, controlled_buffer_284_out,
       controlled_buffer_288_out, controlled_buffer_290_out, controlled_buffer_294_out,
       controlled_buffer_296_out, controlled_buffer_299_out, controlled_buffer_303_out,
       controlled_buffer_306_out, controlled_buffer_308_out, controlled_buffer_312_out,
       controlled_buffer_314_out, controlled_buffer_317_out, controlled_buffer_321_out,
       controlled_buffer_323_out, controlled_buffer_327_out, controlled_buffer_330_out,
       controlled_buffer_333_out, controlled_buffer_336_out, controlled_buffer_339_out,
       controlled_buffer_342_out, controlled_buffer_344_out, controlled_buffer_347_out,
       controlled_buffer_351_out, controlled_buffer_353_out, d_ff_8_q, demultiplexer_3_out0,
       demultiplexer_3_out1, demultiplexer_3_out2, demultiplexer_3_out3, demultiplexer_3_out4,
       demultiplexer_3_out5, demultiplexer_3_out6, demultiplexer_3_out7, multiplexer_1_out, ram_1_data,
       register_1_q, register_2_q, register_3_q, register_4_q, register_5_q, register_6_q, register_7_q,
       register_8_q, register_9_q, register_10_q, register_11_q, register_12_q, register_13_q, register_14_q,
       register_15_q, register_16_q, register_17_q, register_18_q, register_19_q, register_20_q,
       register_21_q, register_22_q, register_23_q, register_24_q, register_25_q, register_26_q,
       register_27_q, register_28_q, register_29_q, register_30_q, register_31_q, register_32_q,
       register_34_q, register_35_q, register_36_q, register_37_q, register_38_q, register_39_q,
       register_40_q, register_41_q, register_42_q, register_43_q, register_44_q, register_45_q,
       register_46_q, register_47_q, register_48_q, register_49_q, register_50_q, register_51_q,
       register_52_q, register_53_q, register_54_q, register_55_q, register_56_q, register_57_q,
       register_58_q, register_59_q, register_60_q, register_61_q, register_62_q, register_63_q,
       register_64_q, register_65_q, register_66_q, register_67_q, register_68_q, register_69_q,
       register_70_q, register_71_q, register_72_q, register_73_q, register_74_q, register_75_q,
       register_76_q, register_77_q, register_78_q, register_79_q, register_80_q, register_81_q,
       register_82_q, register_83_q, register_84_q, register_85_q, register_86_q, register_87_q,
       register_88_q, register_89_q, register_90_q, register_91_q, register_92_q, register_93_q,
       register_94_q, register_95_q, register_96_q, register_97_q, register_98_q, register_99_q,
       register_100_q, register_101_q, register_102_q, register_103_q, register_104_q, register_105_q,
       register_106_q, register_107_q, register_108_q, register_109_q, register_110_q, register_111_q,
       register_112_q, register_113_q, register_114_q, register_115_q, register_116_q, register_117_q,
       register_118_q, register_119_q, register_120_q, register_121_q, register_122_q, register_123_q,
       register_124_q, register_125_q, register_126_q, register_127_q, register_128_q, register_129_q,
       register_130_q, register_131_q, rom_1_data, rom_2_data, rom_3_data, rom_4_data, rom_5_data,
       rom_6_data, rom_7_data, rom_8_data, rom_9_data;
  wire [15:0] register_133_q;
  wire [31:0] decoder_1_out0, register_33_q;

  RAM ram_1 (.addr(rom_9_data), .data(ram_1_data));  // open: sel, clk, ld, clr
  ROM rom_1 (.addr(ram_1_data), .data(rom_1_data));  // open: sel
  ROM rom_2 (.addr(ram_1_data), .data(rom_2_data));  // open: sel
  ROM rom_3 (.addr(ram_1_data), .data(rom_3_data));  // open: sel
  ROM rom_4 (.addr(ram_1_data), .data(rom_4_data));  // open: sel
  ROM rom_5 (.addr(ram_1_data), .data(rom_5_data));  // open: sel
  ROM rom_6 (.addr(ram_1_data), .data(rom_6_data));  // open: sel
  ROM rom_7 (.addr(ram_1_data), .data(rom_7_data));  // open: sel
  ROM rom_8 (.addr(ram_1_data), .data(rom_8_data));  // open: sel
  not not_1 (not_1_out, or_1_out);
  D_Flip_Flop d_ff_1 (.clk(a), .D(not_1_out), .Q(d_ff_8_q[5]));  // open: Qn, preset, en, reset
  or or_1 (or_1_out, d_ff_8_q[5], d_ff_8_q[7], d_ff_8_q[6]);
  D_Flip_Flop d_ff_2 (.clk(a), .D(d_ff_8_q[7]), .Q(d_ff_8_q[6]));  // open: Qn, preset, en, reset
  D_Flip_Flop d_ff_3 (.clk(a), .D(d_ff_8_q[5]), .Q(d_ff_8_q[7]));  // open: Qn, preset, en, reset
  Clock clock_1 (.out(clock_1_out));
  Multiplexer #(.select(3), .width(8)) multiplexer_1 (
    .in0(rom_1_data), .in1(rom_2_data), .in2(rom_3_data), .in3(rom_4_data), .in4(rom_5_data),
    .in5(rom_6_data), .in6(rom_7_data), .in7(rom_8_data), .out(multiplexer_1_out), .sel(counter_1_q));  // open: en
  Counter #(.width(3), .max('h7)) counter_1 (.Q(counter_1_q), .clk(clock_1_out));  // open: load, D, count, carry, clr
  D_Flip_Flop d_ff_4 (.clk(a), .D(d_ff_8_q[6]), .Q(d_ff_4_q));  // open: Qn, preset, en, reset
  Demultiplexer #(.select(3)) demultiplexer_1 (
    .out0(_1b), .out1(_2b), .out2(_3b), .out3(_4b), .out4(_5b), .out5(_6b), .out6(_7b), .out7(_8b),
    .in(d_ff_8_q[6]), .sel(counter_1_q));  // open: en
  Demultiplexer #(.select(3)) demultiplexer_2 (
    .out0(_1c), .out1(_2c), .out2(_3c), .out3(_4c), .out4(_5c), .out5(_6c), .out6(_7c), .out7(_8c),
    .in(d_ff_8_q[7]), .sel(counter_1_q));  // open: en
  Decoder #(.select(5)) decoder_1 (
    .out0(decoder_1_out0[0]), .out1(decoder_1_out0[1]), .out2(decoder_1_out0[2]), .out3(decoder_1_out0[3]),
    .out4(decoder_1_out0[4]), .out5(decoder_1_out0[5]), .out6(decoder_1_out0[6]), .out7(decoder_1_out0[7]),
    .out8(decoder_1_out0[8]), .out9(decoder_1_out0[9]), .out10(decoder_1_out0[10]),
    .out11(decoder_1_out0[11]), .out12(decoder_1_out0[12]), .out13(decoder_1_out0[13]),
    .out14(decoder_1_out0[14]), .out15(decoder_1_out0[15]), .out16(decoder_1_out0[16]),
    .out17(decoder_1_out0[17]), .out18(decoder_1_out0[18]), .out19(decoder_1_out0[19]),
    .out20(decoder_1_out0[20]), .out21(decoder_1_out0[21]), .out22(decoder_1_out0[22]),
    .out23(decoder_1_out0[23]), .out24(decoder_1_out0[24]), .out25(decoder_1_out0[25]),
    .out26(decoder_1_out0[26]), .out27(decoder_1_out0[27]), .out28(decoder_1_out0[28]),
    .out29(decoder_1_out0[29]), .out30(decoder_1_out0[30]), .out31(decoder_1_out0[31]), .sel(counter_2_q));  // open: en
  Counter #(.width(5), .max('h1f)) counter_2 (.Q(counter_2_q), .clk(clock_1_out));  // open: load, D, count, carry, clr
  Demultiplexer #(.select(3), .width(8)) demultiplexer_3 (
    .out0(demultiplexer_3_out0), .out1(demultiplexer_3_out1), .out2(demultiplexer_3_out2),
    .out3(demultiplexer_3_out3), .out4(demultiplexer_3_out4), .out5(demultiplexer_3_out5),
    .out6(demultiplexer_3_out6), .out7(demultiplexer_3_out7), .in(multiplexer_1_out), .sel(counter_1_q));  // open: en
  not not_2 (d_ff_8_q[4], or_1_out);
  Demultiplexer #(.select(3)) demultiplexer_4 (
    .out0(_1), .out1(_2), .out2(_3), .out3(_4), .out4(_5), .out5(_6), .out6(_7), .out7(_8), .in(d_ff_8_q[4]),
    .sel(counter_1_q));  // open: en
  Demultiplexer #(.select(3)) demultiplexer_5 (
    .out0(_1a), .out1(_2a), .out2(_3a), .out3(_4a), .out4(_5a), .out5(_6a), .out6(_7a), .out7(_8a),
    .in(d_ff_8_q[5]), .sel(counter_1_q));  // open: en
  or or_2 (or_2_out, _8a, _8, _8b, _8c);
  D_Flip_Flop d_ff_5 (.clk(or_2_out), .D(not_3_out), .Q(d_ff_8_q[3]));  // open: Qn, preset, en, reset
  not not_3 (not_3_out, or_3_out);
  D_Flip_Flop d_ff_6 (.clk(or_2_out), .D(d_ff_8_q[3]), .Q(d_ff_8_q[2]));  // open: Qn, preset, en, reset
  assign controlled_buffer_1_out = d_ff_8_q[3] ? demultiplexer_3_out0 : 8'bz;  // Controlled_Buffer controlled_buffer_1
  Register register_1 (.D(controlled_buffer_1_out), .Q(register_1_q), .clk(controlled_buffer_3_out));  // open: en, clr
  assign controlled_buffer_2_out = decoder_2_out0 ? register_1_q : 8'bz;  // Controlled_Buffer controlled_buffer_2
  assign controlled_buffer_3_out = d_ff_8_q[3] ? _1 : 1'bz;  // Controlled_Buffer controlled_buffer_3
  Register register_2 (.D(controlled_buffer_5_out), .Q(register_2_q), .clk(controlled_buffer_6_out));  // open: en, clr
  assign controlled_buffer_2_out = decoder_2_out1 ? register_2_q : 8'bz;  // Controlled_Buffer controlled_buffer_4
  assign controlled_buffer_5_out = d_ff_8_q[3] ? demultiplexer_3_out1 : 8'bz;  // Controlled_Buffer controlled_buffer_5
  assign controlled_buffer_6_out = d_ff_8_q[3] ? _2 : 1'bz;  // Controlled_Buffer controlled_buffer_6
  assign controlled_buffer_7_out = d_ff_8_q[3] ? demultiplexer_3_out2 : 8'bz;  // Controlled_Buffer controlled_buffer_7
  Register register_3 (.D(controlled_buffer_7_out), .Q(register_3_q), .clk(controlled_buffer_9_out));  // open: en, clr
  assign controlled_buffer_2_out = decoder_2_out2 ? register_3_q : 8'bz;  // Controlled_Buffer controlled_buffer_8
  assign controlled_buffer_9_out = d_ff_8_q[3] ? _3 : 1'bz;  // Controlled_Buffer controlled_buffer_9
  assign controlled_buffer_10_out = d_ff_8_q[3] ? demultiplexer_3_out3 : 8'bz;  // Controlled_Buffer controlled_buffer_10
  Register register_4 (
    .D(controlled_buffer_10_out), .Q(register_4_q), .clk(controlled_buffer_12_out));  // open: en, clr
  assign controlled_buffer_2_out = decoder_2_out3 ? register_4_q : 8'bz;  // Controlled_Buffer controlled_buffer_11
  assign controlled_buffer_12_out = d_ff_8_q[3] ? _4 : 1'bz;  // Controlled_Buffer controlled_buffer_12
  assign controlled_buffer_13_out = d_ff_8_q[3] ? demultiplexer_3_out4 : 8'bz;  // Controlled_Buffer controlled_buffer_13
  assign controlled_buffer_2_out = decoder_2_out4 ? register_5_q : 8'bz;  // Controlled_Buffer controlled_buffer_14
  Register register_5 (
    .D(controlled_buffer_13_out), .Q(register_5_q), .clk(controlled_buffer_15_out));  // open: en, clr
  assign controlled_buffer_15_out = d_ff_8_q[3] ? _5 : 1'bz;  // Controlled_Buffer controlled_buffer_15
  assign controlled_buffer_16_out = d_ff_8_q[3] ? demultiplexer_3_out5 : 8'bz;  // Controlled_Buffer controlled_buffer_16
  Register register_6 (
    .D(controlled_buffer_16_out), .Q(register_6_q), .clk(controlled_buffer_18_out));  // open: en, clr
  assign controlled_buffer_2_out = decoder_2_out5 ? register_6_q : 8'bz;  // Controlled_Buffer controlled_buffer_17
  assign controlled_buffer_18_out = d_ff_8_q[3] ? _6 : 1'bz;  // Controlled_Buffer controlled_buffer_18
  Register register_7 (
    .D(controlled_buffer_20_out), .Q(register_7_q), .clk(controlled_buffer_21_out));  // open: en, clr
  assign controlled_buffer_2_out = decoder_2_out6 ? register_7_q : 8'bz;  // Controlled_Buffer controlled_buffer_19
  assign controlled_buffer_20_out = d_ff_8_q[3] ? demultiplexer_3_out6 : 8'bz;  // Controlled_Buffer controlled_buffer_20
  assign controlled_buffer_21_out = d_ff_8_q[3] ? _7 : 1'bz;  // Controlled_Buffer controlled_buffer_21
  assign controlled_buffer_22_out = d_ff_8_q[3] ? demultiplexer_3_out7 : 8'bz;  // Controlled_Buffer controlled_buffer_22
  Register register_8 (
    .D(controlled_buffer_22_out), .Q(register_8_q), .clk(controlled_buffer_24_out));  // open: en, clr
  assign controlled_buffer_2_out = decoder_2_out7 ? register_8_q : 8'bz;  // Controlled_Buffer controlled_buffer_23
  assign controlled_buffer_24_out = d_ff_8_q[3] ? _8 : 1'bz;  // Controlled_Buffer controlled_buffer_24
  assign controlled_buffer_25_out = d_ff_8_q[3] ? demultiplexer_3_out0 : 8'bz;  // Controlled_Buffer controlled_buffer_25
  assign controlled_buffer_2_out = decoder_2_out8 ? register_9_q : 8'bz;  // Controlled_Buffer controlled_buffer_26
  Register register_9 (
    .D(controlled_buffer_25_out), .Q(register_9_q), .clk(controlled_buffer_27_out));  // open: en, clr
  assign controlled_buffer_27_out = d_ff_8_q[3] ? _1a : 1'bz;  // Controlled_Buffer controlled_buffer_27
  assign controlled_buffer_2_out = decoder_2_out9 ? register_10_q : 8'bz;  // Controlled_Buffer controlled_buffer_28
  Register register_10 (
    .D(controlled_buffer_29_out), .Q(register_10_q), .clk(controlled_buffer_30_out));  // open: en, clr
  assign controlled_buffer_29_out = d_ff_8_q[3] ? demultiplexer_3_out1 : 8'bz;  // Controlled_Buffer controlled_buffer_29
  assign controlled_buffer_30_out = d_ff_8_q[3] ? _2a : 1'bz;  // Controlled_Buffer controlled_buffer_30
  Register register_11 (
    .D(controlled_buffer_32_out), .Q(register_11_q), .clk(controlled_buffer_33_out));  // open: en, clr
  assign controlled_buffer_2_out = decoder_2_out10 ? register_11_q : 8'bz;  // Controlled_Buffer controlled_buffer_31
  assign controlled_buffer_32_out = d_ff_8_q[3] ? demultiplexer_3_out2 : 8'bz;  // Controlled_Buffer controlled_buffer_32
  assign controlled_buffer_33_out = d_ff_8_q[3] ? _3a : 1'bz;  // Controlled_Buffer controlled_buffer_33
  Register register_12 (
    .D(controlled_buffer_34_out), .Q(register_12_q), .clk(controlled_buffer_36_out));  // open: en, clr
  assign controlled_buffer_34_out = d_ff_8_q[3] ? demultiplexer_3_out3 : 8'bz;  // Controlled_Buffer controlled_buffer_34
  assign controlled_buffer_2_out = decoder_2_out11 ? register_12_q : 8'bz;  // Controlled_Buffer controlled_buffer_35
  assign controlled_buffer_36_out = d_ff_8_q[3] ? _4a : 1'bz;  // Controlled_Buffer controlled_buffer_36
  assign controlled_buffer_2_out = decoder_2_out12 ? register_13_q : 8'bz;  // Controlled_Buffer controlled_buffer_37
  assign controlled_buffer_38_out = d_ff_8_q[3] ? demultiplexer_3_out4 : 8'bz;  // Controlled_Buffer controlled_buffer_38
  Register register_13 (
    .D(controlled_buffer_38_out), .Q(register_13_q), .clk(controlled_buffer_39_out));  // open: en, clr
  assign controlled_buffer_39_out = d_ff_8_q[3] ? _5a : 1'bz;  // Controlled_Buffer controlled_buffer_39
  assign controlled_buffer_40_out = d_ff_8_q[3] ? demultiplexer_3_out5 : 8'bz;  // Controlled_Buffer controlled_buffer_40
  assign controlled_buffer_2_out = decoder_2_out13 ? register_14_q : 8'bz;  // Controlled_Buffer controlled_buffer_41
  Register register_14 (
    .D(controlled_buffer_40_out), .Q(register_14_q), .clk(controlled_buffer_42_out));  // open: en, clr
  assign controlled_buffer_42_out = d_ff_8_q[3] ? _6a : 1'bz;  // Controlled_Buffer controlled_buffer_42
  Register register_15 (
    .D(controlled_buffer_43_out), .Q(register_15_q), .clk(controlled_buffer_45_out));  // open: en, clr
  assign controlled_buffer_43_out = d_ff_8_q[3] ? demultiplexer_3_out6 : 8'bz;  // Controlled_Buffer controlled_buffer_43
  assign controlled_buffer_2_out = decoder_2_out14 ? register_15_q : 8'bz;  // Controlled_Buffer controlled_buffer_44
  assign controlled_buffer_45_out = d_ff_8_q[3] ? _7a : 1'bz;  // Controlled_Buffer controlled_buffer_45
  Register register_16 (
    .D(controlled_buffer_46_out), .Q(register_16_q), .clk(controlled_buffer_48_out));  // open: en, clr
  assign controlled_buffer_46_out = d_ff_8_q[3] ? demultiplexer_3_out7 : 8'bz;  // Controlled_Buffer controlled_buffer_46
  assign controlled_buffer_2_out = decoder_2_out15 ? register_16_q : 8'bz;  // Controlled_Buffer controlled_buffer_47
  assign controlled_buffer_48_out = d_ff_8_q[3] ? _8a : 1'bz;  // Controlled_Buffer controlled_buffer_48
  Register register_17 (
    .D(controlled_buffer_49_out), .Q(register_17_q), .clk(controlled_buffer_51_out));  // open: en, clr
  assign controlled_buffer_49_out = d_ff_8_q[3] ? demultiplexer_3_out0 : 8'bz;  // Controlled_Buffer controlled_buffer_49
  assign controlled_buffer_2_out = decoder_2_out16 ? register_17_q : 8'bz;  // Controlled_Buffer controlled_buffer_50
  assign controlled_buffer_51_out = d_ff_8_q[3] ? _1b : 1'bz;  // Controlled_Buffer controlled_buffer_51
  assign controlled_buffer_2_out = decoder_2_out17 ? register_18_q : 8'bz;  // Controlled_Buffer controlled_buffer_52
  Register register_18 (
    .D(controlled_buffer_53_out), .Q(register_18_q), .clk(controlled_buffer_54_out));  // open: en, clr
  assign controlled_buffer_53_out = d_ff_8_q[3] ? demultiplexer_3_out1 : 8'bz;  // Controlled_Buffer controlled_buffer_53
  assign controlled_buffer_54_out = d_ff_8_q[3] ? _2b : 1'bz;  // Controlled_Buffer controlled_buffer_54
  assign controlled_buffer_55_out = d_ff_8_q[3] ? demultiplexer_3_out2 : 8'bz;  // Controlled_Buffer controlled_buffer_55
  assign controlled_buffer_2_out = decoder_2_out18 ? register_19_q : 8'bz;  // Controlled_Buffer controlled_buffer_56
  Register register_19 (
    .D(controlled_buffer_55_out), .Q(register_19_q), .clk(controlled_buffer_57_out));  // open: en, clr
  assign controlled_buffer_57_out = d_ff_8_q[3] ? _3b : 1'bz;  // Controlled_Buffer controlled_buffer_57
  assign controlled_buffer_2_out = decoder_2_out19 ? register_20_q : 8'bz;  // Controlled_Buffer controlled_buffer_58
  Register register_20 (
    .D(controlled_buffer_59_out), .Q(register_20_q), .clk(controlled_buffer_60_out));  // open: en, clr
  assign controlled_buffer_59_out = d_ff_8_q[3] ? demultiplexer_3_out3 : 8'bz;  // Controlled_Buffer controlled_buffer_59
  assign controlled_buffer_60_out = d_ff_8_q[3] ? _4b : 1'bz;  // Controlled_Buffer controlled_buffer_60
  Register register_21 (
    .D(controlled_buffer_62_out), .Q(register_21_q), .clk(controlled_buffer_63_out));  // open: en, clr
  assign controlled_buffer_2_out = decoder_2_out20 ? register_21_q : 8'bz;  // Controlled_Buffer controlled_buffer_61
  assign controlled_buffer_62_out = d_ff_8_q[3] ? demultiplexer_3_out4 : 8'bz;  // Controlled_Buffer controlled_buffer_62
  assign controlled_buffer_63_out = d_ff_8_q[3] ? _5b : 1'bz;  // Controlled_Buffer controlled_buffer_63
  assign controlled_buffer_64_out = d_ff_8_q[3] ? demultiplexer_3_out5 : 8'bz;  // Controlled_Buffer controlled_buffer_64
  Register register_22 (
    .D(controlled_buffer_64_out), .Q(register_22_q), .clk(controlled_buffer_66_out));  // open: en, clr
  assign controlled_buffer_2_out = decoder_2_out21 ? register_22_q : 8'bz;  // Controlled_Buffer controlled_buffer_65
  assign controlled_buffer_66_out = d_ff_8_q[3] ? _6b : 1'bz;  // Controlled_Buffer controlled_buffer_66
  assign controlled_buffer_2_out = decoder_2_out22 ? register_23_q : 8'bz;  // Controlled_Buffer controlled_buffer_67
  Register register_23 (
    .D(controlled_buffer_68_out), .Q(register_23_q), .clk(controlled_buffer_69_out));  // open: en, clr
  assign controlled_buffer_68_out = d_ff_8_q[3] ? demultiplexer_3_out6 : 8'bz;  // Controlled_Buffer controlled_buffer_68
  assign controlled_buffer_69_out = d_ff_8_q[3] ? _7b : 1'bz;  // Controlled_Buffer controlled_buffer_69
  assign controlled_buffer_70_out = d_ff_8_q[3] ? demultiplexer_3_out7 : 8'bz;  // Controlled_Buffer controlled_buffer_70
  Register register_24 (
    .D(controlled_buffer_70_out), .Q(register_24_q), .clk(controlled_buffer_72_out));  // open: en, clr
  assign controlled_buffer_2_out = decoder_2_out23 ? register_24_q : 8'bz;  // Controlled_Buffer controlled_buffer_71
  assign controlled_buffer_72_out = d_ff_8_q[3] ? _8b : 1'bz;  // Controlled_Buffer controlled_buffer_72
  Register register_25 (
    .D(controlled_buffer_74_out), .Q(register_25_q), .clk(controlled_buffer_75_out));  // open: en, clr
  assign controlled_buffer_2_out = decoder_2_out24 ? register_25_q : 8'bz;  // Controlled_Buffer controlled_buffer_73
  assign controlled_buffer_74_out = d_ff_8_q[3] ? demultiplexer_3_out0 : 8'bz;  // Controlled_Buffer controlled_buffer_74
  assign controlled_buffer_75_out = d_ff_8_q[3] ? _1c : 1'bz;  // Controlled_Buffer controlled_buffer_75
  assign controlled_buffer_76_out = d_ff_8_q[3] ? demultiplexer_3_out1 : 8'bz;  // Controlled_Buffer controlled_buffer_76
  Register register_26 (
    .D(controlled_buffer_76_out), .Q(register_26_q), .clk(controlled_buffer_78_out));  // open: en, clr
  assign controlled_buffer_2_out = decoder_2_out25 ? register_26_q : 8'bz;  // Controlled_Buffer controlled_buffer_77
  assign controlled_buffer_78_out = d_ff_8_q[3] ? _2c : 1'bz;  // Controlled_Buffer controlled_buffer_78
  Register register_27 (
    .D(controlled_buffer_79_out), .Q(register_27_q), .clk(controlled_buffer_81_out));  // open: en, clr
  assign controlled_buffer_79_out = d_ff_8_q[3] ? demultiplexer_3_out2 : 8'bz;  // Controlled_Buffer controlled_buffer_79
  assign controlled_buffer_2_out = decoder_2_out26 ? register_27_q : 8'bz;  // Controlled_Buffer controlled_buffer_80
  assign controlled_buffer_81_out = d_ff_8_q[3] ? _3c : 1'bz;  // Controlled_Buffer controlled_buffer_81
  assign controlled_buffer_82_out = d_ff_8_q[3] ? demultiplexer_3_out3 : 8'bz;  // Controlled_Buffer controlled_buffer_82
  assign controlled_buffer_2_out = decoder_2_out27 ? register_28_q : 8'bz;  // Controlled_Buffer controlled_buffer_83
  Register register_28 (
    .D(controlled_buffer_82_out), .Q(register_28_q), .clk(controlled_buffer_84_out));  // open: en, clr
  assign controlled_buffer_84_out = d_ff_8_q[3] ? _4c : 1'bz;  // Controlled_Buffer controlled_buffer_84
  assign controlled_buffer_85_out = d_ff_8_q[3] ? demultiplexer_3_out4 : 8'bz;  // Controlled_Buffer controlled_buffer_85
  Register register_29 (
    .D(controlled_buffer_85_out), .Q(register_29_q), .clk(controlled_buffer_87_out));  // open: en, clr
  assign controlled_buffer_2_out = decoder_2_out28 ? register_29_q : 8'bz;  // Controlled_Buffer controlled_buffer_86
  assign controlled_buffer_87_out = d_ff_8_q[3] ? _5c : 1'bz;  // Controlled_Buffer controlled_buffer_87
  Register register_30 (
    .D(controlled_buffer_88_out), .Q(register_30_q), .clk(controlled_buffer_90_out));  // open: en, clr
  assign controlled_buffer_88_out = d_ff_8_q[3] ? demultiplexer_3_out5 : 8'bz;  // Controlled_Buffer controlled_buffer_88
  assign controlled_buffer_2_out = decoder_2_out29 ? register_30_q : 8'bz;  // Controlled_Buffer controlled_buffer_89
  assign controlled_buffer_90_out = d_ff_8_q[3] ? _6c : 1'bz;  // Controlled_Buffer controlled_buffer_90
  assign controlled_buffer_2_out = decoder_2_out30 ? register_31_q : 8'bz;  // Controlled_Buffer controlled_buffer_91
  Register register_31 (
    .D(controlled_buffer_92_out), .Q(register_31_q), .clk(controlled_buffer_93_out));  // open: en, clr
  assign controlled_buffer_92_out = d_ff_8_q[3] ? demultiplexer_3_out6 : 8'bz;  // Controlled_Buffer controlled_buffer_92
  assign controlled_buffer_93_out = d_ff_8_q[3] ? _7c : 1'bz;  // Controlled_Buffer controlled_buffer_93
  assign controlled_buffer_94_out = d_ff_8_q[3] ? demultiplexer_3_out7 : 8'bz;  // Controlled_Buffer controlled_buffer_94
  assign controlled_buffer_2_out = decoder_2_out31 ? register_32_q : 8'bz;  // Controlled_Buffer controlled_buffer_95
  Register register_32 (
    .D(controlled_buffer_94_out), .Q(register_32_q), .clk(controlled_buffer_96_out));  // open: en, clr
  assign controlled_buffer_96_out = d_ff_8_q[3] ? _8c : 1'bz;  // Controlled_Buffer controlled_buffer_96
  ROM rom_9 (.addr(d_ff_8_q), .data(rom_9_data));  // open: sel
  Register #(.width(32)) register_33 (.D(decoder_1_out0), .Q(register_33_q), .clk(clock_1_out));  // open: en, clr
  or or_3 (or_3_out, d_ff_8_q[3], d_ff_8_q[2], d_ff_8_q[1], d_ff_8_q[0]);
  D_Flip_Flop d_ff_7 (.clk(or_2_out), .D(d_ff_8_q[2]), .Q(d_ff_8_q[1]));  // open: Qn, preset, en, reset
  assign controlled_buffer_97_out = d_ff_8_q[2] ? demultiplexer_3_out0 : 8'bz;  // Controlled_Buffer controlled_buffer_97
  Register register_34 (
    .D(controlled_buffer_97_out), .Q(register_34_q), .clk(controlled_buffer_99_out));  // open: en, clr
  assign controlled_buffer_98_out = decoder_2_out0 ? register_34_q : 8'bz;  // Controlled_Buffer controlled_buffer_98
  assign controlled_buffer_99_out = d_ff_8_q[2] ? _1 : 1'bz;  // Controlled_Buffer controlled_buffer_99
  assign controlled_buffer_100_out = d_ff_8_q[2] ? demultiplexer_3_out1 : 8'bz;  // Controlled_Buffer controlled_buffer_100
  assign controlled_buffer_98_out = decoder_2_out1 ? register_35_q : 8'bz;  // Controlled_Buffer controlled_buffer_101
  Register register_35 (
    .D(controlled_buffer_100_out), .Q(register_35_q), .clk(controlled_buffer_102_out));  // open: en, clr
  assign controlled_buffer_102_out = d_ff_8_q[2] ? _2 : 1'bz;  // Controlled_Buffer controlled_buffer_102
  assign controlled_buffer_98_out = decoder_2_out2 ? register_36_q : 8'bz;  // Controlled_Buffer controlled_buffer_103
  assign controlled_buffer_104_out = d_ff_8_q[2] ? demultiplexer_3_out2 : 8'bz;  // Controlled_Buffer controlled_buffer_104
  Register register_36 (
    .D(controlled_buffer_104_out), .Q(register_36_q), .clk(controlled_buffer_105_out));  // open: en, clr
  assign controlled_buffer_105_out = d_ff_8_q[2] ? _3 : 1'bz;  // Controlled_Buffer controlled_buffer_105
  assign controlled_buffer_98_out = decoder_2_out3 ? register_37_q : 8'bz;  // Controlled_Buffer controlled_buffer_106
  Register register_37 (
    .D(controlled_buffer_107_out), .Q(register_37_q), .clk(controlled_buffer_108_out));  // open: en, clr
  assign controlled_buffer_107_out = d_ff_8_q[2] ? demultiplexer_3_out3 : 8'bz;  // Controlled_Buffer controlled_buffer_107
  assign controlled_buffer_108_out = d_ff_8_q[2] ? _4 : 1'bz;  // Controlled_Buffer controlled_buffer_108
  assign controlled_buffer_109_out = d_ff_8_q[2] ? demultiplexer_3_out4 : 8'bz;  // Controlled_Buffer controlled_buffer_109
  assign controlled_buffer_98_out = decoder_2_out4 ? register_38_q : 8'bz;  // Controlled_Buffer controlled_buffer_110
  Register register_38 (
    .D(controlled_buffer_109_out), .Q(register_38_q), .clk(controlled_buffer_111_out));  // open: en, clr
  assign controlled_buffer_111_out = d_ff_8_q[2] ? _5 : 1'bz;  // Controlled_Buffer controlled_buffer_111
  Register register_39 (
    .D(controlled_buffer_112_out), .Q(register_39_q), .clk(controlled_buffer_114_out));  // open: en, clr
  assign controlled_buffer_112_out = d_ff_8_q[2] ? demultiplexer_3_out5 : 8'bz;  // Controlled_Buffer controlled_buffer_112
  assign controlled_buffer_98_out = decoder_2_out5 ? register_39_q : 8'bz;  // Controlled_Buffer controlled_buffer_113
  assign controlled_buffer_114_out = d_ff_8_q[2] ? _6 : 1'bz;  // Controlled_Buffer controlled_buffer_114
  assign controlled_buffer_115_out = d_ff_8_q[2] ? demultiplexer_3_out6 : 8'bz;  // Controlled_Buffer controlled_buffer_115
  Register register_40 (
    .D(controlled_buffer_115_out), .Q(register_40_q), .clk(controlled_buffer_117_out));  // open: en, clr
  assign controlled_buffer_98_out = decoder_2_out6 ? register_40_q : 8'bz;  // Controlled_Buffer controlled_buffer_116
  assign controlled_buffer_117_out = d_ff_8_q[2] ? _7 : 1'bz;  // Controlled_Buffer controlled_buffer_117
  assign controlled_buffer_118_out = d_ff_8_q[2] ? demultiplexer_3_out7 : 8'bz;  // Controlled_Buffer controlled_buffer_118
  assign controlled_buffer_98_out = decoder_2_out7 ? register_41_q : 8'bz;  // Controlled_Buffer controlled_buffer_119
  Register register_41 (
    .D(controlled_buffer_118_out), .Q(register_41_q), .clk(controlled_buffer_120_out));  // open: en, clr
  assign controlled_buffer_120_out = d_ff_8_q[2] ? _8 : 1'bz;  // Controlled_Buffer controlled_buffer_120
  assign controlled_buffer_121_out = d_ff_8_q[2] ? demultiplexer_3_out0 : 8'bz;  // Controlled_Buffer controlled_buffer_121
  Register register_42 (
    .D(controlled_buffer_121_out), .Q(register_42_q), .clk(controlled_buffer_123_out));  // open: en, clr
  assign controlled_buffer_98_out = decoder_2_out8 ? register_42_q : 8'bz;  // Controlled_Buffer controlled_buffer_122
  assign controlled_buffer_123_out = d_ff_8_q[2] ? _1a : 1'bz;  // Controlled_Buffer controlled_buffer_123
  assign controlled_buffer_98_out = decoder_2_out9 ? register_43_q : 8'bz;  // Controlled_Buffer controlled_buffer_124
  assign controlled_buffer_125_out = d_ff_8_q[2] ? demultiplexer_3_out1 : 8'bz;  // Controlled_Buffer controlled_buffer_125
  Register register_43 (
    .D(controlled_buffer_125_out), .Q(register_43_q), .clk(controlled_buffer_126_out));  // open: en, clr
  assign controlled_buffer_126_out = d_ff_8_q[2] ? _2a : 1'bz;  // Controlled_Buffer controlled_buffer_126
  Register register_44 (
    .D(controlled_buffer_127_out), .Q(register_44_q), .clk(controlled_buffer_129_out));  // open: en, clr
  assign controlled_buffer_127_out = d_ff_8_q[2] ? demultiplexer_3_out2 : 8'bz;  // Controlled_Buffer controlled_buffer_127
  assign controlled_buffer_98_out = decoder_2_out10 ? register_44_q : 8'bz;  // Controlled_Buffer controlled_buffer_128
  assign controlled_buffer_129_out = d_ff_8_q[2] ? _3a : 1'bz;  // Controlled_Buffer controlled_buffer_129
  Register register_45 (
    .D(controlled_buffer_131_out), .Q(register_45_q), .clk(controlled_buffer_132_out));  // open: en, clr
  assign controlled_buffer_98_out = decoder_2_out11 ? register_45_q : 8'bz;  // Controlled_Buffer controlled_buffer_130
  assign controlled_buffer_131_out = d_ff_8_q[2] ? demultiplexer_3_out3 : 8'bz;  // Controlled_Buffer controlled_buffer_131
  assign controlled_buffer_132_out = d_ff_8_q[2] ? _4a : 1'bz;  // Controlled_Buffer controlled_buffer_132
  Register register_46 (
    .D(controlled_buffer_133_out), .Q(register_46_q), .clk(controlled_buffer_135_out));  // open: en, clr
  assign controlled_buffer_133_out = d_ff_8_q[2] ? demultiplexer_3_out4 : 8'bz;  // Controlled_Buffer controlled_buffer_133
  assign controlled_buffer_98_out = decoder_2_out12 ? register_46_q : 8'bz;  // Controlled_Buffer controlled_buffer_134
  assign controlled_buffer_135_out = d_ff_8_q[2] ? _5a : 1'bz;  // Controlled_Buffer controlled_buffer_135
  Register register_47 (
    .D(controlled_buffer_136_out), .Q(register_47_q), .clk(controlled_buffer_138_out));  // open: en, clr
  assign controlled_buffer_136_out = d_ff_8_q[2] ? demultiplexer_3_out5 : 8'bz;  // Controlled_Buffer controlled_buffer_136
  assign controlled_buffer_98_out = decoder_2_out13 ? register_47_q : 8'bz;  // Controlled_Buffer controlled_buffer_137
  assign controlled_buffer_138_out = d_ff_8_q[2] ? _6a : 1'bz;  // Controlled_Buffer controlled_buffer_138
  Register register_48 (
    .D(controlled_buffer_139_out), .Q(register_48_q), .clk(controlled_buffer_141_out));  // open: en, clr
  assign controlled_buffer_139_out = d_ff_8_q[2] ? demultiplexer_3_out6 : 8'bz;  // Controlled_Buffer controlled_buffer_139
  assign controlled_buffer_98_out = decoder_2_out14 ? register_48_q : 8'bz;  // Controlled_Buffer controlled_buffer_140
  assign controlled_buffer_141_out = d_ff_8_q[2] ? _7a : 1'bz;  // Controlled_Buffer controlled_buffer_141
  Register register_49 (
    .D(controlled_buffer_143_out), .Q(register_49_q), .clk(controlled_buffer_144_out));  // open: en, clr
  assign controlled_buffer_98_out = decoder_2_out15 ? register_49_q : 8'bz;  // Controlled_Buffer controlled_buffer_142
  assign controlled_buffer_143_out = d_ff_8_q[2] ? demultiplexer_3_out7 : 8'bz;  // Controlled_Buffer controlled_buffer_143
  assign controlled_buffer_144_out = d_ff_8_q[2] ? _8a : 1'bz;  // Controlled_Buffer controlled_buffer_144
  Register register_50 (
    .D(controlled_buffer_145_out), .Q(register_50_q), .clk(controlled_buffer_147_out));  // open: en, clr
  assign controlled_buffer_145_out = d_ff_8_q[2] ? demultiplexer_3_out0 : 8'bz;  // Controlled_Buffer controlled_buffer_145
  assign controlled_buffer_98_out = decoder_2_out16 ? register_50_q : 8'bz;  // Controlled_Buffer controlled_buffer_146
  assign controlled_buffer_147_out = d_ff_8_q[2] ? _1b : 1'bz;  // Controlled_Buffer controlled_buffer_147
  assign controlled_buffer_148_out = d_ff_8_q[2] ? demultiplexer_3_out1 : 8'bz;  // Controlled_Buffer controlled_buffer_148
  assign controlled_buffer_98_out = decoder_2_out17 ? register_51_q : 8'bz;  // Controlled_Buffer controlled_buffer_149
  Register register_51 (
    .D(controlled_buffer_148_out), .Q(register_51_q), .clk(controlled_buffer_150_out));  // open: en, clr
  assign controlled_buffer_150_out = d_ff_8_q[2] ? _2b : 1'bz;  // Controlled_Buffer controlled_buffer_150
  assign controlled_buffer_151_out = d_ff_8_q[2] ? demultiplexer_3_out2 : 8'bz;  // Controlled_Buffer controlled_buffer_151
  assign controlled_buffer_98_out = decoder_2_out18 ? register_52_q : 8'bz;  // Controlled_Buffer controlled_buffer_152
  Register register_52 (
    .D(controlled_buffer_151_out), .Q(register_52_q), .clk(controlled_buffer_153_out));  // open: en, clr
  assign controlled_buffer_153_out = d_ff_8_q[2] ? _3b : 1'bz;  // Controlled_Buffer controlled_buffer_153
  assign controlled_buffer_154_out = d_ff_8_q[2] ? demultiplexer_3_out3 : 8'bz;  // Controlled_Buffer controlled_buffer_154
  Register register_53 (
    .D(controlled_buffer_154_out), .Q(register_53_q), .clk(controlled_buffer_156_out));  // open: en, clr
  assign controlled_buffer_98_out = decoder_2_out19 ? register_53_q : 8'bz;  // Controlled_Buffer controlled_buffer_155
  assign controlled_buffer_156_out = d_ff_8_q[2] ? _4b : 1'bz;  // Controlled_Buffer controlled_buffer_156
  assign controlled_buffer_157_out = d_ff_8_q[2] ? demultiplexer_3_out4 : 8'bz;  // Controlled_Buffer controlled_buffer_157
  Register register_54 (
    .D(controlled_buffer_157_out), .Q(register_54_q), .clk(controlled_buffer_159_out));  // open: en, clr
  assign controlled_buffer_98_out = decoder_2_out20 ? register_54_q : 8'bz;  // Controlled_Buffer controlled_buffer_158
  assign controlled_buffer_159_out = d_ff_8_q[2] ? _5b : 1'bz;  // Controlled_Buffer controlled_buffer_159
  assign controlled_buffer_98_out = decoder_2_out21 ? register_55_q : 8'bz;  // Controlled_Buffer controlled_buffer_160
  Register register_55 (
    .D(controlled_buffer_161_out), .Q(register_55_q), .clk(controlled_buffer_162_out));  // open: en, clr
  assign controlled_buffer_161_out = d_ff_8_q[2] ? demultiplexer_3_out5 : 8'bz;  // Controlled_Buffer controlled_buffer_161
  assign controlled_buffer_162_out = d_ff_8_q[2] ? _6b : 1'bz;  // Controlled_Buffer controlled_buffer_162
  assign controlled_buffer_98_out = decoder_2_out22 ? register_56_q : 8'bz;  // Controlled_Buffer controlled_buffer_163
  Register register_56 (
    .D(controlled_buffer_164_out), .Q(register_56_q), .clk(controlled_buffer_165_out));  // open: en, clr
  assign controlled_buffer_164_out = d_ff_8_q[2] ? demultiplexer_3_out6 : 8'bz;  // Controlled_Buffer controlled_buffer_164
  assign controlled_buffer_165_out = d_ff_8_q[2] ? _7b : 1'bz;  // Controlled_Buffer controlled_buffer_165
  assign controlled_buffer_98_out = decoder_2_out23 ? register_57_q : 8'bz;  // Controlled_Buffer controlled_buffer_166
  assign controlled_buffer_167_out = d_ff_8_q[2] ? demultiplexer_3_out7 : 8'bz;  // Controlled_Buffer controlled_buffer_167
  Register register_57 (
    .D(controlled_buffer_167_out), .Q(register_57_q), .clk(controlled_buffer_168_out));  // open: en, clr
  assign controlled_buffer_168_out = d_ff_8_q[2] ? _8b : 1'bz;  // Controlled_Buffer controlled_buffer_168
  assign controlled_buffer_98_out = decoder_2_out24 ? register_58_q : 8'bz;  // Controlled_Buffer controlled_buffer_169
  Register register_58 (
    .D(controlled_buffer_170_out), .Q(register_58_q), .clk(controlled_buffer_171_out));  // open: en, clr
  assign controlled_buffer_170_out = d_ff_8_q[2] ? demultiplexer_3_out0 : 8'bz;  // Controlled_Buffer controlled_buffer_170
  assign controlled_buffer_171_out = d_ff_8_q[2] ? _1c : 1'bz;  // Controlled_Buffer controlled_buffer_171
  assign controlled_buffer_98_out = decoder_2_out25 ? register_59_q : 8'bz;  // Controlled_Buffer controlled_buffer_172
  assign controlled_buffer_173_out = d_ff_8_q[2] ? demultiplexer_3_out1 : 8'bz;  // Controlled_Buffer controlled_buffer_173
  Register register_59 (
    .D(controlled_buffer_173_out), .Q(register_59_q), .clk(controlled_buffer_174_out));  // open: en, clr
  assign controlled_buffer_174_out = d_ff_8_q[2] ? _2c : 1'bz;  // Controlled_Buffer controlled_buffer_174
  assign controlled_buffer_175_out = d_ff_8_q[2] ? demultiplexer_3_out2 : 8'bz;  // Controlled_Buffer controlled_buffer_175
  assign controlled_buffer_98_out = decoder_2_out26 ? register_60_q : 8'bz;  // Controlled_Buffer controlled_buffer_176
  Register register_60 (
    .D(controlled_buffer_175_out), .Q(register_60_q), .clk(controlled_buffer_177_out));  // open: en, clr
  assign controlled_buffer_177_out = d_ff_8_q[2] ? _3c : 1'bz;  // Controlled_Buffer controlled_buffer_177
  assign controlled_buffer_98_out = decoder_2_out27 ? register_61_q : 8'bz;  // Controlled_Buffer controlled_buffer_178
  assign controlled_buffer_179_out = d_ff_8_q[2] ? demultiplexer_3_out3 : 8'bz;  // Controlled_Buffer controlled_buffer_179
  Register register_61 (
    .D(controlled_buffer_179_out), .Q(register_61_q), .clk(controlled_buffer_180_out));  // open: en, clr
  assign controlled_buffer_180_out = d_ff_8_q[2] ? _4c : 1'bz;  // Controlled_Buffer controlled_buffer_180
  assign controlled_buffer_181_out = d_ff_8_q[2] ? demultiplexer_3_out4 : 8'bz;  // Controlled_Buffer controlled_buffer_181
  Register register_62 (
    .D(controlled_buffer_181_out), .Q(register_62_q), .clk(controlled_buffer_183_out));  // open: en, clr
  assign controlled_buffer_98_out = decoder_2_out28 ? register_62_q : 8'bz;  // Controlled_Buffer controlled_buffer_182
  assign controlled_buffer_183_out = d_ff_8_q[2] ? _5c : 1'bz;  // Controlled_Buffer controlled_buffer_183
  assign controlled_buffer_98_out = decoder_2_out29 ? register_63_q : 8'bz;  // Controlled_Buffer controlled_buffer_184
  assign controlled_buffer_185_out = d_ff_8_q[2] ? demultiplexer_3_out5 : 8'bz;  // Controlled_Buffer controlled_buffer_185
  Register register_63 (
    .D(controlled_buffer_185_out), .Q(register_63_q), .clk(controlled_buffer_186_out));  // open: en, clr
  assign controlled_buffer_186_out = d_ff_8_q[2] ? _6c : 1'bz;  // Controlled_Buffer controlled_buffer_186
  assign controlled_buffer_187_out = d_ff_8_q[2] ? demultiplexer_3_out6 : 8'bz;  // Controlled_Buffer controlled_buffer_187
  assign controlled_buffer_98_out = decoder_2_out30 ? register_64_q : 8'bz;  // Controlled_Buffer controlled_buffer_188
  Register register_64 (
    .D(controlled_buffer_187_out), .Q(register_64_q), .clk(controlled_buffer_189_out));  // open: en, clr
  assign controlled_buffer_189_out = d_ff_8_q[2] ? _7c : 1'bz;  // Controlled_Buffer controlled_buffer_189
  assign controlled_buffer_190_out = d_ff_8_q[2] ? demultiplexer_3_out7 : 8'bz;  // Controlled_Buffer controlled_buffer_190
  assign controlled_buffer_98_out = decoder_2_out31 ? register_65_q : 8'bz;  // Controlled_Buffer controlled_buffer_191
  Register register_65 (
    .D(controlled_buffer_190_out), .Q(register_65_q), .clk(controlled_buffer_192_out));  // open: en, clr
  assign controlled_buffer_192_out = d_ff_8_q[2] ? _8c : 1'bz;  // Controlled_Buffer controlled_buffer_192
  Register register_66 (
    .D(controlled_buffer_193_out), .Q(register_66_q), .clk(controlled_buffer_194_out));  // open: en, clr
  assign controlled_buffer_193_out = d_ff_8_q[1] ? demultiplexer_3_out0 : 8'bz;  // Controlled_Buffer controlled_buffer_193
  assign controlled_buffer_194_out = d_ff_8_q[1] ? _1 : 1'bz;  // Controlled_Buffer controlled_buffer_194
  Register register_67 (
    .D(controlled_buffer_195_out), .Q(register_67_q), .clk(controlled_buffer_196_out));  // open: en, clr
  assign controlled_buffer_195_out = d_ff_8_q[1] ? demultiplexer_3_out1 : 8'bz;  // Controlled_Buffer controlled_buffer_195
  assign controlled_buffer_196_out = d_ff_8_q[1] ? _2 : 1'bz;  // Controlled_Buffer controlled_buffer_196
  assign controlled_buffer_197_out = d_ff_8_q[1] ? demultiplexer_3_out2 : 8'bz;  // Controlled_Buffer controlled_buffer_197
  Register register_68 (
    .D(controlled_buffer_197_out), .Q(register_68_q), .clk(controlled_buffer_198_out));  // open: en, clr
  assign controlled_buffer_198_out = d_ff_8_q[1] ? _3 : 1'bz;  // Controlled_Buffer controlled_buffer_198
  Register register_69 (
    .D(controlled_buffer_199_out), .Q(register_69_q), .clk(controlled_buffer_200_out));  // open: en, clr
  assign controlled_buffer_199_out = d_ff_8_q[1] ? demultiplexer_3_out3 : 8'bz;  // Controlled_Buffer controlled_buffer_199
  assign controlled_buffer_200_out = d_ff_8_q[1] ? _4 : 1'bz;  // Controlled_Buffer controlled_buffer_200
  Register register_70 (
    .D(controlled_buffer_201_out), .Q(register_70_q), .clk(controlled_buffer_202_out));  // open: en, clr
  assign controlled_buffer_201_out = d_ff_8_q[1] ? demultiplexer_3_out4 : 8'bz;  // Controlled_Buffer controlled_buffer_201
  assign controlled_buffer_202_out = d_ff_8_q[1] ? _5 : 1'bz;  // Controlled_Buffer controlled_buffer_202
  assign controlled_buffer_203_out = d_ff_8_q[1] ? demultiplexer_3_out5 : 8'bz;  // Controlled_Buffer controlled_buffer_203
  Register register_71 (
    .D(controlled_buffer_203_out), .Q(register_71_q), .clk(controlled_buffer_204_out));  // open: en, clr
  assign controlled_buffer_204_out = d_ff_8_q[1] ? _6 : 1'bz;  // Controlled_Buffer controlled_buffer_204
  Register register_72 (
    .D(controlled_buffer_205_out), .Q(register_72_q), .clk(controlled_buffer_206_out));  // open: en, clr
  assign controlled_buffer_205_out = d_ff_8_q[1] ? demultiplexer_3_out6 : 8'bz;  // Controlled_Buffer controlled_buffer_205
  assign controlled_buffer_206_out = d_ff_8_q[1] ? _7 : 1'bz;  // Controlled_Buffer controlled_buffer_206
  assign controlled_buffer_207_out = d_ff_8_q[1] ? demultiplexer_3_out7 : 8'bz;  // Controlled_Buffer controlled_buffer_207
  Register register_73 (
    .D(controlled_buffer_207_out), .Q(register_73_q), .clk(controlled_buffer_208_out));  // open: en, clr
  assign controlled_buffer_208_out = d_ff_8_q[1] ? _8 : 1'bz;  // Controlled_Buffer controlled_buffer_208
  assign controlled_buffer_209_out = d_ff_8_q[1] ? demultiplexer_3_out0 : 8'bz;  // Controlled_Buffer controlled_buffer_209
  Register register_74 (
    .D(controlled_buffer_209_out), .Q(register_74_q), .clk(controlled_buffer_210_out));  // open: en, clr
  assign controlled_buffer_210_out = d_ff_8_q[1] ? _1a : 1'bz;  // Controlled_Buffer controlled_buffer_210
  Register register_75 (
    .D(controlled_buffer_211_out), .Q(register_75_q), .clk(controlled_buffer_212_out));  // open: en, clr
  assign controlled_buffer_211_out = d_ff_8_q[1] ? demultiplexer_3_out1 : 8'bz;  // Controlled_Buffer controlled_buffer_211
  assign controlled_buffer_212_out = d_ff_8_q[1] ? _2a : 1'bz;  // Controlled_Buffer controlled_buffer_212
  Register register_76 (
    .D(controlled_buffer_213_out), .Q(register_76_q), .clk(controlled_buffer_214_out));  // open: en, clr
  assign controlled_buffer_213_out = d_ff_8_q[1] ? demultiplexer_3_out2 : 8'bz;  // Controlled_Buffer controlled_buffer_213
  assign controlled_buffer_214_out = d_ff_8_q[1] ? _3a : 1'bz;  // Controlled_Buffer controlled_buffer_214
  Register register_77 (
    .D(controlled_buffer_215_out), .Q(register_77_q), .clk(controlled_buffer_216_out));  // open: en, clr
  assign controlled_buffer_215_out = d_ff_8_q[1] ? demultiplexer_3_out3 : 8'bz;  // Controlled_Buffer controlled_buffer_215
  assign controlled_buffer_216_out = d_ff_8_q[1] ? _4a : 1'bz;  // Controlled_Buffer controlled_buffer_216
  assign controlled_buffer_217_out = d_ff_8_q[1] ? demultiplexer_3_out4 : 8'bz;  // Controlled_Buffer controlled_buffer_217
  Register register_78 (
    .D(controlled_buffer_217_out), .Q(register_78_q), .clk(controlled_buffer_218_out));  // open: en, clr
  assign controlled_buffer_218_out = d_ff_8_q[1] ? _5a : 1'bz;  // Controlled_Buffer controlled_buffer_218
  Register register_79 (
    .D(controlled_buffer_219_out), .Q(register_79_q), .clk(controlled_buffer_220_out));  // open: en, clr
  assign controlled_buffer_219_out = d_ff_8_q[1] ? demultiplexer_3_out5 : 8'bz;  // Controlled_Buffer controlled_buffer_219
  assign controlled_buffer_220_out = d_ff_8_q[1] ? _6a : 1'bz;  // Controlled_Buffer controlled_buffer_220
  assign controlled_buffer_221_out = d_ff_8_q[1] ? demultiplexer_3_out6 : 8'bz;  // Controlled_Buffer controlled_buffer_221
  Register register_80 (
    .D(controlled_buffer_221_out), .Q(register_80_q), .clk(controlled_buffer_222_out));  // open: en, clr
  assign controlled_buffer_222_out = d_ff_8_q[1] ? _7a : 1'bz;  // Controlled_Buffer controlled_buffer_222
  assign controlled_buffer_223_out = d_ff_8_q[1] ? demultiplexer_3_out7 : 8'bz;  // Controlled_Buffer controlled_buffer_223
  Register register_81 (
    .D(controlled_buffer_223_out), .Q(register_81_q), .clk(controlled_buffer_224_out));  // open: en, clr
  assign controlled_buffer_224_out = d_ff_8_q[1] ? _8a : 1'bz;  // Controlled_Buffer controlled_buffer_224
  Register register_82 (
    .D(controlled_buffer_225_out), .Q(register_82_q), .clk(controlled_buffer_226_out));  // open: en, clr
  assign controlled_buffer_225_out = d_ff_8_q[1] ? demultiplexer_3_out0 : 8'bz;  // Controlled_Buffer controlled_buffer_225
  assign controlled_buffer_226_out = d_ff_8_q[1] ? _1b : 1'bz;  // Controlled_Buffer controlled_buffer_226
  Register register_83 (
    .D(controlled_buffer_227_out), .Q(register_83_q), .clk(controlled_buffer_228_out));  // open: en, clr
  assign controlled_buffer_227_out = d_ff_8_q[1] ? demultiplexer_3_out1 : 8'bz;  // Controlled_Buffer controlled_buffer_227
  assign controlled_buffer_228_out = d_ff_8_q[1] ? _2b : 1'bz;  // Controlled_Buffer controlled_buffer_228
  Register register_84 (
    .D(controlled_buffer_229_out), .Q(register_84_q), .clk(controlled_buffer_230_out));  // open: en, clr
  assign controlled_buffer_229_out = d_ff_8_q[1] ? demultiplexer_3_out2 : 8'bz;  // Controlled_Buffer controlled_buffer_229
  assign controlled_buffer_230_out = d_ff_8_q[1] ? _3b : 1'bz;  // Controlled_Buffer controlled_buffer_230
  Register register_85 (
    .D(controlled_buffer_231_out), .Q(register_85_q), .clk(controlled_buffer_232_out));  // open: en, clr
  assign controlled_buffer_231_out = d_ff_8_q[1] ? demultiplexer_3_out3 : 8'bz;  // Controlled_Buffer controlled_buffer_231
  assign controlled_buffer_232_out = d_ff_8_q[1] ? _4b : 1'bz;  // Controlled_Buffer controlled_buffer_232
  assign controlled_buffer_233_out = d_ff_8_q[1] ? demultiplexer_3_out4 : 8'bz;  // Controlled_Buffer controlled_buffer_233
  Register register_86 (
    .D(controlled_buffer_233_out), .Q(register_86_q), .clk(controlled_buffer_234_out));  // open: en, clr
  assign controlled_buffer_234_out = d_ff_8_q[1] ? _5b : 1'bz;  // Controlled_Buffer controlled_buffer_234
  Register register_87 (
    .D(controlled_buffer_235_out), .Q(register_87_q), .clk(controlled_buffer_236_out));  // open: en, clr
  assign controlled_buffer_235_out = d_ff_8_q[1] ? demultiplexer_3_out5 : 8'bz;  // Controlled_Buffer controlled_buffer_235
  assign controlled_buffer_236_out = d_ff_8_q[1] ? _6b : 1'bz;  // Controlled_Buffer controlled_buffer_236
  assign controlled_buffer_237_out = d_ff_8_q[1] ? demultiplexer_3_out6 : 8'bz;  // Controlled_Buffer controlled_buffer_237
  Register register_88 (
    .D(controlled_buffer_237_out), .Q(register_88_q), .clk(controlled_buffer_238_out));  // open: en, clr
  assign controlled_buffer_238_out = d_ff_8_q[1] ? _7b : 1'bz;  // Controlled_Buffer controlled_buffer_238
  assign controlled_buffer_239_out = d_ff_8_q[1] ? demultiplexer_3_out7 : 8'bz;  // Controlled_Buffer controlled_buffer_239
  Register register_89 (
    .D(controlled_buffer_239_out), .Q(register_89_q), .clk(controlled_buffer_240_out));  // open: en, clr
  assign controlled_buffer_240_out = d_ff_8_q[1] ? _8b : 1'bz;  // Controlled_Buffer controlled_buffer_240
  Register register_90 (
    .D(controlled_buffer_241_out), .Q(register_90_q), .clk(controlled_buffer_242_out));  // open: en, clr
  assign controlled_buffer_241_out = d_ff_8_q[1] ? demultiplexer_3_out0 : 8'bz;  // Controlled_Buffer controlled_buffer_241
  assign controlled_buffer_242_out = d_ff_8_q[1] ? _1c : 1'bz;  // Controlled_Buffer controlled_buffer_242
  Register register_91 (
    .D(controlled_buffer_243_out), .Q(register_91_q), .clk(controlled_buffer_244_out));  // open: en, clr
  assign controlled_buffer_243_out = d_ff_8_q[1] ? demultiplexer_3_out1 : 8'bz;  // Controlled_Buffer controlled_buffer_243
  assign controlled_buffer_244_out = d_ff_8_q[1] ? _2c : 1'bz;  // Controlled_Buffer controlled_buffer_244
  Register register_92 (
    .D(controlled_buffer_245_out), .Q(register_92_q), .clk(controlled_buffer_246_out));  // open: en, clr
  assign controlled_buffer_245_out = d_ff_8_q[1] ? demultiplexer_3_out2 : 8'bz;  // Controlled_Buffer controlled_buffer_245
  assign controlled_buffer_246_out = d_ff_8_q[1] ? _3c : 1'bz;  // Controlled_Buffer controlled_buffer_246
  assign controlled_buffer_247_out = d_ff_8_q[1] ? demultiplexer_3_out3 : 8'bz;  // Controlled_Buffer controlled_buffer_247
  Register register_93 (
    .D(controlled_buffer_247_out), .Q(register_93_q), .clk(controlled_buffer_248_out));  // open: en, clr
  assign controlled_buffer_248_out = d_ff_8_q[1] ? _4c : 1'bz;  // Controlled_Buffer controlled_buffer_248
  assign controlled_buffer_249_out = d_ff_8_q[1] ? demultiplexer_3_out4 : 8'bz;  // Controlled_Buffer controlled_buffer_249
  Register register_94 (
    .D(controlled_buffer_249_out), .Q(register_94_q), .clk(controlled_buffer_250_out));  // open: en, clr
  assign controlled_buffer_250_out = d_ff_8_q[1] ? _5c : 1'bz;  // Controlled_Buffer controlled_buffer_250
  assign controlled_buffer_251_out = d_ff_8_q[1] ? demultiplexer_3_out5 : 8'bz;  // Controlled_Buffer controlled_buffer_251
  Register register_95 (
    .D(controlled_buffer_251_out), .Q(register_95_q), .clk(controlled_buffer_252_out));  // open: en, clr
  assign controlled_buffer_252_out = d_ff_8_q[1] ? _6c : 1'bz;  // Controlled_Buffer controlled_buffer_252
  assign controlled_buffer_253_out = d_ff_8_q[1] ? demultiplexer_3_out6 : 8'bz;  // Controlled_Buffer controlled_buffer_253
  Register register_96 (
    .D(controlled_buffer_253_out), .Q(register_96_q), .clk(controlled_buffer_254_out));  // open: en, clr
  assign controlled_buffer_254_out = d_ff_8_q[1] ? _7c : 1'bz;  // Controlled_Buffer controlled_buffer_254
  Register register_97 (
    .D(controlled_buffer_255_out), .Q(register_97_q), .clk(controlled_buffer_256_out));  // open: en, clr
  assign controlled_buffer_255_out = d_ff_8_q[1] ? demultiplexer_3_out7 : 8'bz;  // Controlled_Buffer controlled_buffer_255
  assign controlled_buffer_256_out = d_ff_8_q[1] ? _8c : 1'bz;  // Controlled_Buffer controlled_buffer_256
  D_Flip_Flop d_ff_8 (.clk(or_2_out), .D(d_ff_8_q[1]), .Q(d_ff_8_q[0]));  // open: Qn, preset, en, reset
  Register register_98 (
    .D(controlled_buffer_257_out), .Q(register_98_q), .clk(controlled_buffer_259_out));  // open: en, clr
  assign controlled_buffer_257_out = d_ff_8_q[0] ? demultiplexer_3_out0 : 8'bz;  // Controlled_Buffer controlled_buffer_257
  assign controlled_buffer_258_out = decoder_2_out0 ? register_66_q : 8'bz;  // Controlled_Buffer controlled_buffer_258
  assign controlled_buffer_259_out = d_ff_8_q[0] ? _1 : 1'bz;  // Controlled_Buffer controlled_buffer_259
  Register register_99 (
    .D(controlled_buffer_260_out), .Q(register_99_q), .clk(controlled_buffer_262_out));  // open: en, clr
  assign controlled_buffer_260_out = d_ff_8_q[0] ? demultiplexer_3_out1 : 8'bz;  // Controlled_Buffer controlled_buffer_260
  assign controlled_buffer_258_out = decoder_2_out1 ? register_67_q : 8'bz;  // Controlled_Buffer controlled_buffer_261
  assign controlled_buffer_262_out = d_ff_8_q[0] ? _2 : 1'bz;  // Controlled_Buffer controlled_buffer_262
  Register register_100 (
    .D(controlled_buffer_264_out), .Q(register_100_q), .clk(controlled_buffer_265_out));  // open: en, clr
  assign controlled_buffer_258_out = decoder_2_out2 ? register_68_q : 8'bz;  // Controlled_Buffer controlled_buffer_263
  assign controlled_buffer_264_out = d_ff_8_q[0] ? demultiplexer_3_out2 : 8'bz;  // Controlled_Buffer controlled_buffer_264
  assign controlled_buffer_265_out = d_ff_8_q[0] ? _3 : 1'bz;  // Controlled_Buffer controlled_buffer_265
  assign controlled_buffer_258_out = decoder_2_out3 ? register_69_q : 8'bz;  // Controlled_Buffer controlled_buffer_266
  Register register_101 (
    .D(controlled_buffer_267_out), .Q(register_101_q), .clk(controlled_buffer_268_out));  // open: en, clr
  assign controlled_buffer_267_out = d_ff_8_q[0] ? demultiplexer_3_out3 : 8'bz;  // Controlled_Buffer controlled_buffer_267
  assign controlled_buffer_268_out = d_ff_8_q[0] ? _4 : 1'bz;  // Controlled_Buffer controlled_buffer_268
  Register register_102 (
    .D(controlled_buffer_269_out), .Q(register_102_q), .clk(controlled_buffer_271_out));  // open: en, clr
  assign controlled_buffer_269_out = d_ff_8_q[0] ? demultiplexer_3_out4 : 8'bz;  // Controlled_Buffer controlled_buffer_269
  assign controlled_buffer_258_out = decoder_2_out4 ? register_70_q : 8'bz;  // Controlled_Buffer controlled_buffer_270
  assign controlled_buffer_271_out = d_ff_8_q[0] ? _5 : 1'bz;  // Controlled_Buffer controlled_buffer_271
  assign controlled_buffer_272_out = d_ff_8_q[0] ? demultiplexer_3_out5 : 8'bz;  // Controlled_Buffer controlled_buffer_272
  Register register_103 (
    .D(controlled_buffer_272_out), .Q(register_103_q), .clk(controlled_buffer_274_out));  // open: en, clr
  assign controlled_buffer_258_out = decoder_2_out5 ? register_71_q : 8'bz;  // Controlled_Buffer controlled_buffer_273
  assign controlled_buffer_274_out = d_ff_8_q[0] ? _6 : 1'bz;  // Controlled_Buffer controlled_buffer_274
  assign controlled_buffer_275_out = d_ff_8_q[0] ? demultiplexer_3_out6 : 8'bz;  // Controlled_Buffer controlled_buffer_275
  assign controlled_buffer_258_out = decoder_2_out6 ? register_72_q : 8'bz;  // Controlled_Buffer controlled_buffer_276
  Register register_104 (
    .D(controlled_buffer_275_out), .Q(register_104_q), .clk(controlled_buffer_277_out));  // open: en, clr
  assign controlled_buffer_277_out = d_ff_8_q[0] ? _7 : 1'bz;  // Controlled_Buffer controlled_buffer_277
  assign controlled_buffer_278_out = d_ff_8_q[0] ? demultiplexer_3_out7 : 8'bz;  // Controlled_Buffer controlled_buffer_278
  assign controlled_buffer_258_out = decoder_2_out7 ? register_73_q : 8'bz;  // Controlled_Buffer controlled_buffer_279
  Register register_105 (
    .D(controlled_buffer_278_out), .Q(register_105_q), .clk(controlled_buffer_280_out));  // open: en, clr
  assign controlled_buffer_280_out = d_ff_8_q[0] ? _8 : 1'bz;  // Controlled_Buffer controlled_buffer_280
  assign controlled_buffer_281_out = d_ff_8_q[0] ? demultiplexer_3_out0 : 8'bz;  // Controlled_Buffer controlled_buffer_281
  assign controlled_buffer_258_out = decoder_2_out8 ? register_74_q : 8'bz;  // Controlled_Buffer controlled_buffer_282
  Register register_106 (
    .D(controlled_buffer_281_out), .Q(register_106_q), .clk(controlled_buffer_283_out));  // open: en, clr
  assign controlled_buffer_283_out = d_ff_8_q[0] ? _1a : 1'bz;  // Controlled_Buffer controlled_buffer_283
  Register register_107 (
    .D(controlled_buffer_284_out), .Q(register_107_q), .clk(controlled_buffer_286_out));  // open: en, clr
  assign controlled_buffer_284_out = d_ff_8_q[0] ? demultiplexer_3_out1 : 8'bz;  // Controlled_Buffer controlled_buffer_284
  assign controlled_buffer_258_out = decoder_2_out9 ? register_75_q : 8'bz;  // Controlled_Buffer controlled_buffer_285
  assign controlled_buffer_286_out = d_ff_8_q[0] ? _2a : 1'bz;  // Controlled_Buffer controlled_buffer_286
  assign controlled_buffer_258_out = decoder_2_out10 ? register_76_q : 8'bz;  // Controlled_Buffer controlled_buffer_287
  assign controlled_buffer_288_out = d_ff_8_q[0] ? demultiplexer_3_out2 : 8'bz;  // Controlled_Buffer controlled_buffer_288
  Register register_108 (
    .D(controlled_buffer_288_out), .Q(register_108_q), .clk(controlled_buffer_289_out));  // open: en, clr
  assign controlled_buffer_289_out = d_ff_8_q[0] ? _3a : 1'bz;  // Controlled_Buffer controlled_buffer_289
  assign controlled_buffer_290_out = d_ff_8_q[0] ? demultiplexer_3_out3 : 8'bz;  // Controlled_Buffer controlled_buffer_290
  Register register_109 (
    .D(controlled_buffer_290_out), .Q(register_109_q), .clk(controlled_buffer_292_out));  // open: en, clr
  assign controlled_buffer_258_out = decoder_2_out11 ? register_77_q : 8'bz;  // Controlled_Buffer controlled_buffer_291
  assign controlled_buffer_292_out = d_ff_8_q[0] ? _4a : 1'bz;  // Controlled_Buffer controlled_buffer_292
  assign controlled_buffer_258_out = decoder_2_out12 ? register_78_q : 8'bz;  // Controlled_Buffer controlled_buffer_293
  assign controlled_buffer_294_out = d_ff_8_q[0] ? demultiplexer_3_out4 : 8'bz;  // Controlled_Buffer controlled_buffer_294
  Register register_110 (
    .D(controlled_buffer_294_out), .Q(register_110_q), .clk(controlled_buffer_295_out));  // open: en, clr
  assign controlled_buffer_295_out = d_ff_8_q[0] ? _5a : 1'bz;  // Controlled_Buffer controlled_buffer_295
  assign controlled_buffer_296_out = d_ff_8_q[0] ? demultiplexer_3_out5 : 8'bz;  // Controlled_Buffer controlled_buffer_296
  Register register_111 (
    .D(controlled_buffer_296_out), .Q(register_111_q), .clk(controlled_buffer_298_out));  // open: en, clr
  assign controlled_buffer_258_out = decoder_2_out13 ? register_79_q : 8'bz;  // Controlled_Buffer controlled_buffer_297
  assign controlled_buffer_298_out = d_ff_8_q[0] ? _6a : 1'bz;  // Controlled_Buffer controlled_buffer_298
  Register register_112 (
    .D(controlled_buffer_299_out), .Q(register_112_q), .clk(controlled_buffer_301_out));  // open: en, clr
  assign controlled_buffer_299_out = d_ff_8_q[0] ? demultiplexer_3_out6 : 8'bz;  // Controlled_Buffer controlled_buffer_299
  assign controlled_buffer_258_out = decoder_2_out14 ? register_80_q : 8'bz;  // Controlled_Buffer controlled_buffer_300
  assign controlled_buffer_301_out = d_ff_8_q[0] ? _7a : 1'bz;  // Controlled_Buffer controlled_buffer_301
  assign controlled_buffer_258_out = decoder_2_out15 ? register_81_q : 8'bz;  // Controlled_Buffer controlled_buffer_302
  Register register_113 (
    .D(controlled_buffer_303_out), .Q(register_113_q), .clk(controlled_buffer_304_out));  // open: en, clr
  assign controlled_buffer_303_out = d_ff_8_q[0] ? demultiplexer_3_out7 : 8'bz;  // Controlled_Buffer controlled_buffer_303
  assign controlled_buffer_304_out = d_ff_8_q[0] ? _8a : 1'bz;  // Controlled_Buffer controlled_buffer_304
  assign controlled_buffer_258_out = decoder_2_out16 ? register_82_q : 8'bz;  // Controlled_Buffer controlled_buffer_305
  assign controlled_buffer_306_out = d_ff_8_q[0] ? demultiplexer_3_out0 : 8'bz;  // Controlled_Buffer controlled_buffer_306
  Register register_114 (
    .D(controlled_buffer_306_out), .Q(register_114_q), .clk(controlled_buffer_307_out));  // open: en, clr
  assign controlled_buffer_307_out = d_ff_8_q[0] ? _1b : 1'bz;  // Controlled_Buffer controlled_buffer_307
  assign controlled_buffer_308_out = d_ff_8_q[0] ? demultiplexer_3_out1 : 8'bz;  // Controlled_Buffer controlled_buffer_308
  Register register_115 (
    .D(controlled_buffer_308_out), .Q(register_115_q), .clk(controlled_buffer_310_out));  // open: en, clr
  assign controlled_buffer_258_out = decoder_2_out17 ? register_83_q : 8'bz;  // Controlled_Buffer controlled_buffer_309
  assign controlled_buffer_310_out = d_ff_8_q[0] ? _2b : 1'bz;  // Controlled_Buffer controlled_buffer_310
  Register register_116 (
    .D(controlled_buffer_312_out), .Q(register_116_q), .clk(controlled_buffer_313_out));  // open: en, clr
  assign controlled_buffer_258_out = decoder_2_out18 ? register_84_q : 8'bz;  // Controlled_Buffer controlled_buffer_311
  assign controlled_buffer_312_out = d_ff_8_q[0] ? demultiplexer_3_out2 : 8'bz;  // Controlled_Buffer controlled_buffer_312
  assign controlled_buffer_313_out = d_ff_8_q[0] ? _3b : 1'bz;  // Controlled_Buffer controlled_buffer_313
  assign controlled_buffer_314_out = d_ff_8_q[0] ? demultiplexer_3_out3 : 8'bz;  // Controlled_Buffer controlled_buffer_314
  assign controlled_buffer_258_out = decoder_2_out19 ? register_85_q : 8'bz;  // Controlled_Buffer controlled_buffer_315
  Register register_117 (
    .D(controlled_buffer_314_out), .Q(register_117_q), .clk(controlled_buffer_316_out));  // open: en, clr
  assign controlled_buffer_316_out = d_ff_8_q[0] ? _4b : 1'bz;  // Controlled_Buffer controlled_buffer_316
  Register register_118 (
    .D(controlled_buffer_317_out), .Q(register_118_q), .clk(controlled_buffer_319_out));  // open: en, clr
  assign controlled_buffer_317_out = d_ff_8_q[0] ? demultiplexer_3_out4 : 8'bz;  // Controlled_Buffer controlled_buffer_317
  assign controlled_buffer_258_out = decoder_2_out20 ? register_86_q : 8'bz;  // Controlled_Buffer controlled_buffer_318
  assign controlled_buffer_319_out = d_ff_8_q[0] ? _5b : 1'bz;  // Controlled_Buffer controlled_buffer_319
  assign controlled_buffer_258_out = decoder_2_out21 ? register_87_q : 8'bz;  // Controlled_Buffer controlled_buffer_320
  Register register_119 (
    .D(controlled_buffer_321_out), .Q(register_119_q), .clk(controlled_buffer_322_out));  // open: en, clr
  assign controlled_buffer_321_out = d_ff_8_q[0] ? demultiplexer_3_out5 : 8'bz;  // Controlled_Buffer controlled_buffer_321
  assign controlled_buffer_322_out = d_ff_8_q[0] ? _6b : 1'bz;  // Controlled_Buffer controlled_buffer_322
  Register register_120 (
    .D(controlled_buffer_323_out), .Q(register_120_q), .clk(controlled_buffer_325_out));  // open: en, clr
  assign controlled_buffer_323_out = d_ff_8_q[0] ? demultiplexer_3_out6 : 8'bz;  // Controlled_Buffer controlled_buffer_323
  assign controlled_buffer_258_out = decoder_2_out22 ? register_88_q : 8'bz;  // Controlled_Buffer controlled_buffer_324
  assign controlled_buffer_325_out = d_ff_8_q[0] ? _7b : 1'bz;  // Controlled_Buffer controlled_buffer_325
  Register register_121 (
    .D(controlled_buffer_327_out), .Q(register_121_q), .clk(controlled_buffer_328_out));  // open: en, clr
  assign controlled_buffer_258_out = decoder_2_out23 ? register_89_q : 8'bz;  // Controlled_Buffer controlled_buffer_326
  assign controlled_buffer_327_out = d_ff_8_q[0] ? demultiplexer_3_out7 : 8'bz;  // Controlled_Buffer controlled_buffer_327
  assign controlled_buffer_328_out = d_ff_8_q[0] ? _8b : 1'bz;  // Controlled_Buffer controlled_buffer_328
  Register register_122 (
    .D(controlled_buffer_330_out), .Q(register_122_q), .clk(controlled_buffer_331_out));  // open: en, clr
  assign controlled_buffer_258_out = decoder_2_out24 ? register_90_q : 8'bz;  // Controlled_Buffer controlled_buffer_329
  assign controlled_buffer_330_out = d_ff_8_q[0] ? demultiplexer_3_out0 : 8'bz;  // Controlled_Buffer controlled_buffer_330
  assign controlled_buffer_331_out = d_ff_8_q[0] ? _1c : 1'bz;  // Controlled_Buffer controlled_buffer_331
  assign controlled_buffer_258_out = decoder_2_out25 ? register_91_q : 8'bz;  // Controlled_Buffer controlled_buffer_332
  assign controlled_buffer_333_out = d_ff_8_q[0] ? demultiplexer_3_out1 : 8'bz;  // Controlled_Buffer controlled_buffer_333
  Register register_123 (
    .D(controlled_buffer_333_out), .Q(register_123_q), .clk(controlled_buffer_334_out));  // open: en, clr
  assign controlled_buffer_334_out = d_ff_8_q[0] ? _2c : 1'bz;  // Controlled_Buffer controlled_buffer_334
  assign controlled_buffer_258_out = decoder_2_out26 ? register_92_q : 8'bz;  // Controlled_Buffer controlled_buffer_335
  Register register_124 (
    .D(controlled_buffer_336_out), .Q(register_124_q), .clk(controlled_buffer_337_out));  // open: en, clr
  assign controlled_buffer_336_out = d_ff_8_q[0] ? demultiplexer_3_out2 : 8'bz;  // Controlled_Buffer controlled_buffer_336
  assign controlled_buffer_337_out = d_ff_8_q[0] ? _3c : 1'bz;  // Controlled_Buffer controlled_buffer_337
  assign controlled_buffer_258_out = decoder_2_out27 ? register_93_q : 8'bz;  // Controlled_Buffer controlled_buffer_338
  assign controlled_buffer_339_out = d_ff_8_q[0] ? demultiplexer_3_out3 : 8'bz;  // Controlled_Buffer controlled_buffer_339
  Register register_125 (
    .D(controlled_buffer_339_out), .Q(register_125_q), .clk(controlled_buffer_340_out));  // open: en, clr
  assign controlled_buffer_340_out = d_ff_8_q[0] ? _4c : 1'bz;  // Controlled_Buffer controlled_buffer_340
  assign controlled_buffer_258_out = decoder_2_out28 ? register_94_q : 8'bz;  // Controlled_Buffer controlled_buffer_341
  assign controlled_buffer_342_out = d_ff_8_q[0] ? demultiplexer_3_out4 : 8'bz;  // Controlled_Buffer controlled_buffer_342
  Register register_126 (
    .D(controlled_buffer_342_out), .Q(register_126_q), .clk(controlled_buffer_343_out));  // open: en, clr
  assign controlled_buffer_343_out = d_ff_8_q[0] ? _5c : 1'bz;  // Controlled_Buffer controlled_buffer_343
  assign controlled_buffer_344_out = d_ff_8_q[0] ? demultiplexer_3_out5 : 8'bz;  // Controlled_Buffer controlled_buffer_344
  assign controlled_buffer_258_out = decoder_2_out29 ? register_95_q : 8'bz;  // Controlled_Buffer controlled_buffer_345
  Register register_127 (
    .D(controlled_buffer_344_out), .Q(register_127_q), .clk(controlled_buffer_346_out));  // open: en, clr
  assign controlled_buffer_346_out = d_ff_8_q[0] ? _6c : 1'bz;  // Controlled_Buffer controlled_buffer_346
  assign controlled_buffer_347_out = d_ff_8_q[0] ? demultiplexer_3_out6 : 8'bz;  // Controlled_Buffer controlled_buffer_347
  assign controlled_buffer_258_out = decoder_2_out30 ? register_96_q : 8'bz;  // Controlled_Buffer controlled_buffer_348
  Register register_128 (
    .D(controlled_buffer_347_out), .Q(register_128_q), .clk(controlled_buffer_349_out));  // open: en, clr
  assign controlled_buffer_349_out = d_ff_8_q[0] ? _7c : 1'bz;  // Controlled_Buffer controlled_buffer_349
  Register register_129 (
    .D(controlled_buffer_351_out), .Q(register_129_q), .clk(controlled_buffer_352_out));  // open: en, clr
  assign controlled_buffer_258_out = decoder_2_out31 ? register_97_q : 8'bz;  // Controlled_Buffer controlled_buffer_350
  assign controlled_buffer_351_out = d_ff_8_q[0] ? demultiplexer_3_out7 : 8'bz;  // Controlled_Buffer controlled_buffer_351
  assign controlled_buffer_352_out = d_ff_8_q[0] ? _8c : 1'bz;  // Controlled_Buffer controlled_buffer_352
  D_Flip_Flop d_ff_9 (.clk(or_2_out), .D(d_ff_8_q[0]), .Q(a));  // open: Qn, preset, en, reset
  assign controlled_buffer_353_out = decoder_2_out0 ? register_98_q : 8'bz;  // Controlled_Buffer controlled_buffer_353
  assign controlled_buffer_353_out = decoder_2_out1 ? register_99_q : 8'bz;  // Controlled_Buffer controlled_buffer_354
  assign controlled_buffer_353_out = decoder_2_out2 ? register_100_q : 8'bz;  // Controlled_Buffer controlled_buffer_355
  assign controlled_buffer_353_out = decoder_2_out3 ? register_101_q : 8'bz;  // Controlled_Buffer controlled_buffer_356
  assign controlled_buffer_353_out = decoder_2_out4 ? register_102_q : 8'bz;  // Controlled_Buffer controlled_buffer_357
  assign controlled_buffer_353_out = decoder_2_out5 ? register_103_q : 8'bz;  // Controlled_Buffer controlled_buffer_358
  assign controlled_buffer_353_out = decoder_2_out6 ? register_104_q : 8'bz;  // Controlled_Buffer controlled_buffer_359
  assign controlled_buffer_353_out = decoder_2_out7 ? register_105_q : 8'bz;  // Controlled_Buffer controlled_buffer_360
  assign controlled_buffer_353_out = decoder_2_out8 ? register_106_q : 8'bz;  // Controlled_Buffer controlled_buffer_361
  assign controlled_buffer_353_out = decoder_2_out9 ? register_107_q : 8'bz;  // Controlled_Buffer controlled_buffer_362
  assign controlled_buffer_353_out = decoder_2_out10 ? register_108_q : 8'bz;  // Controlled_Buffer controlled_buffer_363
  assign controlled_buffer_353_out = decoder_2_out11 ? register_109_q : 8'bz;  // Controlled_Buffer controlled_buffer_364
  assign controlled_buffer_353_out = decoder_2_out12 ? register_110_q : 8'bz;  // Controlled_Buffer controlled_buffer_365
  assign controlled_buffer_353_out = decoder_2_out13 ? register_111_q : 8'bz;  // Controlled_Buffer controlled_buffer_366
  assign controlled_buffer_353_out = decoder_2_out14 ? register_112_q : 8'bz;  // Controlled_Buffer controlled_buffer_367
  assign controlled_buffer_353_out = decoder_2_out15 ? register_113_q : 8'bz;  // Controlled_Buffer controlled_buffer_368
  assign controlled_buffer_353_out = decoder_2_out16 ? register_114_q : 8'bz;  // Controlled_Buffer controlled_buffer_369
  assign controlled_buffer_353_out = decoder_2_out17 ? register_115_q : 8'bz;  // Controlled_Buffer controlled_buffer_370
  assign controlled_buffer_353_out = decoder_2_out18 ? register_116_q : 8'bz;  // Controlled_Buffer controlled_buffer_371
  assign controlled_buffer_353_out = decoder_2_out19 ? register_117_q : 8'bz;  // Controlled_Buffer controlled_buffer_372
  assign controlled_buffer_353_out = decoder_2_out20 ? register_118_q : 8'bz;  // Controlled_Buffer controlled_buffer_373
  assign controlled_buffer_353_out = decoder_2_out21 ? register_119_q : 8'bz;  // Controlled_Buffer controlled_buffer_374
  assign controlled_buffer_353_out = decoder_2_out22 ? register_120_q : 8'bz;  // Controlled_Buffer controlled_buffer_375
  assign controlled_buffer_353_out = decoder_2_out23 ? register_121_q : 8'bz;  // Controlled_Buffer controlled_buffer_376
  assign controlled_buffer_353_out = decoder_2_out24 ? register_122_q : 8'bz;  // Controlled_Buffer controlled_buffer_377
  assign controlled_buffer_353_out = decoder_2_out25 ? register_123_q : 8'bz;  // Controlled_Buffer controlled_buffer_378
  assign controlled_buffer_353_out = decoder_2_out26 ? register_124_q : 8'bz;  // Controlled_Buffer controlled_buffer_379
  assign controlled_buffer_353_out = decoder_2_out27 ? register_125_q : 8'bz;  // Controlled_Buffer controlled_buffer_380
  assign controlled_buffer_353_out = decoder_2_out28 ? register_126_q : 8'bz;  // Controlled_Buffer controlled_buffer_381
  assign controlled_buffer_353_out = decoder_2_out29 ? register_127_q : 8'bz;  // Controlled_Buffer controlled_buffer_382
  assign controlled_buffer_353_out = decoder_2_out30 ? register_128_q : 8'bz;  // Controlled_Buffer controlled_buffer_383
  assign controlled_buffer_353_out = decoder_2_out31 ? register_129_q : 8'bz;  // Controlled_Buffer controlled_buffer_384
  Decoder #(.select(5)) decoder_2 (
    .out0(decoder_2_out0), .out1(decoder_2_out1), .out2(decoder_2_out2), .out3(decoder_2_out3),
    .out4(decoder_2_out4), .out5(decoder_2_out5), .out6(decoder_2_out6), .out7(decoder_2_out7),
    .out8(decoder_2_out8), .out9(decoder_2_out9), .out10(decoder_2_out10), .out11(decoder_2_out11),
    .out12(decoder_2_out12), .out13(decoder_2_out13), .out14(decoder_2_out14), .out15(decoder_2_out15),
    .out16(decoder_2_out16), .out17(decoder_2_out17), .out18(decoder_2_out18), .out19(decoder_2_out19),
    .out20(decoder_2_out20), .out21(decoder_2_out21), .out22(decoder_2_out22), .out23(decoder_2_out23),
    .out24(decoder_2_out24), .out25(decoder_2_out25), .out26(decoder_2_out26), .out27(decoder_2_out27),
    .out28(decoder_2_out28), .out29(decoder_2_out29), .out30(decoder_2_out30), .out31(decoder_2_out31),
    .sel(counter_2_q));  // open: en
  Register register_130 (.D(controlled_buffer_353_out), .Q(register_130_q), .clk(clock_1_out));  // open: en, clr
  Register register_131 (.D(controlled_buffer_258_out), .Q(register_131_q), .clk(clock_1_out));  // open: en, clr
  Register register_132 (.D(controlled_buffer_98_out), .Q(register_133_q[15:8]), .clk(clock_1_out));  // open: en, clr
  Register register_133 (.D(controlled_buffer_2_out), .Q(register_133_q[7:0]), .clk(clock_1_out));  // open: en, clr
  // DotMatrix #(.inputtype("select"), .matrixcols(32), .matrixrows(32), .persist(63)) dotmatrix_1: pin names not known; wires that end beside it: {register_130_q, register_131_q, register_133_q}, register_33_q

  // Notes on the sheet:
  //   contents of rom_1 (hex, n*v repeats v):
  //   0 22 1e 1c 1e 3e 2 1c 22 1c 3c 44 3e 42 42 1c 2 20 12 1c 8 1c 18 24 21 1c
  //   contents of rom_2 (hex, n*v repeats v):
  //   0 4*22 2 2 22 22 8 24 24 2 42 62 22 2 30 a 22 8 22 18 5a 12 8
  //   contents of rom_3 (hex, n*v repeats v):
  //   0 4*22 2 2 3a 22 8 24 14 2 42 52 22 2 1c 6 20 8 22 24 99 c 8
  //   contents of rom_4 (hex, n*v repeats v):
  //   0 3e 1e 2 22 3e 3e 2 3e 8 20 c 2 5a 4a 22 1e 22 e 1c 8 22 24 99 c 8
  //   contents of rom_5 (hex, n*v repeats v):
  //   0 4*22 2 2 22 22 8 20 c 2 66 46 22 22 22 12 2 8 22 42 99 c 1c
  //   contents of rom_6 (hex, n*v repeats v):
  //   0 4*22 2 2 22 22 8 20 14 2 42 42 22 22 22 12 22 8 22 42 81 12 22
  //   contents of rom_7 (hex, n*v repeats v):
  //   0 1c 1e 1c 1e 3e 3e 1c 22 1c 20 24 2 0 0 1c 1e 1c e 1c 3e 22 42 81 21 22
  //   contents of rom_9 (hex, n*v repeats v):
  //   17*0 f e 0 d 0 0 0 c 8*0 b a 0 9 0 0 0 8 24*0 7 6 0 5 0 0 0 4 56*0 3 2 0 1
endmodule
